// Logisim project alu.circ as structural Verilog: 5 circuits, main circuit ALU
module ALU (
  input  [7:0] A,
  input  [7:0] B,
  input  [2:0] Op,
  output [7:0] R,
  output Z,
  output N,
  output C,
  output EQ,
  output NE,
  output GT,
  output LT,
  output GE,
  output LE
);

  wire plus_1_c;
  wire [7:0] and_1_out, minus_1_r, nand_1_out, nor_1_out, not_1_out, or_1_out, xor_1_x;

  assign not_1_out = ~A;  // NOT_Gate not_1, 8 bits wide
  assign nand_1_out = ~(A & B);  // NAND_Gate nand_1, 8 bits wide
  MINUS minus_1 (.A(A), .B(B), .R(minus_1_r), .C(LT));
  assign nor_1_out = ~(A | B);  // NOR_Gate nor_1, 8 bits wide
  assign and_1_out = A & B;  // AND_Gate and_1, 8 bits wide
  XOR xor_1 (.A(A), .B(B), .X(xor_1_x));
  PLUS plus_1 (.A(A), .B(B), .R(minus_1_r), .C(plus_1_c));
  assign or_1_out = A | B;  // OR_Gate or_1, 8 bits wide
  Multiplexer #(.select(3), .width(8)) multiplexer_1 (
    .in0(not_1_out), .in1(nand_1_out), .in2(minus_1_r), .in3(nor_1_out), .in4(and_1_out), .in5(xor_1_x),
    .in6(minus_1_r), .in7(or_1_out), .out({N, R[6:0]}), .sel(Op));
  Custom_NOR custom_nor_1 (.N(minus_1_r), .R(EQ));
  Custom_NOR custom_nor_2 (.N({N, R[6:0]}), .R(Z));
  Multiplexer #(.select(3)) multiplexer_2 (
    .in0(1'b0), .in1(1'b0), .in2(LT), .in3(1'b0), .in4(1'b0), .in5(1'b0), .in6(plus_1_c), .in7(1'b0),
    .out(C), .sel(Op));
  not not_2 (NE, EQ);
  nor nor_2 (GT, EQ, LT);
  not not_3 (GE, LT);
  or or_2 (LE, EQ, LT);

  assign R[7] = N;
endmodule

module XOR (
  input  [7:0] A,
  input  [7:0] B,
  output [7:0] X
);

  wire [7:0] and_1_out, and_2_out;

  assign and_1_out = A & ~B;  // AND_Gate and_1, 8 bits wide
  assign and_2_out = ~A & B;  // AND_Gate and_2, 8 bits wide
  assign X = and_1_out | and_2_out;  // OR_Gate or_1, 8 bits wide
endmodule

// +
module PLUS (
  input  [7:0] A,
  input  [7:0] B,
  output [7:0] R,
  output C
);

  Adder adder_1 (.a(A), .b(B), .out(R), .cout(C));  // open: cin
endmodule

// -
module MINUS (
  input  [7:0] A,
  input  [7:0] B,
  output [7:0] R,
  output C
);

  Subtractor subtractor_1 (.a(A), .b(B), .out(R), .bout(C));  // open: bin
endmodule

// NOR
module Custom_NOR (
  input  [7:0] N,
  output R
);

  nor nor_1 (R, N[0], N[1], N[2], N[3], N[4], N[5], N[6], N[7]);
endmodule
