// Logisim project DC.circ as structural Verilog
module DC1 (
  input  x0,
  input  E,
  output y0,
  output y1
);

  and and_1 (y0, ~x0, E);  // AND_Gate
  and and_2 (y1, x0, E);
endmodule

module DC2 (
  input  x0,
  input  x1,
  input  E,
  output y0,
  output y1,
  output y2,
  output y3
);

  wire dc1_1_y0, dc1_1_y1;

  DC1 dc1_1 (.x0(x1), .E(E), .y0(dc1_1_y0), .y1(dc1_1_y1));
  DC1 dc1_2 (.x0(x0), .E(dc1_1_y0), .y0(y0), .y1(y1));
  DC1 dc1_3 (.x0(x0), .E(dc1_1_y1), .y0(y2), .y1(y3));

  // Notes on the sheet:
  //   DC 1bit
  //   DC 1bit
endmodule

module DC3 (
  input  x0,
  input  x1,
  input  x2,
  input  E,
  output y0,
  output y1,
  output y2,
  output y3,
  output y4,
  output y5,
  output y6,
  output y7
);

  wire dc1_1_y0, dc1_1_y1;

  DC1 dc1_1 (.x0(x2), .E(E), .y0(dc1_1_y0), .y1(dc1_1_y1));
  DC2 dc2_1 (.x0(x0), .x1(x1), .E(dc1_1_y0), .y0(y0), .y1(y1), .y2(y2), .y3(y3));
  DC2 dc2_2 (.x0(x0), .x1(x1), .E(dc1_1_y1), .y0(y4), .y1(y5), .y2(y6), .y3(y7));

  // Notes on the sheet:
  //   DC 1bit
  //   DC 2bit
endmodule

module DC4 (
  input  x0,
  input  x1,
  input  x2,
  input  x3,
  input  E,
  output y0,
  output y1,
  output y2,
  output y3,
  output y4,
  output y5,
  output y6,
  output y7,
  output y8,
  output y9,
  output y10,
  output y11,
  output y12,
  output y13,
  output y14,
  output y15
);

  wire dc1_1_y0, dc1_1_y1;

  DC1 dc1_1 (.x0(x3), .E(E), .y0(dc1_1_y0), .y1(dc1_1_y1));
  DC3 dc3_1 (
    .x0(x0), .x1(x1), .x2(x2), .E(dc1_1_y0), .y0(y0), .y1(y1), .y2(y2), .y3(y3), .y4(y4), .y5(y5), .y6(y6),
    .y7(y7));
  DC3 dc3_2 (
    .x0(x0), .x1(x1), .x2(x2), .E(dc1_1_y1), .y0(y8), .y1(y9), .y2(y10), .y3(y11), .y4(y12), .y5(y13),
    .y6(y14), .y7(y15));

  // Notes on the sheet:
  //   DC 1bit
  //   DC 3bit
endmodule
