// Logisim project tests.circ as structural Verilog: 26 circuits, main circuit main
module main (
  input  [4:0] n
);

  wire [3:0] and_1_out, bit_extender_1_out, creator_1_f0, creator_1_f1, creator_1_f2, creator_1_f3,
       creator_2_f0, creator_2_f1, creator_2_f2, creator_2_f3, creator_4bit_1_f0, creator_4bit_1_f1,
       creator_4bit_1_f2, creator_noai_1_f0, creator_noai_1_f1, creator_noai_1_f2, creator_noai_1_f3,
       eater_rom_1_f0, eater_rom_1_f1, eater_rom_1_f2, eater_rom_1_f3;

  CREATOR creator_1 (.n(n), .F3(creator_1_f3), .F2(creator_1_f2), .F0(creator_1_f0), .F1(creator_1_f1));
  CREATOR creator_2 (.n(n), .F3(creator_2_f3), .F2(creator_2_f2), .F0(creator_2_f0), .F1(creator_2_f1));
  CREATOR_noAI creator_noai_1 (
    .n(n), .F3(creator_noai_1_f3), .F2(creator_noai_1_f2), .F0(creator_noai_1_f0), .F1(creator_noai_1_f1));
  LED led_1 (.in(creator_2_f3[3]));
  LED led_2 (.in(creator_2_f3[3]));
  LED led_3 (.in(creator_2_f3[2]));
  LED led_4 (.in(creator_2_f3[2]));
  LED led_5 (.in(creator_2_f3[2]));
  LED led_6 (.in(creator_2_f3[2]));
  LED led_7 (.in(creator_2_f3[3]));
  LED led_8 (.in(creator_2_f3[3]));
  LED led_9 (.in(creator_2_f2[3]));
  LED led_10 (.in(creator_2_f2[3]));
  LED led_11 (.in(creator_2_f2[2]));
  LED led_12 (.in(creator_2_f2[2]));
  LED led_13 (.in(creator_2_f2[2]));
  LED led_14 (.in(creator_2_f2[2]));
  LED led_15 (.in(creator_2_f2[3]));
  LED led_16 (.in(creator_2_f2[3]));
  LED led_17 (.in(creator_2_f1[3]));
  LED led_18 (.in(creator_2_f1[3]));
  LED led_19 (.in(creator_2_f1[2]));
  LED led_20 (.in(creator_2_f1[2]));
  LED led_21 (.in(creator_2_f1[2]));
  LED led_22 (.in(creator_2_f1[2]));
  LED led_23 (.in(creator_2_f1[3]));
  LED led_24 (.in(creator_2_f1[3]));
  LED led_25 (.in(creator_2_f0[3]));
  LED led_26 (.in(creator_2_f0[3]));
  LED led_27 (.in(creator_2_f0[2]));
  LED led_28 (.in(creator_2_f0[2]));
  LED led_29 (.in(creator_2_f0[2]));
  LED led_30 (.in(creator_2_f0[2]));
  LED led_31 (.in(creator_2_f0[3]));
  LED led_32 (.in(creator_2_f0[3]));
  LED led_33 (.in(creator_noai_1_f3[3]));
  LED led_34 (.in(creator_noai_1_f3[3]));
  LED led_35 (.in(creator_noai_1_f3[2]));
  LED led_36 (.in(creator_noai_1_f3[2]));
  LED led_37 (.in(creator_noai_1_f3[2]));
  LED led_38 (.in(creator_noai_1_f3[2]));
  LED led_39 (.in(creator_noai_1_f3[3]));
  LED led_40 (.in(creator_noai_1_f3[3]));
  LED led_41 (.in(creator_noai_1_f2[3]));
  LED led_42 (.in(creator_noai_1_f2[3]));
  LED led_43 (.in(creator_noai_1_f2[2]));
  LED led_44 (.in(creator_noai_1_f2[2]));
  LED led_45 (.in(creator_noai_1_f2[2]));
  LED led_46 (.in(creator_noai_1_f2[2]));
  LED led_47 (.in(creator_noai_1_f2[3]));
  LED led_48 (.in(creator_noai_1_f2[3]));
  LED led_49 (.in(creator_noai_1_f1[3]));
  LED led_50 (.in(creator_noai_1_f1[3]));
  LED led_51 (.in(creator_noai_1_f1[2]));
  LED led_52 (.in(creator_noai_1_f1[2]));
  LED led_53 (.in(creator_noai_1_f1[2]));
  LED led_54 (.in(creator_noai_1_f1[2]));
  LED led_55 (.in(creator_noai_1_f1[3]));
  LED led_56 (.in(creator_noai_1_f1[3]));
  LED led_57 (.in(creator_noai_1_f0[3]));
  LED led_58 (.in(creator_noai_1_f0[3]));
  LED led_59 (.in(creator_noai_1_f0[2]));
  LED led_60 (.in(creator_noai_1_f0[2]));
  LED led_61 (.in(creator_noai_1_f0[2]));
  LED led_62 (.in(creator_noai_1_f0[2]));
  LED led_63 (.in(creator_noai_1_f0[3]));
  LED led_64 (.in(creator_noai_1_f0[3]));
  LED led_65 (.in(creator_2_f3[1]));
  LED led_66 (.in(creator_2_f3[1]));
  LED led_67 (.in(creator_2_f3[0]));
  LED led_68 (.in(creator_2_f3[0]));
  LED led_69 (.in(creator_2_f3[1]));
  LED led_70 (.in(creator_2_f3[1]));
  LED led_71 (.in(creator_2_f3[0]));
  LED led_72 (.in(creator_2_f3[0]));
  LED led_73 (.in(creator_2_f2[1]));
  LED led_74 (.in(creator_2_f2[1]));
  LED led_75 (.in(creator_2_f2[0]));
  LED led_76 (.in(creator_2_f2[0]));
  LED led_77 (.in(creator_2_f2[1]));
  LED led_78 (.in(creator_2_f2[1]));
  LED led_79 (.in(creator_2_f2[0]));
  LED led_80 (.in(creator_2_f2[0]));
  LED led_81 (.in(creator_2_f1[1]));
  LED led_82 (.in(creator_2_f1[1]));
  LED led_83 (.in(creator_2_f1[0]));
  LED led_84 (.in(creator_2_f1[0]));
  LED led_85 (.in(creator_2_f1[1]));
  LED led_86 (.in(creator_2_f1[1]));
  LED led_87 (.in(creator_2_f1[0]));
  LED led_88 (.in(creator_2_f1[0]));
  LED led_89 (.in(creator_2_f0[1]));
  LED led_90 (.in(creator_2_f0[1]));
  LED led_91 (.in(creator_2_f0[0]));
  LED led_92 (.in(creator_2_f0[0]));
  LED led_93 (.in(creator_2_f0[1]));
  LED led_94 (.in(creator_2_f0[1]));
  LED led_95 (.in(creator_2_f0[0]));
  LED led_96 (.in(creator_2_f0[0]));
  LED led_97 (.in(creator_noai_1_f3[1]));
  LED led_98 (.in(creator_noai_1_f3[1]));
  LED led_99 (.in(creator_noai_1_f3[0]));
  LED led_100 (.in(creator_noai_1_f3[0]));
  LED led_101 (.in(creator_noai_1_f3[1]));
  LED led_102 (.in(creator_noai_1_f3[1]));
  LED led_103 (.in(creator_noai_1_f3[0]));
  LED led_104 (.in(creator_noai_1_f3[0]));
  LED led_105 (.in(creator_noai_1_f2[1]));
  LED led_106 (.in(creator_noai_1_f2[1]));
  LED led_107 (.in(creator_noai_1_f2[0]));
  LED led_108 (.in(creator_noai_1_f2[0]));
  LED led_109 (.in(creator_noai_1_f2[1]));
  LED led_110 (.in(creator_noai_1_f2[1]));
  LED led_111 (.in(creator_noai_1_f2[0]));
  LED led_112 (.in(creator_noai_1_f2[0]));
  LED led_113 (.in(creator_noai_1_f1[1]));
  LED led_114 (.in(creator_noai_1_f1[1]));
  LED led_115 (.in(creator_noai_1_f1[0]));
  LED led_116 (.in(creator_noai_1_f1[0]));
  LED led_117 (.in(creator_noai_1_f1[1]));
  LED led_118 (.in(creator_noai_1_f1[1]));
  LED led_119 (.in(creator_noai_1_f1[0]));
  LED led_120 (.in(creator_noai_1_f1[0]));
  LED led_121 (.in(creator_noai_1_f0[1]));
  LED led_122 (.in(creator_noai_1_f0[1]));
  LED led_123 (.in(creator_noai_1_f0[0]));
  LED led_124 (.in(creator_noai_1_f0[0]));
  LED led_125 (.in(creator_noai_1_f0[1]));
  LED led_126 (.in(creator_noai_1_f0[1]));
  LED led_127 (.in(creator_noai_1_f0[0]));
  LED led_128 (.in(creator_noai_1_f0[0]));
  LED led_129 (.in(creator_2_f3[1]));
  LED led_130 (.in(creator_2_f3[1]));
  LED led_131 (.in(creator_2_f3[2]));
  LED led_132 (.in(creator_2_f3[2]));
  LED led_133 (.in(creator_2_f3[1]));
  LED led_134 (.in(creator_2_f3[1]));
  LED led_135 (.in(creator_2_f3[2]));
  LED led_136 (.in(creator_2_f3[2]));
  LED led_137 (.in(creator_2_f2[1]));
  LED led_138 (.in(creator_2_f2[1]));
  LED led_139 (.in(creator_2_f2[2]));
  LED led_140 (.in(creator_2_f2[2]));
  LED led_141 (.in(creator_2_f2[1]));
  LED led_142 (.in(creator_2_f2[1]));
  LED led_143 (.in(creator_2_f2[2]));
  LED led_144 (.in(creator_2_f2[2]));
  LED led_145 (.in(creator_2_f1[1]));
  LED led_146 (.in(creator_2_f1[1]));
  LED led_147 (.in(creator_2_f1[2]));
  LED led_148 (.in(creator_2_f1[2]));
  LED led_149 (.in(creator_2_f1[1]));
  LED led_150 (.in(creator_2_f1[1]));
  LED led_151 (.in(creator_2_f1[2]));
  LED led_152 (.in(creator_2_f1[2]));
  LED led_153 (.in(creator_2_f0[1]));
  LED led_154 (.in(creator_2_f0[1]));
  LED led_155 (.in(creator_2_f0[2]));
  LED led_156 (.in(creator_2_f0[2]));
  LED led_157 (.in(creator_2_f0[1]));
  LED led_158 (.in(creator_2_f0[1]));
  LED led_159 (.in(creator_2_f0[2]));
  LED led_160 (.in(creator_2_f0[2]));
  LED led_161 (.in(creator_noai_1_f3[1]));
  LED led_162 (.in(creator_noai_1_f3[1]));
  LED led_163 (.in(creator_noai_1_f3[2]));
  LED led_164 (.in(creator_noai_1_f3[2]));
  LED led_165 (.in(creator_noai_1_f3[1]));
  LED led_166 (.in(creator_noai_1_f3[1]));
  LED led_167 (.in(creator_noai_1_f3[2]));
  LED led_168 (.in(creator_noai_1_f3[2]));
  LED led_169 (.in(creator_noai_1_f2[1]));
  LED led_170 (.in(creator_noai_1_f2[1]));
  LED led_171 (.in(creator_noai_1_f2[2]));
  LED led_172 (.in(creator_noai_1_f2[2]));
  LED led_173 (.in(creator_noai_1_f2[1]));
  LED led_174 (.in(creator_noai_1_f2[1]));
  LED led_175 (.in(creator_noai_1_f2[2]));
  LED led_176 (.in(creator_noai_1_f2[2]));
  LED led_177 (.in(creator_noai_1_f1[1]));
  LED led_178 (.in(creator_noai_1_f1[1]));
  LED led_179 (.in(creator_noai_1_f1[2]));
  LED led_180 (.in(creator_noai_1_f1[2]));
  LED led_181 (.in(creator_noai_1_f1[1]));
  LED led_182 (.in(creator_noai_1_f1[1]));
  LED led_183 (.in(creator_noai_1_f1[2]));
  LED led_184 (.in(creator_noai_1_f1[2]));
  LED led_185 (.in(creator_noai_1_f0[1]));
  LED led_186 (.in(creator_noai_1_f0[1]));
  LED led_187 (.in(creator_noai_1_f0[2]));
  LED led_188 (.in(creator_noai_1_f0[2]));
  LED led_189 (.in(creator_noai_1_f0[1]));
  LED led_190 (.in(creator_noai_1_f0[1]));
  LED led_191 (.in(creator_noai_1_f0[2]));
  LED led_192 (.in(creator_noai_1_f0[2]));
  LED led_193 (.in(creator_2_f3[3]));
  LED led_194 (.in(creator_2_f3[3]));
  LED led_195 (.in(creator_2_f3[3]));
  LED led_196 (.in(creator_2_f3[3]));
  LED led_197 (.in(creator_2_f2[3]));
  LED led_198 (.in(creator_2_f2[3]));
  LED led_199 (.in(creator_2_f2[3]));
  LED led_200 (.in(creator_2_f2[3]));
  LED led_201 (.in(creator_2_f1[3]));
  LED led_202 (.in(creator_2_f1[3]));
  LED led_203 (.in(creator_2_f1[3]));
  LED led_204 (.in(creator_2_f1[3]));
  LED led_205 (.in(creator_2_f0[3]));
  LED led_206 (.in(creator_2_f0[3]));
  LED led_207 (.in(creator_2_f0[3]));
  LED led_208 (.in(creator_2_f0[3]));
  LED led_209 (.in(creator_noai_1_f3[3]));
  LED led_210 (.in(creator_noai_1_f3[3]));
  LED led_211 (.in(creator_noai_1_f3[3]));
  LED led_212 (.in(creator_noai_1_f3[3]));
  LED led_213 (.in(creator_noai_1_f2[3]));
  LED led_214 (.in(creator_noai_1_f2[3]));
  LED led_215 (.in(creator_noai_1_f2[3]));
  LED led_216 (.in(creator_noai_1_f2[3]));
  LED led_217 (.in(creator_noai_1_f1[3]));
  LED led_218 (.in(creator_noai_1_f1[3]));
  LED led_219 (.in(creator_noai_1_f1[3]));
  LED led_220 (.in(creator_noai_1_f1[3]));
  LED led_221 (.in(creator_noai_1_f0[3]));
  LED led_222 (.in(creator_noai_1_f0[3]));
  LED led_223 (.in(creator_noai_1_f0[3]));
  LED led_224 (.in(creator_noai_1_f0[3]));
  EATER_ROM eater_rom_1 (.n(n), .F3(eater_rom_1_f3), .F2(eater_rom_1_f2), .F0(eater_rom_1_f0), .F1(eater_rom_1_f1));
  CREATOR_4bit creator_4bit_1 (.n(and_1_out), .F2(creator_4bit_1_f2), .F0(creator_4bit_1_f0), .F1(creator_4bit_1_f1));
  LED led_225 (.in(eater_rom_1_f3[3]));
  LED led_226 (.in(eater_rom_1_f3[3]));
  LED led_227 (.in(eater_rom_1_f3[3]));
  LED led_228 (.in(eater_rom_1_f3[3]));
  LED led_229 (.in(eater_rom_1_f2[3]));
  LED led_230 (.in(eater_rom_1_f2[3]));
  LED led_231 (.in(eater_rom_1_f2[3]));
  LED led_232 (.in(eater_rom_1_f2[3]));
  LED led_233 (.in(eater_rom_1_f1[3]));
  LED led_234 (.in(eater_rom_1_f1[3]));
  LED led_235 (.in(eater_rom_1_f1[3]));
  LED led_236 (.in(eater_rom_1_f1[3]));
  LED led_237 (.in(eater_rom_1_f0[3]));
  LED led_238 (.in(eater_rom_1_f0[3]));
  LED led_239 (.in(eater_rom_1_f0[3]));
  LED led_240 (.in(eater_rom_1_f0[3]));
  assign bit_extender_1_out = {{3{n[4]}}, n[4]};  // Bit_Extender bit_extender_1
  assign and_1_out = ~bit_extender_1_out & n[3:0];  // AND_Gate and_1, 4 bits wide
  LED led_241 (.in(creator_4bit_1_f2[3]));
  LED led_242 (.in(creator_4bit_1_f2[3]));
  LED led_243 (.in(creator_4bit_1_f2[3]));
  LED led_244 (.in(creator_4bit_1_f2[3]));
  LED led_245 (.in(creator_4bit_1_f1[3]));
  LED led_246 (.in(creator_4bit_1_f1[3]));
  LED led_247 (.in(creator_4bit_1_f1[3]));
  LED led_248 (.in(creator_4bit_1_f1[3]));
  LED led_249 (.in(creator_4bit_1_f0[3]));
  LED led_250 (.in(creator_4bit_1_f0[3]));
  LED led_251 (.in(creator_4bit_1_f0[3]));
  LED led_252 (.in(creator_4bit_1_f0[3]));
  LED led_253 (.in(eater_rom_1_f3[2]));
  LED led_254 (.in(eater_rom_1_f3[2]));
  LED led_255 (.in(eater_rom_1_f3[1]));
  LED led_256 (.in(eater_rom_1_f3[1]));
  LED led_257 (.in(eater_rom_1_f3[2]));
  LED led_258 (.in(eater_rom_1_f3[2]));
  LED led_259 (.in(eater_rom_1_f3[1]));
  LED led_260 (.in(eater_rom_1_f3[1]));
  LED led_261 (.in(eater_rom_1_f2[2]));
  LED led_262 (.in(eater_rom_1_f2[2]));
  LED led_263 (.in(eater_rom_1_f2[1]));
  LED led_264 (.in(eater_rom_1_f2[1]));
  LED led_265 (.in(eater_rom_1_f2[2]));
  LED led_266 (.in(eater_rom_1_f2[2]));
  LED led_267 (.in(eater_rom_1_f2[1]));
  LED led_268 (.in(eater_rom_1_f2[1]));
  LED led_269 (.in(eater_rom_1_f1[2]));
  LED led_270 (.in(eater_rom_1_f1[2]));
  LED led_271 (.in(eater_rom_1_f1[1]));
  LED led_272 (.in(eater_rom_1_f1[1]));
  LED led_273 (.in(eater_rom_1_f1[2]));
  LED led_274 (.in(eater_rom_1_f1[2]));
  LED led_275 (.in(eater_rom_1_f1[1]));
  LED led_276 (.in(eater_rom_1_f1[1]));
  LED led_277 (.in(eater_rom_1_f0[2]));
  LED led_278 (.in(eater_rom_1_f0[2]));
  LED led_279 (.in(eater_rom_1_f0[1]));
  LED led_280 (.in(eater_rom_1_f0[1]));
  LED led_281 (.in(eater_rom_1_f0[2]));
  LED led_282 (.in(eater_rom_1_f0[2]));
  LED led_283 (.in(eater_rom_1_f0[1]));
  LED led_284 (.in(eater_rom_1_f0[1]));
  LED led_285 (.in(creator_4bit_1_f2[2]));
  LED led_286 (.in(creator_4bit_1_f2[2]));
  LED led_287 (.in(creator_4bit_1_f2[1]));
  LED led_288 (.in(creator_4bit_1_f2[1]));
  LED led_289 (.in(creator_4bit_1_f2[2]));
  LED led_290 (.in(creator_4bit_1_f2[2]));
  LED led_291 (.in(creator_4bit_1_f2[1]));
  LED led_292 (.in(creator_4bit_1_f2[1]));
  LED led_293 (.in(creator_4bit_1_f1[2]));
  LED led_294 (.in(creator_4bit_1_f1[2]));
  LED led_295 (.in(creator_4bit_1_f1[1]));
  LED led_296 (.in(creator_4bit_1_f1[1]));
  LED led_297 (.in(creator_4bit_1_f1[2]));
  LED led_298 (.in(creator_4bit_1_f1[2]));
  LED led_299 (.in(creator_4bit_1_f1[1]));
  LED led_300 (.in(creator_4bit_1_f1[1]));
  LED led_301 (.in(creator_4bit_1_f0[2]));
  LED led_302 (.in(creator_4bit_1_f0[2]));
  LED led_303 (.in(creator_4bit_1_f0[1]));
  LED led_304 (.in(creator_4bit_1_f0[1]));
  LED led_305 (.in(creator_4bit_1_f0[2]));
  LED led_306 (.in(creator_4bit_1_f0[2]));
  LED led_307 (.in(creator_4bit_1_f0[1]));
  LED led_308 (.in(creator_4bit_1_f0[1]));
  LED led_309 (.in(eater_rom_1_f3[0]));
  LED led_310 (.in(eater_rom_1_f3[0]));
  LED led_311 (.in(eater_rom_1_f3[1]));
  LED led_312 (.in(eater_rom_1_f3[1]));
  LED led_313 (.in(eater_rom_1_f3[0]));
  LED led_314 (.in(eater_rom_1_f3[0]));
  LED led_315 (.in(eater_rom_1_f3[1]));
  LED led_316 (.in(eater_rom_1_f3[1]));
  LED led_317 (.in(eater_rom_1_f2[0]));
  LED led_318 (.in(eater_rom_1_f2[0]));
  LED led_319 (.in(eater_rom_1_f2[1]));
  LED led_320 (.in(eater_rom_1_f2[1]));
  LED led_321 (.in(eater_rom_1_f2[0]));
  LED led_322 (.in(eater_rom_1_f2[0]));
  LED led_323 (.in(eater_rom_1_f2[1]));
  LED led_324 (.in(eater_rom_1_f2[1]));
  LED led_325 (.in(eater_rom_1_f1[0]));
  LED led_326 (.in(eater_rom_1_f1[0]));
  LED led_327 (.in(eater_rom_1_f1[1]));
  LED led_328 (.in(eater_rom_1_f1[1]));
  LED led_329 (.in(eater_rom_1_f1[0]));
  LED led_330 (.in(eater_rom_1_f1[0]));
  LED led_331 (.in(eater_rom_1_f1[1]));
  LED led_332 (.in(eater_rom_1_f1[1]));
  LED led_333 (.in(eater_rom_1_f0[0]));
  LED led_334 (.in(eater_rom_1_f0[0]));
  LED led_335 (.in(eater_rom_1_f0[1]));
  LED led_336 (.in(eater_rom_1_f0[1]));
  LED led_337 (.in(eater_rom_1_f0[0]));
  LED led_338 (.in(eater_rom_1_f0[0]));
  LED led_339 (.in(eater_rom_1_f0[1]));
  LED led_340 (.in(eater_rom_1_f0[1]));
  LED led_341 (.in(creator_4bit_1_f2[0]));
  LED led_342 (.in(creator_4bit_1_f2[0]));
  LED led_343 (.in(creator_4bit_1_f2[1]));
  LED led_344 (.in(creator_4bit_1_f2[1]));
  LED led_345 (.in(creator_4bit_1_f2[0]));
  LED led_346 (.in(creator_4bit_1_f2[0]));
  LED led_347 (.in(creator_4bit_1_f2[1]));
  LED led_348 (.in(creator_4bit_1_f2[1]));
  LED led_349 (.in(creator_4bit_1_f1[0]));
  LED led_350 (.in(creator_4bit_1_f1[0]));
  LED led_351 (.in(creator_4bit_1_f1[1]));
  LED led_352 (.in(creator_4bit_1_f1[1]));
  LED led_353 (.in(creator_4bit_1_f1[0]));
  LED led_354 (.in(creator_4bit_1_f1[0]));
  LED led_355 (.in(creator_4bit_1_f1[1]));
  LED led_356 (.in(creator_4bit_1_f1[1]));
  LED led_357 (.in(creator_4bit_1_f0[0]));
  LED led_358 (.in(creator_4bit_1_f0[0]));
  LED led_359 (.in(creator_4bit_1_f0[1]));
  LED led_360 (.in(creator_4bit_1_f0[1]));
  LED led_361 (.in(creator_4bit_1_f0[0]));
  LED led_362 (.in(creator_4bit_1_f0[0]));
  LED led_363 (.in(creator_4bit_1_f0[1]));
  LED led_364 (.in(creator_4bit_1_f0[1]));
  LED led_365 (.in(eater_rom_1_f3[2]));
  LED led_366 (.in(eater_rom_1_f3[2]));
  LED led_367 (.in(eater_rom_1_f3[3]));
  LED led_368 (.in(eater_rom_1_f3[3]));
  LED led_369 (.in(eater_rom_1_f3[2]));
  LED led_370 (.in(eater_rom_1_f3[2]));
  LED led_371 (.in(eater_rom_1_f3[3]));
  LED led_372 (.in(eater_rom_1_f3[3]));
  LED led_373 (.in(eater_rom_1_f2[2]));
  LED led_374 (.in(eater_rom_1_f2[2]));
  LED led_375 (.in(eater_rom_1_f2[3]));
  LED led_376 (.in(eater_rom_1_f2[3]));
  LED led_377 (.in(eater_rom_1_f2[2]));
  LED led_378 (.in(eater_rom_1_f2[2]));
  LED led_379 (.in(eater_rom_1_f2[3]));
  LED led_380 (.in(eater_rom_1_f2[3]));
  LED led_381 (.in(eater_rom_1_f1[2]));
  LED led_382 (.in(eater_rom_1_f1[2]));
  LED led_383 (.in(eater_rom_1_f1[3]));
  LED led_384 (.in(eater_rom_1_f1[3]));
  LED led_385 (.in(eater_rom_1_f1[2]));
  LED led_386 (.in(eater_rom_1_f1[2]));
  LED led_387 (.in(eater_rom_1_f1[3]));
  LED led_388 (.in(eater_rom_1_f1[3]));
  LED led_389 (.in(eater_rom_1_f0[2]));
  LED led_390 (.in(eater_rom_1_f0[2]));
  LED led_391 (.in(eater_rom_1_f0[3]));
  LED led_392 (.in(eater_rom_1_f0[3]));
  LED led_393 (.in(eater_rom_1_f0[2]));
  LED led_394 (.in(eater_rom_1_f0[2]));
  LED led_395 (.in(eater_rom_1_f0[3]));
  LED led_396 (.in(eater_rom_1_f0[3]));
  LED led_397 (.in(creator_4bit_1_f2[2]));
  LED led_398 (.in(creator_4bit_1_f2[2]));
  LED led_399 (.in(creator_4bit_1_f2[3]));
  LED led_400 (.in(creator_4bit_1_f2[3]));
  LED led_401 (.in(creator_4bit_1_f2[2]));
  LED led_402 (.in(creator_4bit_1_f2[2]));
  LED led_403 (.in(creator_4bit_1_f2[3]));
  LED led_404 (.in(creator_4bit_1_f2[3]));
  LED led_405 (.in(creator_4bit_1_f1[2]));
  LED led_406 (.in(creator_4bit_1_f1[2]));
  LED led_407 (.in(creator_4bit_1_f1[3]));
  LED led_408 (.in(creator_4bit_1_f1[3]));
  LED led_409 (.in(creator_4bit_1_f1[2]));
  LED led_410 (.in(creator_4bit_1_f1[2]));
  LED led_411 (.in(creator_4bit_1_f1[3]));
  LED led_412 (.in(creator_4bit_1_f1[3]));
  LED led_413 (.in(creator_4bit_1_f0[2]));
  LED led_414 (.in(creator_4bit_1_f0[2]));
  LED led_415 (.in(creator_4bit_1_f0[3]));
  LED led_416 (.in(creator_4bit_1_f0[3]));
  LED led_417 (.in(creator_4bit_1_f0[2]));
  LED led_418 (.in(creator_4bit_1_f0[2]));
  LED led_419 (.in(creator_4bit_1_f0[3]));
  LED led_420 (.in(creator_4bit_1_f0[3]));

  // Notes on the sheet:
  //   Wiring
  //   CREATOR
  //   No AI
  //   Showcase
  //   ROM
  //   4 bits
endmodule

module EATER (
  input  [4:0] n,
  output C0,
  output C1,
  output C2,
  output R0,
  output R1
);

  wire and_1_out, and_2_out, and_3_out, and_4_out, and_5_out, and_6_out, and_7_out, and_8_out, and_9_out,
       and_10_out, and_11_out, or_2_out, or_4_out, or_7_out, variables_1_a, variables_1_b, variables_1_c,
       variables_1_d, variables_1_e, variables_1_f, variables_1_g, variables_1_y0, variables_1_y1,
       variables_1_y2, xor_1_out, xor_2_out, xor_3_out, xor_4_out;

  VARIABLES variables_1 (
    .n(n), .y0(variables_1_y0), .y1(variables_1_y1), .y2(variables_1_y2), .a(variables_1_a),
    .b(variables_1_b), .c(variables_1_c), .d(variables_1_d), .e(variables_1_e), .f(variables_1_f),
    .g(variables_1_g));
  and and_1 (and_1_out, variables_1_g, variables_1_f);
  or or_1 (R1, variables_1_d, and_1_out);
  and and_2 (and_2_out, variables_1_g, ~variables_1_f);  // AND_Gate
  or or_2 (or_2_out, variables_1_b, ~n[3]);  // OR_Gate
  or or_3 (R0, and_2_out, variables_1_d, and_4_out);
  or or_4 (or_4_out, n[1], n[0]);
  and and_3 (and_3_out, variables_1_e, ~variables_1_y1, ~n[0]);  // AND_Gate
  and and_4 (and_4_out, or_2_out, variables_1_e, or_4_out);
  xor xor_1 (xor_1_out, n[4], n[3]);
  and and_5 (and_5_out, ~n[2], n[0]);  // AND_Gate
  and and_6 (and_6_out, xor_1_out, variables_1_y1, and_5_out);
  or or_5 (C2, and_3_out, and_6_out);
  xor xor_2 (xor_2_out, n[1], n[0]);
  and and_7 (and_7_out, variables_1_d, xor_2_out);
  and and_8 (and_8_out, variables_1_a, or_7_out);
  or or_6 (C1, and_7_out, and_8_out);
  or or_7 (or_7_out, ~variables_1_y2, variables_1_y0);  // OR_Gate
  xor xor_3 (xor_3_out, n[4], n[0]);
  and and_9 (and_9_out, xor_3_out, ~variables_1_c);  // AND_Gate
  and and_10 (and_10_out, variables_1_b, ~n[4], ~n[2]);  // AND_Gate
  xor xor_4 (xor_4_out, variables_1_y0, n[2]);
  and and_11 (and_11_out, variables_1_a, xor_4_out);
  or or_8 (C0, and_9_out, and_10_out, and_11_out);

  // Notes on the sheet:
  //   x0
  //   x1
  //   x2
  //   x3
  //   x4
  //   R1
  //   R0
  //   C2
  //   C1
  //   C0
endmodule

module EATER_noAI (
  input  [4:0] n,
  output C0,
  output C1,
  output C2,
  output R0,
  output R1
);

  wire and_1_out, and_2_out, and_3_out, and_4_out, and_5_out, and_6_out, and_7_out, and_8_out, and_9_out,
       and_10_out, and_11_out, and_12_out, and_13_out, and_14_out, and_15_out, and_16_out, and_17_out,
       and_18_out, and_19_out, and_20_out, and_21_out, and_22_out, and_23_out, and_24_out, and_25_out,
       and_26_out, and_27_out, and_28_out, nor_1_out, nor_2_out, nor_3_out, nor_4_out, nor_5_out, nor_6_out,
       or_1_out, or_3_out, or_5_out, or_6_out, or_8_out, or_9_out, or_11_out, or_12_out, xor_1_out, xor_2_out;

  and and_1 (and_1_out, n[4], ~n[3], ~n[2]);  // AND_Gate
  and and_2 (and_2_out, ~n[4], n[3]);  // AND_Gate
  or or_1 (or_1_out, n[2], n[1]);
  and and_3 (and_3_out, and_2_out, or_1_out);
  or or_2 (R1, and_1_out, and_3_out);
  and and_4 (and_4_out, n[4], ~n[3], ~n[2]);  // AND_Gate
  and and_5 (and_5_out, ~n[4], n[3]);  // AND_Gate
  and and_6 (and_6_out, n[2], n[1], n[0]);
  nor nor_1 (nor_1_out, n[2], n[1]);
  nor nor_2 (nor_2_out, n[4], n[3]);
  or or_3 (or_3_out, nor_1_out, and_6_out);
  and and_7 (and_7_out, and_5_out, or_3_out);
  or or_4 (R0, and_4_out, and_7_out, and_9_out);
  or or_5 (or_5_out, n[1], n[0]);
  and and_8 (and_8_out, n[2], or_5_out);
  and and_9 (and_9_out, nor_2_out, and_8_out);
  and and_10 (and_10_out, ~n[2], n[0]);  // AND_Gate
  and and_11 (and_11_out, n[4], ~n[3], n[1]);  // AND_Gate
  and and_12 (and_12_out, ~n[4], n[3], ~n[1]);  // AND_Gate
  or or_6 (or_6_out, and_11_out, and_12_out);
  and and_13 (and_13_out, and_10_out, or_6_out);
  or or_7 (C2, and_13_out, and_16_out);
  and and_14 (and_14_out, ~n[4], n[2], ~n[0]);  // AND_Gate
  and and_15 (and_15_out, n[3], n[1]);
  nor nor_3 (nor_3_out, n[3], n[1]);
  or or_8 (or_8_out, and_15_out, nor_3_out);
  and and_16 (and_16_out, and_14_out, or_8_out);
  and and_17 (and_17_out, ~n[4], ~n[3], n[1], n[0]);  // AND_Gate
  and and_18 (and_18_out, n[4], ~n[1], n[0]);  // AND_Gate
  and and_19 (and_19_out, n[1], ~n[0]);  // AND_Gate
  nor nor_4 (nor_4_out, n[3], n[2]);
  or or_9 (or_9_out, and_18_out, and_19_out);
  and and_20 (and_20_out, nor_4_out, or_9_out);
  or or_10 (C1, and_17_out, and_20_out, and_22_out);
  or or_11 (or_11_out, n[2], ~n[0]);  // OR_Gate
  and and_21 (and_21_out, ~n[4], n[3], ~n[1]);  // AND_Gate
  and and_22 (and_22_out, or_11_out, and_21_out);
  xor xor_1 (xor_1_out, n[4], n[0]);
  nor nor_5 (nor_5_out, n[3], n[2]);
  and and_23 (and_23_out, xor_1_out, nor_5_out);
  and and_24 (and_24_out, n[3], ~n[2], ~n[1]);  // AND_Gate
  and and_25 (and_25_out, ~n[3], n[2], n[1]);  // AND_Gate
  nor nor_6 (nor_6_out, n[4], n[0]);
  or or_12 (or_12_out, and_24_out, and_25_out);
  and and_26 (and_26_out, nor_6_out, or_12_out);
  or or_13 (C0, and_23_out, and_26_out, and_28_out);
  and and_27 (and_27_out, ~n[4], n[3], n[0]);  // AND_Gate
  xor xor_2 (xor_2_out, n[2], n[1]);
  and and_28 (and_28_out, and_27_out, xor_2_out);

  // Notes on the sheet:
  //   R1
  //   R0
  //   C2
  //   C1
  //   C0
endmodule

module EATER_4bit (
  input  [3:0] n,
  output C0,
  output C1,
  output C2,
  output R0,
  output R1
);

  wire and_2_out, and_3_out, and_4_out, and_6_out, and_7_out, and_8_out, or_1_out, or_2_out, or_5_out,
       variables_4_1_b, variables_4_1_f, variables_4_1_h, variables_4_1_y0, variables_4_1_y1,
       variables_4_1_y2, xor_1_out;

  VARIABLES_4 variables_4_1 (
    .n(n), .y0(variables_4_1_y0), .y1(variables_4_1_y1), .y2(variables_4_1_y2), .b(variables_4_1_b),
    .f(variables_4_1_f), .h(variables_4_1_h));
  and and_1 (R1, variables_4_1_f, n[3]);
  or or_1 (or_1_out, variables_4_1_b, ~n[3]);  // OR_Gate
  or or_2 (or_2_out, n[1], n[0]);
  and and_2 (and_2_out, or_1_out, n[2], or_2_out);
  or or_3 (R0, variables_4_1_h, and_2_out);
  and and_3 (and_3_out, variables_4_1_h, n[0]);
  and and_4 (and_4_out, ~variables_4_1_y1, n[2], ~n[0]);  // AND_Gate
  or or_4 (C2, and_3_out, and_4_out);
  or or_5 (or_5_out, ~variables_4_1_y2, variables_4_1_y0);  // OR_Gate
  and and_5 (C1, variables_4_1_y1, or_5_out);
  and and_6 (and_6_out, ~variables_4_1_f, variables_4_1_y0);  // AND_Gate
  and and_7 (and_7_out, variables_4_1_b, ~n[2]);  // AND_Gate
  or or_6 (C0, and_6_out, and_7_out, and_8_out);
  xor xor_1 (xor_1_out, n[2], variables_4_1_y0);
  and and_8 (and_8_out, variables_4_1_y1, xor_1_out);

  // Notes on the sheet:
  //   x0
  //   x1
  //   x2
  //   x3
  //   R1
  //   R0
  //   C2
  //   C1
  //   C0
endmodule

module EATER_ROM (
  input  [4:0] n,
  output [3:0] F3,
  output [3:0] F2,
  output [3:0] F0,
  output [3:0] F1
);

  ROM #(.addrWidth(5), .dataWidth(16)) rom_1 (.addr(n), .data({F3, F2, F1, F0}));

  // Notes on the sheet:
  //   contents of rom_1 (hex, n*v repeats v):
  //   787 1 2 5 a f 1f 2f 5f af ff 1ff 2ff 5ff aff fff 1fff 2fff 5fff afff 787 787 787 787 787 787 787 787
  //   787 787 787 787
endmodule

module VARIABLES (
  input  [4:0] n,
  output y0,
  output y1,
  output y2,
  output a,
  output b,
  output c,
  output d,
  output e,
  output f,
  output g
);

  xor xor_1 (y0, n[0], n[3]);
  xor xor_2 (y1, n[1], n[3]);
  xor xor_3 (y2, n[2], n[3]);
  and and_1 (a, y1, ~n[4]);  // AND_Gate
  and and_2 (b, n[0], n[1]);
  or or_1 (c, n[2], n[3]);
  and and_3 (d, ~c, n[4]);  // AND_Gate
  and and_4 (e, n[2], ~n[4]);  // AND_Gate
  or or_2 (f, n[1], n[2]);
  and and_5 (g, n[3], ~n[4]);  // AND_Gate
endmodule

module VARIABLES_4 (
  input  [3:0] n,
  output y0,
  output y1,
  output y2,
  output b,
  output f,
  output h
);

  xor xor_1 (y0, n[0], n[3]);
  xor xor_2 (y1, n[1], n[3]);
  xor xor_3 (y2, n[2], n[3]);
  and and_1 (b, n[0], n[1]);
  or or_1 (f, n[1], n[2]);
  and and_2 (h, ~f, n[3]);  // AND_Gate
endmodule

module CREATOR (
  input  [4:0] n,
  output [3:0] F3,
  output [3:0] F2,
  output [3:0] F0,
  output [3:0] F1
);

  wire and_1_out, and_3_out, eater_1_c1, eater_1_r0, eater_1_r1, nor_1_out, or_1_out;
  wire [3:0] and_7_out, and_8_out, bit_extender_1_out, bit_extender_2_out, bit_extender_3_out, eater_1_c0,
       or_4_out, or_5_out;
  wire [3:2] and_5_out;

  EATER eater_1 (.n(n), .C0(eater_1_c0[0]), .C1(eater_1_c1), .C2(eater_1_c0[3]), .R0(eater_1_r0), .R1(eater_1_r1));
  nor nor_1 (nor_1_out, eater_1_r1, eater_1_r0, eater_1_c0[3], eater_1_c1, eater_1_c0[0]);
  and and_1 (and_1_out, ~eater_1_c0[0], eater_1_c1);  // AND_Gate
  and and_2 (eater_1_c0[2], eater_1_c0[0], eater_1_c1);
  and and_3 (and_3_out, eater_1_r0, eater_1_r1);
  or or_1 (or_1_out, eater_1_r0, eater_1_r1);
  and and_4 (and_5_out[3], nor_1_out, 1'b1);
  and and_5 (and_5_out[2], nor_1_out, 1'b0);
  or or_2 (eater_1_c0[1], and_1_out, eater_1_c0[3]);
  assign bit_extender_1_out = {{3{and_3_out}}, and_3_out};  // Bit_Extender bit_extender_1
  assign bit_extender_2_out = {{3{eater_1_r1}}, eater_1_r1};  // Bit_Extender bit_extender_2
  assign bit_extender_3_out = {{3{or_1_out}}, or_1_out};  // Bit_Extender bit_extender_3
  assign F2 = {and_5_out[2], {3{and_5_out[3]}}} | and_7_out;  // OR_Gate or_3, 4 bits wide
  assign F3 = bit_extender_1_out & eater_1_c0;  // AND_Gate and_6, 4 bits wide
  assign and_7_out = bit_extender_2_out & or_4_out;  // AND_Gate and_7, 4 bits wide
  assign or_4_out = bit_extender_1_out | eater_1_c0;  // OR_Gate or_4, 4 bits wide
  assign or_5_out = bit_extender_2_out | eater_1_c0;  // OR_Gate or_5, 4 bits wide
  assign F0 = {and_5_out[2], {3{and_5_out[3]}}} | bit_extender_3_out | eater_1_c0;  // OR_Gate or_6, 4 bits wide
  assign and_8_out = bit_extender_3_out & or_5_out;  // AND_Gate and_8, 4 bits wide
  assign F1 = {and_5_out, {2{and_5_out[2]}}} | and_8_out;  // OR_Gate or_7, 4 bits wide

  // Notes on the sheet:
  //   EATER
endmodule

module CREATOR_noAI (
  input  [4:0] n,
  output [3:0] F3,
  output [3:0] F2,
  output [3:0] F0,
  output [3:0] F1
);

  wire and_1_out, and_3_out, eater_noai_1_c1, eater_noai_1_r0, eater_noai_1_r1, nor_1_out, or_1_out;
  wire [3:0] and_7_out, and_8_out, bit_extender_1_out, bit_extender_2_out, bit_extender_3_out,
       eater_noai_1_c0, or_4_out, or_5_out;
  wire [3:2] and_5_out;

  EATER_noAI eater_noai_1 (
    .n(n), .C0(eater_noai_1_c0[0]), .C1(eater_noai_1_c1), .C2(eater_noai_1_c0[3]), .R0(eater_noai_1_r0),
    .R1(eater_noai_1_r1));
  nor nor_1 (nor_1_out, eater_noai_1_r1, eater_noai_1_r0, eater_noai_1_c0[3], eater_noai_1_c1, eater_noai_1_c0[0]);
  and and_1 (and_1_out, ~eater_noai_1_c0[0], eater_noai_1_c1);  // AND_Gate
  and and_2 (eater_noai_1_c0[2], eater_noai_1_c0[0], eater_noai_1_c1);
  and and_3 (and_3_out, eater_noai_1_r0, eater_noai_1_r1);
  or or_1 (or_1_out, eater_noai_1_r0, eater_noai_1_r1);
  and and_4 (and_5_out[3], nor_1_out, 1'b1);
  and and_5 (and_5_out[2], nor_1_out, 1'b0);
  or or_2 (eater_noai_1_c0[1], and_1_out, eater_noai_1_c0[3]);
  assign bit_extender_1_out = {{3{and_3_out}}, and_3_out};  // Bit_Extender bit_extender_1
  assign bit_extender_2_out = {{3{eater_noai_1_r1}}, eater_noai_1_r1};  // Bit_Extender bit_extender_2
  assign bit_extender_3_out = {{3{or_1_out}}, or_1_out};  // Bit_Extender bit_extender_3
  assign F2 = {and_5_out[2], {3{and_5_out[3]}}} | and_7_out;  // OR_Gate or_3, 4 bits wide
  assign F3 = bit_extender_1_out & eater_noai_1_c0;  // AND_Gate and_6, 4 bits wide
  assign and_7_out = bit_extender_2_out & or_4_out;  // AND_Gate and_7, 4 bits wide
  assign or_4_out = bit_extender_1_out | eater_noai_1_c0;  // OR_Gate or_4, 4 bits wide
  assign or_5_out = bit_extender_2_out | eater_noai_1_c0;  // OR_Gate or_5, 4 bits wide
  assign F0 = {and_5_out[2], {3{and_5_out[3]}}} | bit_extender_3_out | eater_noai_1_c0;  // OR_Gate or_6, 4 bits wide
  assign and_8_out = bit_extender_3_out & or_5_out;  // AND_Gate and_8, 4 bits wide
  assign F1 = {and_5_out, {2{and_5_out[2]}}} | and_8_out;  // OR_Gate or_7, 4 bits wide

  // Notes on the sheet:
  //   EATER no AI
endmodule

module CREATOR_4bit (
  input  [3:0] n,
  output [3:0] F2,
  output [3:0] F0,
  output [3:0] F1
);

  wire and_1_out, and_3_out, eater_4bit_1_c1, eater_4bit_1_r0, eater_4bit_1_r1, nor_1_out, or_1_out;
  wire [3:0] and_6_out, and_7_out, bit_extender_1_out, bit_extender_2_out, bit_extender_3_out,
       eater_4bit_1_c0, or_4_out, or_5_out;
  wire [3:2] and_5_out;

  EATER_4bit eater_4bit_1 (
    .n(n), .C0(eater_4bit_1_c0[0]), .C1(eater_4bit_1_c1), .C2(eater_4bit_1_c0[3]), .R0(eater_4bit_1_r0),
    .R1(eater_4bit_1_r1));
  nor nor_1 (nor_1_out, eater_4bit_1_r1, eater_4bit_1_r0, eater_4bit_1_c0[3], eater_4bit_1_c1, eater_4bit_1_c0[0]);
  and and_1 (and_1_out, ~eater_4bit_1_c0[0], eater_4bit_1_c1);  // AND_Gate
  and and_2 (eater_4bit_1_c0[2], eater_4bit_1_c0[0], eater_4bit_1_c1);
  and and_3 (and_3_out, eater_4bit_1_r0, eater_4bit_1_r1);
  or or_1 (or_1_out, eater_4bit_1_r0, eater_4bit_1_r1);
  and and_4 (and_5_out[3], nor_1_out, 1'b1);
  and and_5 (and_5_out[2], nor_1_out, 1'b0);
  or or_2 (eater_4bit_1_c0[1], and_1_out, eater_4bit_1_c0[3]);
  assign bit_extender_1_out = {{3{and_3_out}}, and_3_out};  // Bit_Extender bit_extender_1
  assign bit_extender_2_out = {{3{eater_4bit_1_r1}}, eater_4bit_1_r1};  // Bit_Extender bit_extender_2
  assign bit_extender_3_out = {{3{or_1_out}}, or_1_out};  // Bit_Extender bit_extender_3
  assign F2 = {and_5_out[2], {3{and_5_out[3]}}} | and_6_out;  // OR_Gate or_3, 4 bits wide
  assign and_6_out = bit_extender_2_out & or_4_out;  // AND_Gate and_6, 4 bits wide
  assign or_4_out = bit_extender_1_out | eater_4bit_1_c0;  // OR_Gate or_4, 4 bits wide
  assign or_5_out = bit_extender_2_out | eater_4bit_1_c0;  // OR_Gate or_5, 4 bits wide
  assign F0 = {and_5_out[2], {3{and_5_out[3]}}} | bit_extender_3_out | eater_4bit_1_c0;  // OR_Gate or_6, 4 bits wide
  assign and_7_out = bit_extender_3_out & or_5_out;  // AND_Gate and_7, 4 bits wide
  assign F1 = {and_5_out, {2{and_5_out[2]}}} | and_7_out;  // OR_Gate or_7, 4 bits wide

  // Notes on the sheet:
  //   EATER 4 bits
endmodule

module MAYA_IDEA (
  input  in_1,
  input  [3:0] in_2,
  input  [3:0] in_3,
  input  [3:0] in_4,
  input  [3:0] in_5,
  input  [3:0] in_6,
  input  [3:0] in_7,
  input  [3:0] in_8,
  input  [3:0] in_9,
  input  [3:0] in_10,
  input  [3:0] in_11,
  input  [3:0] in_12,
  input  [3:0] in_13,
  input  [3:0] in_14,
  input  [3:0] in_15,
  input  [3:0] in_16,
  input  [3:0] in_17,
  input  [3:0] in_18,
  input  [3:0] in_19,
  input  [3:0] in_20,
  input  [3:0] in_21,
  input  [3:0] in_22,
  input  [3:0] in_23,
  input  in_24,
  input  [6:0] in_25,
  input  [3:0] in_26,
  input  [3:0] in_27,
  input  in_28,
  input  [6:0] in_29,
  input  [6:0] in_30,
  input  [6:0] in_31,
  input  [6:0] in_32,
  input  [6:0] in_33,
  input  [6:0] in_34,
  input  [6:0] in_35,
  input  [6:0] in_36,
  input  [6:0] in_37,
  output [3:0] out_38,
  output [3:0] out_39
);

  wire or_1_out, or_2_out, or_3_out, undriven, undriven_2, undriven_4, undriven_5, undriven_6, undriven_7,
       undriven_8, undriven_9, undriven_10, undriven_11, undriven_12, undriven_13, undriven_15, undriven_16,
       undriven_17, undriven_18;
  wire [2:0] undriven_3, undriven_14;

  LED led_1 (.in(in_5[3]));
  LED led_2 (.in(in_5[3]));
  LED led_3 (.in(in_5[2]));
  LED led_4 (.in(in_5[2]));
  LED led_5 (.in(in_5[2]));
  LED led_6 (.in(in_5[2]));
  LED led_7 (.in(in_5[3]));
  LED led_8 (.in(in_5[3]));
  LED led_9 (.in(in_4[3]));
  LED led_10 (.in(in_4[3]));
  LED led_11 (.in(in_4[2]));
  LED led_12 (.in(in_4[2]));
  LED led_13 (.in(in_4[2]));
  LED led_14 (.in(in_4[2]));
  LED led_15 (.in(in_4[3]));
  LED led_16 (.in(in_4[3]));
  LED led_17 (.in(in_3[3]));
  LED led_18 (.in(in_3[3]));
  LED led_19 (.in(in_3[2]));
  LED led_20 (.in(in_3[2]));
  LED led_21 (.in(in_3[2]));
  LED led_22 (.in(in_3[2]));
  LED led_23 (.in(in_3[3]));
  LED led_24 (.in(in_3[3]));
  LED led_25 (.in(in_2[3]));
  LED led_26 (.in(in_2[3]));
  LED led_27 (.in(in_2[2]));
  LED led_28 (.in(in_2[2]));
  LED led_29 (.in(in_2[2]));
  LED led_30 (.in(in_2[2]));
  LED led_31 (.in(in_2[3]));
  LED led_32 (.in(in_2[3]));
  ROM rom_1 ();  // open: addr, data
  Multiplexer multiplexer_1 ();  // open: in0, in1, out, sel
  LED led_33 (.in(in_5[1]));
  LED led_34 (.in(in_5[1]));
  LED led_35 (.in(in_5[0]));
  LED led_36 (.in(in_5[0]));
  LED led_37 (.in(in_5[1]));
  LED led_38 (.in(in_5[1]));
  LED led_39 (.in(in_5[0]));
  LED led_40 (.in(in_5[0]));
  LED led_41 (.in(in_4[1]));
  LED led_42 (.in(in_4[1]));
  LED led_43 (.in(in_4[0]));
  LED led_44 (.in(in_4[0]));
  LED led_45 (.in(in_4[1]));
  LED led_46 (.in(in_4[1]));
  LED led_47 (.in(in_4[0]));
  LED led_48 (.in(in_4[0]));
  LED led_49 (.in(in_3[1]));
  LED led_50 (.in(in_3[1]));
  LED led_51 (.in(in_3[0]));
  LED led_52 (.in(in_3[0]));
  LED led_53 (.in(in_3[1]));
  LED led_54 (.in(in_3[1]));
  LED led_55 (.in(in_3[0]));
  LED led_56 (.in(in_3[0]));
  LED led_57 (.in(in_2[1]));
  LED led_58 (.in(in_2[1]));
  LED led_59 (.in(in_2[0]));
  LED led_60 (.in(in_2[0]));
  LED led_61 (.in(in_2[1]));
  LED led_62 (.in(in_2[1]));
  LED led_63 (.in(in_2[0]));
  LED led_64 (.in(in_2[0]));
  DotMatrix #(.dotshape("circle"), .matrixcols(7), .matrixrows(4)) dotmatrix_1 (
    .col2(in_26), .col3(in_27));  // open: col0, col1, col4, col5, col6
  LED led_65 (.in(in_5[1]));
  LED led_66 (.in(in_5[1]));
  LED led_67 (.in(in_5[2]));
  LED led_68 (.in(in_5[2]));
  LED led_69 (.in(in_5[1]));
  LED led_70 (.in(in_5[1]));
  LED led_71 (.in(in_5[2]));
  LED led_72 (.in(in_5[2]));
  LED led_73 (.in(in_4[1]));
  LED led_74 (.in(in_4[1]));
  LED led_75 (.in(in_4[2]));
  LED led_76 (.in(in_4[2]));
  LED led_77 (.in(in_4[1]));
  LED led_78 (.in(in_4[1]));
  LED led_79 (.in(in_4[2]));
  LED led_80 (.in(in_4[2]));
  LED led_81 (.in(in_3[1]));
  LED led_82 (.in(in_3[1]));
  LED led_83 (.in(in_3[2]));
  LED led_84 (.in(in_3[2]));
  LED led_85 (.in(in_3[1]));
  LED led_86 (.in(in_3[1]));
  LED led_87 (.in(in_3[2]));
  LED led_88 (.in(in_3[2]));
  LED led_89 (.in(in_2[1]));
  LED led_90 (.in(in_2[1]));
  LED led_91 (.in(in_2[2]));
  LED led_92 (.in(in_2[2]));
  LED led_93 (.in(in_2[1]));
  LED led_94 (.in(in_2[1]));
  LED led_95 (.in(in_2[2]));
  LED led_96 (.in(in_2[2]));
  LED led_97 (.in(in_5[3]));
  LED led_98 (.in(in_5[3]));
  LED led_99 (.in(in_5[3]));
  LED led_100 (.in(in_5[3]));
  LED led_101 (.in(in_4[3]));
  LED led_102 (.in(in_4[3]));
  LED led_103 (.in(in_4[3]));
  LED led_104 (.in(in_4[3]));
  LED led_105 (.in(in_3[3]));
  LED led_106 (.in(in_3[3]));
  LED led_107 (.in(in_3[3]));
  LED led_108 (.in(in_3[3]));
  LED led_109 (.in(in_2[3]));
  LED led_110 (.in(in_2[3]));
  LED led_111 (.in(in_2[3]));
  LED led_112 (.in(in_2[3]));
  assign out_39 = {{3{in_28}}, in_28};  // Bit_Extender bit_extender_1
  LED led_113 (.in(undriven));
  LED led_114 (.in(undriven));
  LED led_115 (.in(undriven));
  LED led_116 (.in(undriven));
  LED led_117 (.in(undriven_2));
  LED led_118 (.in(undriven_2));
  LED led_119 (.in(undriven_2));
  LED led_120 (.in(undriven_2));
  LED led_121 (.in(in_14[3]));
  LED led_122 (.in(in_14[3]));
  LED led_123 (.in(in_15[3]));
  LED led_124 (.in(in_15[3]));
  LED led_125 (.in(in_14[3]));
  LED led_126 (.in(in_14[3]));
  LED led_127 (.in(in_15[3]));
  LED led_128 (.in(in_15[3]));
  LED led_129 (.in(in_14[2]));
  LED led_130 (.in(in_14[2]));
  LED led_131 (.in(in_15[2]));
  LED led_132 (.in(in_15[2]));
  LED led_133 (.in(in_14[2]));
  LED led_134 (.in(in_14[2]));
  LED led_135 (.in(in_15[2]));
  LED led_136 (.in(in_15[2]));
  LED led_137 (.in(in_14[1]));
  LED led_138 (.in(in_14[1]));
  LED led_139 (.in(in_15[1]));
  LED led_140 (.in(in_15[1]));
  LED led_141 (.in(in_14[1]));
  LED led_142 (.in(in_14[1]));
  LED led_143 (.in(in_15[1]));
  LED led_144 (.in(in_15[1]));
  LED led_145 (.in(in_14[0]));
  LED led_146 (.in(in_14[0]));
  LED led_147 (.in(in_15[0]));
  LED led_148 (.in(in_15[0]));
  LED led_149 (.in(in_14[0]));
  LED led_150 (.in(in_14[0]));
  LED led_151 (.in(in_15[0]));
  LED led_152 (.in(in_15[0]));
  LED led_153 (.in(undriven_4));
  LED led_154 (.in(undriven_4));
  LED led_155 (.in(undriven_5));
  LED led_156 (.in(undriven_5));
  LED led_157 (.in(undriven_4));
  LED led_158 (.in(undriven_4));
  LED led_159 (.in(undriven_5));
  LED led_160 (.in(undriven_5));
  LED led_161 (.in(in_1));
  LED led_162 (.in(in_1));
  LED led_163 (.in(undriven_6));
  LED led_164 (.in(undriven_6));
  LED led_165 (.in(in_1));
  LED led_166 (.in(in_1));
  LED led_167 (.in(undriven_6));
  LED led_168 (.in(undriven_6));
  LED led_169 (.in(in_16[3]));
  LED led_170 (.in(in_16[3]));
  LED led_171 (.in(in_17[3]));
  LED led_172 (.in(in_17[3]));
  LED led_173 (.in(in_16[3]));
  LED led_174 (.in(in_16[3]));
  LED led_175 (.in(in_17[3]));
  LED led_176 (.in(in_17[3]));
  LED led_177 (.in(in_16[2]));
  LED led_178 (.in(in_16[2]));
  LED led_179 (.in(in_17[2]));
  LED led_180 (.in(in_17[2]));
  LED led_181 (.in(in_16[2]));
  LED led_182 (.in(in_16[2]));
  LED led_183 (.in(in_17[2]));
  LED led_184 (.in(in_17[2]));
  LED led_185 (.in(in_16[1]));
  LED led_186 (.in(in_16[1]));
  LED led_187 (.in(in_17[1]));
  LED led_188 (.in(in_17[1]));
  LED led_189 (.in(in_16[1]));
  LED led_190 (.in(in_16[1]));
  LED led_191 (.in(in_17[1]));
  LED led_192 (.in(in_17[1]));
  LED led_193 (.in(in_16[0]));
  LED led_194 (.in(in_16[0]));
  LED led_195 (.in(in_17[0]));
  LED led_196 (.in(in_17[0]));
  LED led_197 (.in(in_16[0]));
  LED led_198 (.in(in_16[0]));
  LED led_199 (.in(in_17[0]));
  LED led_200 (.in(in_17[0]));
  LED led_201 (.in(in_25[0]));
  LED led_202 (.in(in_25[0]));
  LED led_203 (.in(in_25[1]));
  LED led_204 (.in(in_25[1]));
  LED led_205 (.in(in_25[0]));
  LED led_206 (.in(in_25[0]));
  LED led_207 (.in(in_25[1]));
  LED led_208 (.in(in_25[1]));
  LED led_209 (.in(in_34[0]));
  LED led_210 (.in(in_34[0]));
  LED led_211 (.in(in_34[1]));
  LED led_212 (.in(in_34[1]));
  LED led_213 (.in(in_34[0]));
  LED led_214 (.in(in_34[0]));
  LED led_215 (.in(in_34[1]));
  LED led_216 (.in(in_34[1]));
  LED led_217 (.in(in_35[0]));
  LED led_218 (.in(in_35[0]));
  LED led_219 (.in(in_35[1]));
  LED led_220 (.in(in_35[1]));
  LED led_221 (.in(in_35[0]));
  LED led_222 (.in(in_35[0]));
  LED led_223 (.in(in_35[1]));
  LED led_224 (.in(in_35[1]));
  LED led_225 (.in(in_36[0]));
  LED led_226 (.in(in_36[0]));
  LED led_227 (.in(in_36[1]));
  LED led_228 (.in(in_36[1]));
  LED led_229 (.in(in_36[0]));
  LED led_230 (.in(in_36[0]));
  LED led_231 (.in(in_36[1]));
  LED led_232 (.in(in_36[1]));
  LED led_233 (.in(in_37[0]));
  LED led_234 (.in(in_37[0]));
  LED led_235 (.in(in_37[1]));
  LED led_236 (.in(in_37[1]));
  LED led_237 (.in(in_37[0]));
  LED led_238 (.in(in_37[0]));
  LED led_239 (.in(in_37[1]));
  LED led_240 (.in(in_37[1]));
  LED led_241 (.in(undriven_3[0]));
  LED led_242 (.in(undriven_3[0]));
  LED led_243 (.in(undriven_3[1]));
  LED led_244 (.in(undriven_3[1]));
  LED led_245 (.in(undriven_3[1]));
  LED led_246 (.in(undriven_3[1]));
  LED led_247 (.in(undriven_3[0]));
  LED led_248 (.in(undriven_3[0]));
  LED led_249 (.in(undriven_8));
  LED led_250 (.in(undriven_8));
  LED led_251 (.in(undriven_7));
  LED led_252 (.in(undriven_7));
  LED led_253 (.in(undriven_8));
  LED led_254 (.in(undriven_8));
  LED led_255 (.in(undriven_7));
  LED led_256 (.in(undriven_7));
  LED led_257 (.in(undriven_6));
  LED led_258 (.in(undriven_6));
  LED led_259 (.in(in_1));
  LED led_260 (.in(in_1));
  LED led_261 (.in(undriven_6));
  LED led_262 (.in(undriven_6));
  LED led_263 (.in(in_1));
  LED led_264 (.in(in_1));
  LED led_265 (.in(in_19[3]));
  LED led_266 (.in(in_19[3]));
  LED led_267 (.in(in_18[3]));
  LED led_268 (.in(in_18[3]));
  LED led_269 (.in(in_19[3]));
  LED led_270 (.in(in_19[3]));
  LED led_271 (.in(in_18[3]));
  LED led_272 (.in(in_18[3]));
  LED led_273 (.in(in_19[2]));
  LED led_274 (.in(in_19[2]));
  LED led_275 (.in(in_18[2]));
  LED led_276 (.in(in_18[2]));
  LED led_277 (.in(in_19[2]));
  LED led_278 (.in(in_19[2]));
  LED led_279 (.in(in_18[2]));
  LED led_280 (.in(in_18[2]));
  LED led_281 (.in(in_19[1]));
  LED led_282 (.in(in_19[1]));
  LED led_283 (.in(in_18[1]));
  LED led_284 (.in(in_18[1]));
  LED led_285 (.in(in_19[1]));
  LED led_286 (.in(in_19[1]));
  LED led_287 (.in(in_18[1]));
  LED led_288 (.in(in_18[1]));
  LED led_289 (.in(in_19[0]));
  LED led_290 (.in(in_19[0]));
  LED led_291 (.in(in_18[0]));
  LED led_292 (.in(in_18[0]));
  LED led_293 (.in(in_19[0]));
  LED led_294 (.in(in_19[0]));
  LED led_295 (.in(in_18[0]));
  LED led_296 (.in(in_18[0]));
  LED led_297 (.in(in_25[3]));
  LED led_298 (.in(in_25[3]));
  LED led_299 (.in(in_25[2]));
  LED led_300 (.in(in_25[2]));
  LED led_301 (.in(in_25[3]));
  LED led_302 (.in(in_25[3]));
  LED led_303 (.in(in_25[2]));
  LED led_304 (.in(in_25[2]));
  LED led_305 (.in(in_34[3]));
  LED led_306 (.in(in_34[3]));
  LED led_307 (.in(in_34[2]));
  LED led_308 (.in(in_34[2]));
  LED led_309 (.in(in_34[3]));
  LED led_310 (.in(in_34[3]));
  LED led_311 (.in(in_34[2]));
  LED led_312 (.in(in_34[2]));
  LED led_313 (.in(in_35[3]));
  LED led_314 (.in(in_35[3]));
  LED led_315 (.in(in_35[2]));
  LED led_316 (.in(in_35[2]));
  LED led_317 (.in(in_35[3]));
  LED led_318 (.in(in_35[3]));
  LED led_319 (.in(in_35[2]));
  LED led_320 (.in(in_35[2]));
  LED led_321 (.in(in_36[3]));
  LED led_322 (.in(in_36[3]));
  LED led_323 (.in(in_36[2]));
  LED led_324 (.in(in_36[2]));
  LED led_325 (.in(in_36[3]));
  LED led_326 (.in(in_36[3]));
  LED led_327 (.in(in_36[2]));
  LED led_328 (.in(in_36[2]));
  LED led_329 (.in(in_37[3]));
  LED led_330 (.in(in_37[3]));
  LED led_331 (.in(in_37[2]));
  LED led_332 (.in(in_37[2]));
  LED led_333 (.in(in_37[3]));
  LED led_334 (.in(in_37[3]));
  LED led_335 (.in(in_37[2]));
  LED led_336 (.in(in_37[2]));
  LED led_337 (.in(undriven_9));
  LED led_338 (.in(undriven_9));
  LED led_339 (.in(undriven_3[2]));
  LED led_340 (.in(undriven_3[2]));
  LED led_341 (.in(undriven_9));
  LED led_342 (.in(undriven_9));
  LED led_343 (.in(undriven_3[2]));
  LED led_344 (.in(undriven_3[2]));
  LED led_345 (.in(undriven_10));
  LED led_346 (.in(undriven_10));
  LED led_347 (.in(undriven_12));
  LED led_348 (.in(undriven_12));
  LED led_349 (.in(undriven_10));
  LED led_350 (.in(undriven_10));
  LED led_351 (.in(undriven_12));
  LED led_352 (.in(undriven_12));
  LED led_353 (.in(undriven_11));
  LED led_354 (.in(undriven_11));
  LED led_355 (.in(undriven_13));
  LED led_356 (.in(undriven_13));
  LED led_357 (.in(undriven_11));
  LED led_358 (.in(undriven_11));
  LED led_359 (.in(undriven_13));
  LED led_360 (.in(undriven_13));
  LED led_361 (.in(in_20[3]));
  LED led_362 (.in(in_20[3]));
  LED led_363 (.in(in_20[3]));
  LED led_364 (.in(in_20[3]));
  LED led_365 (.in(in_20[2]));
  LED led_366 (.in(in_20[2]));
  LED led_367 (.in(in_20[2]));
  LED led_368 (.in(in_20[2]));
  LED led_369 (.in(in_20[1]));
  LED led_370 (.in(in_20[1]));
  LED led_371 (.in(in_20[1]));
  LED led_372 (.in(in_20[1]));
  LED led_373 (.in(in_20[0]));
  LED led_374 (.in(in_20[0]));
  LED led_375 (.in(in_20[0]));
  LED led_376 (.in(in_20[0]));
  LED led_377 (.in(in_25[4]));
  LED led_378 (.in(in_25[4]));
  LED led_379 (.in(in_25[5]));
  LED led_380 (.in(in_25[5]));
  LED led_381 (.in(in_25[4]));
  LED led_382 (.in(in_25[4]));
  LED led_383 (.in(in_25[5]));
  LED led_384 (.in(in_25[5]));
  LED led_385 (.in(in_34[4]));
  LED led_386 (.in(in_34[4]));
  LED led_387 (.in(in_34[5]));
  LED led_388 (.in(in_34[5]));
  LED led_389 (.in(in_34[4]));
  LED led_390 (.in(in_34[4]));
  LED led_391 (.in(in_34[5]));
  LED led_392 (.in(in_34[5]));
  LED led_393 (.in(in_35[4]));
  LED led_394 (.in(in_35[4]));
  LED led_395 (.in(in_35[5]));
  LED led_396 (.in(in_35[5]));
  LED led_397 (.in(in_35[4]));
  LED led_398 (.in(in_35[4]));
  LED led_399 (.in(in_35[5]));
  LED led_400 (.in(in_35[5]));
  LED led_401 (.in(in_36[4]));
  LED led_402 (.in(in_36[4]));
  LED led_403 (.in(in_36[5]));
  LED led_404 (.in(in_36[5]));
  LED led_405 (.in(in_36[4]));
  LED led_406 (.in(in_36[4]));
  LED led_407 (.in(in_36[5]));
  LED led_408 (.in(in_36[5]));
  LED led_409 (.in(in_37[4]));
  LED led_410 (.in(in_37[4]));
  LED led_411 (.in(in_37[5]));
  LED led_412 (.in(in_37[5]));
  LED led_413 (.in(in_37[4]));
  LED led_414 (.in(in_37[4]));
  LED led_415 (.in(in_37[5]));
  LED led_416 (.in(in_37[5]));
  LED led_417 (.in(undriven_14[0]));
  LED led_418 (.in(undriven_14[0]));
  LED led_419 (.in(undriven_14[1]));
  LED led_420 (.in(undriven_14[1]));
  LED led_421 (.in(undriven_14[0]));
  LED led_422 (.in(undriven_14[0]));
  LED led_423 (.in(undriven_14[1]));
  LED led_424 (.in(undriven_14[1]));
  LED led_425 (.in(in_6[3]));
  LED led_426 (.in(in_6[3]));
  LED led_427 (.in(in_6[3]));
  LED led_428 (.in(in_6[3]));
  LED led_429 (.in(in_6[2]));
  LED led_430 (.in(in_6[2]));
  LED led_431 (.in(in_6[2]));
  LED led_432 (.in(in_6[2]));
  LED led_433 (.in(in_6[1]));
  LED led_434 (.in(in_6[1]));
  LED led_435 (.in(in_6[1]));
  LED led_436 (.in(in_6[1]));
  LED led_437 (.in(in_6[0]));
  LED led_438 (.in(in_6[0]));
  LED led_439 (.in(in_6[0]));
  LED led_440 (.in(in_6[0]));
  LED led_441 (.in(in_25[6]));
  LED led_442 (.in(in_25[6]));
  LED led_443 (.in(in_25[6]));
  LED led_444 (.in(in_25[6]));
  LED led_445 (.in(in_34[6]));
  LED led_446 (.in(in_34[6]));
  LED led_447 (.in(in_34[6]));
  LED led_448 (.in(in_34[6]));
  LED led_449 (.in(in_35[6]));
  LED led_450 (.in(in_35[6]));
  LED led_451 (.in(in_35[6]));
  LED led_452 (.in(in_35[6]));
  LED led_453 (.in(in_36[6]));
  LED led_454 (.in(in_36[6]));
  LED led_455 (.in(in_36[6]));
  LED led_456 (.in(in_36[6]));
  LED led_457 (.in(in_37[6]));
  LED led_458 (.in(in_37[6]));
  LED led_459 (.in(in_37[6]));
  LED led_460 (.in(in_37[6]));
  LED led_461 (.in(undriven_14[2]));
  LED led_462 (.in(undriven_14[2]));
  LED led_463 (.in(undriven_14[2]));
  LED led_464 (.in(undriven_14[2]));
  LED led_465 (.in(in_7[3]));
  LED led_466 (.in(in_7[3]));
  LED led_467 (.in(in_8[3]));
  LED led_468 (.in(in_8[3]));
  LED led_469 (.in(in_7[3]));
  LED led_470 (.in(in_7[3]));
  LED led_471 (.in(in_8[3]));
  LED led_472 (.in(in_8[3]));
  LED led_473 (.in(in_7[2]));
  LED led_474 (.in(in_7[2]));
  LED led_475 (.in(in_8[2]));
  LED led_476 (.in(in_8[2]));
  LED led_477 (.in(in_7[2]));
  LED led_478 (.in(in_7[2]));
  LED led_479 (.in(in_8[2]));
  LED led_480 (.in(in_8[2]));
  LED led_481 (.in(in_7[1]));
  LED led_482 (.in(in_7[1]));
  LED led_483 (.in(in_8[1]));
  LED led_484 (.in(in_8[1]));
  LED led_485 (.in(in_7[1]));
  LED led_486 (.in(in_7[1]));
  LED led_487 (.in(in_8[1]));
  LED led_488 (.in(in_8[1]));
  LED led_489 (.in(in_7[0]));
  LED led_490 (.in(in_7[0]));
  LED led_491 (.in(in_8[0]));
  LED led_492 (.in(in_8[0]));
  LED led_493 (.in(in_7[0]));
  LED led_494 (.in(in_7[0]));
  LED led_495 (.in(in_8[0]));
  LED led_496 (.in(in_8[0]));
  LED led_497 (.in(in_9[3]));
  LED led_498 (.in(in_9[3]));
  LED led_499 (.in(in_10[3]));
  LED led_500 (.in(in_10[3]));
  LED led_501 (.in(in_9[3]));
  LED led_502 (.in(in_9[3]));
  LED led_503 (.in(in_10[3]));
  LED led_504 (.in(in_10[3]));
  LED led_505 (.in(in_9[2]));
  LED led_506 (.in(in_9[2]));
  LED led_507 (.in(in_10[2]));
  LED led_508 (.in(in_10[2]));
  LED led_509 (.in(in_9[2]));
  LED led_510 (.in(in_9[2]));
  LED led_511 (.in(in_10[2]));
  LED led_512 (.in(in_10[2]));
  LED led_513 (.in(in_9[1]));
  LED led_514 (.in(in_9[1]));
  LED led_515 (.in(in_10[1]));
  LED led_516 (.in(in_10[1]));
  LED led_517 (.in(in_9[1]));
  LED led_518 (.in(in_9[1]));
  LED led_519 (.in(in_10[1]));
  LED led_520 (.in(in_10[1]));
  LED led_521 (.in(in_9[0]));
  LED led_522 (.in(in_9[0]));
  LED led_523 (.in(in_10[0]));
  LED led_524 (.in(in_10[0]));
  LED led_525 (.in(in_9[0]));
  LED led_526 (.in(in_9[0]));
  LED led_527 (.in(in_10[0]));
  LED led_528 (.in(in_10[0]));
  LED led_529 (.in(in_11[3]));
  LED led_530 (.in(in_11[3]));
  LED led_531 (.in(in_12[3]));
  LED led_532 (.in(in_12[3]));
  LED led_533 (.in(in_11[3]));
  LED led_534 (.in(in_11[3]));
  LED led_535 (.in(in_12[3]));
  LED led_536 (.in(in_12[3]));
  LED led_537 (.in(in_11[2]));
  LED led_538 (.in(in_11[2]));
  LED led_539 (.in(in_12[2]));
  LED led_540 (.in(in_12[2]));
  LED led_541 (.in(in_11[2]));
  LED led_542 (.in(in_11[2]));
  LED led_543 (.in(in_12[2]));
  LED led_544 (.in(in_12[2]));
  LED led_545 (.in(in_11[1]));
  LED led_546 (.in(in_11[1]));
  LED led_547 (.in(in_12[1]));
  LED led_548 (.in(in_12[1]));
  LED led_549 (.in(in_11[1]));
  LED led_550 (.in(in_11[1]));
  LED led_551 (.in(in_12[1]));
  LED led_552 (.in(in_12[1]));
  LED led_553 (.in(in_11[0]));
  LED led_554 (.in(in_11[0]));
  LED led_555 (.in(in_12[0]));
  LED led_556 (.in(in_12[0]));
  LED led_557 (.in(in_11[0]));
  LED led_558 (.in(in_11[0]));
  LED led_559 (.in(in_12[0]));
  LED led_560 (.in(in_12[0]));
  LED led_561 (.in(in_33[0]));
  LED led_562 (.in(in_33[0]));
  LED led_563 (.in(in_33[0]));
  LED led_564 (.in(in_33[0]));
  LED led_565 (.in(in_32[0]));
  LED led_566 (.in(in_32[0]));
  LED led_567 (.in(in_32[0]));
  LED led_568 (.in(in_32[0]));
  LED led_569 (.in(in_31[0]));
  LED led_570 (.in(in_31[0]));
  LED led_571 (.in(in_31[0]));
  LED led_572 (.in(in_31[0]));
  LED led_573 (.in(in_30[0]));
  LED led_574 (.in(in_30[0]));
  LED led_575 (.in(in_30[0]));
  LED led_576 (.in(in_30[0]));
  LED led_577 (.in(in_33[1]));
  LED led_578 (.in(in_33[1]));
  LED led_579 (.in(in_33[2]));
  LED led_580 (.in(in_33[2]));
  LED led_581 (.in(in_33[1]));
  LED led_582 (.in(in_33[1]));
  LED led_583 (.in(in_33[2]));
  LED led_584 (.in(in_33[2]));
  LED led_585 (.in(in_32[1]));
  LED led_586 (.in(in_32[1]));
  LED led_587 (.in(in_32[2]));
  LED led_588 (.in(in_32[2]));
  LED led_589 (.in(in_32[1]));
  LED led_590 (.in(in_32[1]));
  LED led_591 (.in(in_32[2]));
  LED led_592 (.in(in_32[2]));
  LED led_593 (.in(in_31[1]));
  LED led_594 (.in(in_31[1]));
  LED led_595 (.in(in_31[2]));
  LED led_596 (.in(in_31[2]));
  LED led_597 (.in(in_31[1]));
  LED led_598 (.in(in_31[1]));
  LED led_599 (.in(in_31[2]));
  LED led_600 (.in(in_31[2]));
  LED led_601 (.in(in_30[1]));
  LED led_602 (.in(in_30[1]));
  LED led_603 (.in(in_30[2]));
  LED led_604 (.in(in_30[2]));
  LED led_605 (.in(in_30[1]));
  LED led_606 (.in(in_30[1]));
  LED led_607 (.in(in_30[2]));
  LED led_608 (.in(in_30[2]));
  LED led_609 (.in(in_33[3]));
  LED led_610 (.in(in_33[3]));
  LED led_611 (.in(in_33[4]));
  LED led_612 (.in(in_33[4]));
  LED led_613 (.in(in_33[3]));
  LED led_614 (.in(in_33[3]));
  LED led_615 (.in(in_33[4]));
  LED led_616 (.in(in_33[4]));
  LED led_617 (.in(in_32[3]));
  LED led_618 (.in(in_32[3]));
  LED led_619 (.in(in_32[4]));
  LED led_620 (.in(in_32[4]));
  LED led_621 (.in(in_32[3]));
  LED led_622 (.in(in_32[3]));
  LED led_623 (.in(in_32[4]));
  LED led_624 (.in(in_32[4]));
  LED led_625 (.in(in_31[3]));
  LED led_626 (.in(in_31[3]));
  LED led_627 (.in(in_31[4]));
  LED led_628 (.in(in_31[4]));
  LED led_629 (.in(in_31[3]));
  LED led_630 (.in(in_31[3]));
  LED led_631 (.in(in_31[4]));
  LED led_632 (.in(in_31[4]));
  LED led_633 (.in(in_30[3]));
  LED led_634 (.in(in_30[3]));
  LED led_635 (.in(in_30[4]));
  LED led_636 (.in(in_30[4]));
  LED led_637 (.in(in_30[3]));
  LED led_638 (.in(in_30[3]));
  LED led_639 (.in(in_30[4]));
  LED led_640 (.in(in_30[4]));
  LED led_641 (.in(in_33[5]));
  LED led_642 (.in(in_33[5]));
  LED led_643 (.in(in_33[6]));
  LED led_644 (.in(in_33[6]));
  LED led_645 (.in(in_33[5]));
  LED led_646 (.in(in_33[5]));
  LED led_647 (.in(in_33[6]));
  LED led_648 (.in(in_33[6]));
  LED led_649 (.in(in_32[5]));
  LED led_650 (.in(in_32[5]));
  LED led_651 (.in(in_32[6]));
  LED led_652 (.in(in_32[6]));
  LED led_653 (.in(in_32[5]));
  LED led_654 (.in(in_32[5]));
  LED led_655 (.in(in_32[6]));
  LED led_656 (.in(in_32[6]));
  LED led_657 (.in(in_31[5]));
  LED led_658 (.in(in_31[5]));
  LED led_659 (.in(in_31[6]));
  LED led_660 (.in(in_31[6]));
  LED led_661 (.in(in_31[5]));
  LED led_662 (.in(in_31[5]));
  LED led_663 (.in(in_31[6]));
  LED led_664 (.in(in_31[6]));
  LED led_665 (.in(in_30[5]));
  LED led_666 (.in(in_30[5]));
  LED led_667 (.in(in_30[6]));
  LED led_668 (.in(in_30[6]));
  LED led_669 (.in(in_30[5]));
  LED led_670 (.in(in_30[5]));
  LED led_671 (.in(in_30[6]));
  LED led_672 (.in(in_30[6]));
  LED led_673 (.in(undriven_18));
  LED led_674 (.in(undriven_18));
  LED led_675 (.in(undriven_18));
  LED led_676 (.in(undriven_18));
  LED led_677 (.in(undriven_17));
  LED led_678 (.in(undriven_17));
  LED led_679 (.in(or_1_out));
  LED led_680 (.in(or_1_out));
  LED led_681 (.in(undriven_17));
  LED led_682 (.in(undriven_17));
  LED led_683 (.in(or_1_out));
  LED led_684 (.in(or_1_out));
  or or_1 (or_1_out, undriven_16, undriven_18);
  LED led_685 (.in(or_2_out));
  LED led_686 (.in(or_2_out));
  LED led_687 (.in(or_3_out));
  LED led_688 (.in(or_3_out));
  LED led_689 (.in(or_2_out));
  LED led_690 (.in(or_2_out));
  LED led_691 (.in(or_3_out));
  LED led_692 (.in(or_3_out));
  or or_2 (or_2_out, undriven_15, undriven_17);
  or or_3 (or_3_out, undriven_16, undriven_18);
  LED led_693 (.in(undriven_17));
  LED led_694 (.in(undriven_17));
  LED led_695 (.in(undriven_18));
  LED led_696 (.in(undriven_18));
  LED led_697 (.in(undriven_17));
  LED led_698 (.in(undriven_17));
  LED led_699 (.in(undriven_18));
  LED led_700 (.in(undriven_18));

  assign out_38 = {4{in_24}};
endmodule

module LEDS (
  input  [4:0] n,
  input  [4:0] in_2,
  input  [3:0] in_3,
  input  [3:0] in_4,
  input  [4:0] in_5
);

  wire or_1_out, or_2_out, or_3_out, or_4_out, or_7_out, or_8_out, undriven_6, undriven_7, undriven_8,
       undriven_9, undriven_10, undriven_11, undriven_12, undriven_13, undriven_14, undriven_15, undriven_16,
       undriven_17, undriven_18, undriven_19;
  wire [3:0] creator_6_1_f0, creator_6_1_f1, creator_6_1_f2, creator_6_1_f3, creator_6_2_f0, creator_6_2_f1,
       creator_6_2_f2, creator_6_2_f3, undriven, undriven_2, undriven_3, undriven_4, undriven_5;
  wire [15:0] eater_rom_1_p2;

  CREATOR_6 creator_6_1 (.x(n), .F3(creator_6_1_f3), .F2(creator_6_1_f2), .F0(creator_6_1_f0), .F1(creator_6_1_f1));
  LED led_1 (.in(creator_6_1_f3[3]));
  LED led_2 (.in(creator_6_1_f2[3]));
  LED led_3 (.in(creator_6_1_f1[3]));
  LED led_4 (.in(creator_6_1_f0[3]));
  LED led_5 (.in(undriven[3]));
  LED led_6 (.in(in_3[3]));
  LED led_7 (.in(in_4[3]));
  LED led_8 (.in(in_3[3]));
  LED led_9 (.in(creator_6_1_f3[3]));
  LED led_10 (.in(creator_6_1_f3[3]));
  LED led_11 (.in(creator_6_1_f3[2]));
  LED led_12 (.in(creator_6_1_f3[2]));
  LED led_13 (.in(creator_6_1_f3[2]));
  LED led_14 (.in(creator_6_1_f3[2]));
  LED led_15 (.in(creator_6_1_f3[3]));
  LED led_16 (.in(creator_6_1_f2[3]));
  LED led_17 (.in(creator_6_1_f2[3]));
  LED led_18 (.in(creator_6_1_f2[2]));
  LED led_19 (.in(creator_6_1_f2[2]));
  LED led_20 (.in(creator_6_1_f2[2]));
  LED led_21 (.in(creator_6_1_f2[2]));
  LED led_22 (.in(creator_6_1_f2[3]));
  LED led_23 (.in(creator_6_1_f1[3]));
  LED led_24 (.in(creator_6_1_f1[3]));
  LED led_25 (.in(creator_6_1_f1[2]));
  LED led_26 (.in(creator_6_1_f1[2]));
  LED led_27 (.in(creator_6_1_f1[2]));
  LED led_28 (.in(creator_6_1_f1[2]));
  LED led_29 (.in(creator_6_1_f1[3]));
  LED led_30 (.in(creator_6_1_f0[3]));
  LED led_31 (.in(creator_6_1_f0[3]));
  LED led_32 (.in(creator_6_1_f0[2]));
  LED led_33 (.in(creator_6_1_f0[2]));
  LED led_34 (.in(creator_6_1_f0[2]));
  LED led_35 (.in(creator_6_1_f0[2]));
  LED led_36 (.in(creator_6_1_f0[3]));
  LED led_37 (.in(undriven[3]));
  LED led_38 (.in(undriven[3]));
  LED led_39 (.in(undriven[2]));
  LED led_40 (.in(undriven[2]));
  LED led_41 (.in(undriven[2]));
  LED led_42 (.in(undriven[2]));
  LED led_43 (.in(undriven[3]));
  LED led_44 (.in(in_3[3]));
  LED led_45 (.in(in_3[3]));
  LED led_46 (.in(in_3[2]));
  LED led_47 (.in(in_3[2]));
  LED led_48 (.in(in_3[2]));
  LED led_49 (.in(in_3[2]));
  LED led_50 (.in(in_3[3]));
  LED led_51 (.in(in_4[3]));
  LED led_52 (.in(in_4[3]));
  LED led_53 (.in(in_4[2]));
  LED led_54 (.in(in_4[2]));
  LED led_55 (.in(in_4[2]));
  LED led_56 (.in(in_4[2]));
  LED led_57 (.in(in_4[3]));
  LED led_58 (.in(in_3[3]));
  LED led_59 (.in(in_3[3]));
  LED led_60 (.in(in_3[2]));
  LED led_61 (.in(in_3[2]));
  LED led_62 (.in(in_3[2]));
  LED led_63 (.in(in_3[2]));
  LED led_64 (.in(in_3[3]));
  LED led_65 (.in(creator_6_1_f3[1]));
  LED led_66 (.in(creator_6_1_f3[1]));
  LED led_67 (.in(creator_6_1_f3[0]));
  LED led_68 (.in(creator_6_1_f3[0]));
  LED led_69 (.in(creator_6_1_f3[1]));
  LED led_70 (.in(creator_6_1_f3[1]));
  LED led_71 (.in(creator_6_1_f3[0]));
  LED led_72 (.in(creator_6_1_f3[0]));
  LED led_73 (.in(creator_6_1_f2[1]));
  LED led_74 (.in(creator_6_1_f2[1]));
  LED led_75 (.in(creator_6_1_f2[0]));
  LED led_76 (.in(creator_6_1_f2[0]));
  LED led_77 (.in(creator_6_1_f2[1]));
  LED led_78 (.in(creator_6_1_f2[1]));
  LED led_79 (.in(creator_6_1_f2[0]));
  LED led_80 (.in(creator_6_1_f2[0]));
  LED led_81 (.in(creator_6_1_f1[1]));
  LED led_82 (.in(creator_6_1_f1[1]));
  LED led_83 (.in(creator_6_1_f1[0]));
  LED led_84 (.in(creator_6_1_f1[0]));
  LED led_85 (.in(creator_6_1_f1[1]));
  LED led_86 (.in(creator_6_1_f1[1]));
  LED led_87 (.in(creator_6_1_f1[0]));
  LED led_88 (.in(creator_6_1_f1[0]));
  LED led_89 (.in(creator_6_1_f0[1]));
  LED led_90 (.in(creator_6_1_f0[1]));
  LED led_91 (.in(creator_6_1_f0[0]));
  LED led_92 (.in(creator_6_1_f0[0]));
  LED led_93 (.in(creator_6_1_f0[1]));
  LED led_94 (.in(creator_6_1_f0[1]));
  LED led_95 (.in(creator_6_1_f0[0]));
  LED led_96 (.in(creator_6_1_f0[0]));
  LED led_97 (.in(undriven[1]));
  LED led_98 (.in(undriven[1]));
  LED led_99 (.in(undriven[0]));
  LED led_100 (.in(undriven[0]));
  LED led_101 (.in(undriven[1]));
  LED led_102 (.in(undriven[1]));
  LED led_103 (.in(undriven[0]));
  LED led_104 (.in(undriven[0]));
  LED led_105 (.in(in_3[1]));
  LED led_106 (.in(in_3[1]));
  LED led_107 (.in(in_3[0]));
  LED led_108 (.in(in_3[0]));
  LED led_109 (.in(in_3[1]));
  LED led_110 (.in(in_3[1]));
  LED led_111 (.in(in_3[0]));
  LED led_112 (.in(in_3[0]));
  LED led_113 (.in(in_4[1]));
  LED led_114 (.in(in_4[1]));
  LED led_115 (.in(in_4[0]));
  LED led_116 (.in(in_4[0]));
  LED led_117 (.in(in_4[1]));
  LED led_118 (.in(in_4[1]));
  LED led_119 (.in(in_4[0]));
  LED led_120 (.in(in_4[0]));
  LED led_121 (.in(in_3[1]));
  LED led_122 (.in(in_3[1]));
  LED led_123 (.in(in_3[0]));
  LED led_124 (.in(in_3[0]));
  LED led_125 (.in(in_3[1]));
  LED led_126 (.in(in_3[1]));
  LED led_127 (.in(in_3[0]));
  LED led_128 (.in(in_3[0]));
  // EATER_ROM eater_rom_1: pin names not known; wires that end beside it: in_5, eater_rom_1_p2
  LED led_129 (.in(creator_6_1_f3[1]));
  LED led_130 (.in(creator_6_1_f3[1]));
  LED led_131 (.in(creator_6_1_f3[2]));
  LED led_132 (.in(creator_6_1_f3[2]));
  LED led_133 (.in(creator_6_1_f3[1]));
  LED led_134 (.in(creator_6_1_f3[1]));
  LED led_135 (.in(creator_6_1_f3[2]));
  LED led_136 (.in(creator_6_1_f3[2]));
  LED led_137 (.in(creator_6_1_f3[3]));
  LED led_138 (.in(creator_6_1_f2[1]));
  LED led_139 (.in(creator_6_1_f2[1]));
  LED led_140 (.in(creator_6_1_f2[2]));
  LED led_141 (.in(creator_6_1_f2[2]));
  LED led_142 (.in(creator_6_1_f2[1]));
  LED led_143 (.in(creator_6_1_f2[1]));
  LED led_144 (.in(creator_6_1_f2[2]));
  LED led_145 (.in(creator_6_1_f2[2]));
  LED led_146 (.in(creator_6_1_f2[3]));
  LED led_147 (.in(creator_6_1_f1[1]));
  LED led_148 (.in(creator_6_1_f1[1]));
  LED led_149 (.in(creator_6_1_f1[2]));
  LED led_150 (.in(creator_6_1_f1[2]));
  LED led_151 (.in(creator_6_1_f1[1]));
  LED led_152 (.in(creator_6_1_f1[1]));
  LED led_153 (.in(creator_6_1_f1[2]));
  LED led_154 (.in(creator_6_1_f1[2]));
  LED led_155 (.in(creator_6_1_f1[3]));
  LED led_156 (.in(creator_6_1_f0[1]));
  LED led_157 (.in(creator_6_1_f0[1]));
  LED led_158 (.in(creator_6_1_f0[2]));
  LED led_159 (.in(creator_6_1_f0[2]));
  LED led_160 (.in(creator_6_1_f0[1]));
  LED led_161 (.in(creator_6_1_f0[1]));
  LED led_162 (.in(creator_6_1_f0[2]));
  LED led_163 (.in(creator_6_1_f0[2]));
  LED led_164 (.in(creator_6_1_f0[3]));
  LED led_165 (.in(undriven[1]));
  LED led_166 (.in(undriven[1]));
  LED led_167 (.in(undriven[2]));
  LED led_168 (.in(undriven[2]));
  LED led_169 (.in(undriven[1]));
  LED led_170 (.in(undriven[1]));
  LED led_171 (.in(undriven[2]));
  LED led_172 (.in(undriven[2]));
  LED led_173 (.in(undriven[3]));
  LED led_174 (.in(in_3[1]));
  LED led_175 (.in(in_3[1]));
  LED led_176 (.in(in_3[2]));
  LED led_177 (.in(in_3[2]));
  LED led_178 (.in(in_3[1]));
  LED led_179 (.in(in_3[1]));
  LED led_180 (.in(in_3[2]));
  LED led_181 (.in(in_3[2]));
  LED led_182 (.in(in_3[3]));
  LED led_183 (.in(in_4[1]));
  LED led_184 (.in(in_4[1]));
  LED led_185 (.in(in_4[2]));
  LED led_186 (.in(in_4[2]));
  LED led_187 (.in(in_4[1]));
  LED led_188 (.in(in_4[1]));
  LED led_189 (.in(in_4[2]));
  LED led_190 (.in(in_4[2]));
  LED led_191 (.in(in_4[3]));
  LED led_192 (.in(in_3[1]));
  LED led_193 (.in(in_3[1]));
  LED led_194 (.in(in_3[2]));
  LED led_195 (.in(in_3[2]));
  LED led_196 (.in(in_3[1]));
  LED led_197 (.in(in_3[1]));
  LED led_198 (.in(in_3[2]));
  LED led_199 (.in(in_3[2]));
  LED led_200 (.in(in_3[3]));
  LED led_201 (.in(creator_6_1_f3[3]));
  LED led_202 (.in(creator_6_1_f3[3]));
  LED led_203 (.in(creator_6_1_f3[3]));
  LED led_204 (.in(creator_6_1_f2[3]));
  LED led_205 (.in(creator_6_1_f2[3]));
  LED led_206 (.in(creator_6_1_f2[3]));
  LED led_207 (.in(creator_6_1_f1[3]));
  LED led_208 (.in(creator_6_1_f1[3]));
  LED led_209 (.in(creator_6_1_f1[3]));
  LED led_210 (.in(creator_6_1_f0[3]));
  LED led_211 (.in(creator_6_1_f0[3]));
  LED led_212 (.in(creator_6_1_f0[3]));
  LED led_213 (.in(undriven[3]));
  LED led_214 (.in(undriven[3]));
  LED led_215 (.in(undriven[3]));
  LED led_216 (.in(in_3[3]));
  LED led_217 (.in(in_3[3]));
  LED led_218 (.in(in_3[3]));
  LED led_219 (.in(in_4[3]));
  LED led_220 (.in(in_4[3]));
  LED led_221 (.in(in_4[3]));
  LED led_222 (.in(in_3[3]));
  LED led_223 (.in(in_3[3]));
  LED led_224 (.in(in_3[3]));
  LED led_225 (.in(eater_rom_1_p2[15]));
  LED led_226 (.in(eater_rom_1_p2[15]));
  LED led_227 (.in(eater_rom_1_p2[14]));
  LED led_228 (.in(eater_rom_1_p2[14]));
  LED led_229 (.in(eater_rom_1_p2[14]));
  LED led_230 (.in(eater_rom_1_p2[14]));
  LED led_231 (.in(eater_rom_1_p2[15]));
  LED led_232 (.in(eater_rom_1_p2[15]));
  LED led_233 (.in(eater_rom_1_p2[11]));
  LED led_234 (.in(eater_rom_1_p2[11]));
  LED led_235 (.in(eater_rom_1_p2[10]));
  LED led_236 (.in(eater_rom_1_p2[10]));
  LED led_237 (.in(eater_rom_1_p2[10]));
  LED led_238 (.in(eater_rom_1_p2[10]));
  LED led_239 (.in(eater_rom_1_p2[11]));
  LED led_240 (.in(eater_rom_1_p2[11]));
  LED led_241 (.in(eater_rom_1_p2[7]));
  LED led_242 (.in(eater_rom_1_p2[7]));
  LED led_243 (.in(eater_rom_1_p2[6]));
  LED led_244 (.in(eater_rom_1_p2[6]));
  LED led_245 (.in(eater_rom_1_p2[6]));
  LED led_246 (.in(eater_rom_1_p2[6]));
  LED led_247 (.in(eater_rom_1_p2[7]));
  LED led_248 (.in(eater_rom_1_p2[7]));
  LED led_249 (.in(eater_rom_1_p2[3]));
  LED led_250 (.in(eater_rom_1_p2[3]));
  LED led_251 (.in(eater_rom_1_p2[2]));
  LED led_252 (.in(eater_rom_1_p2[2]));
  LED led_253 (.in(eater_rom_1_p2[2]));
  LED led_254 (.in(eater_rom_1_p2[2]));
  LED led_255 (.in(eater_rom_1_p2[3]));
  LED led_256 (.in(eater_rom_1_p2[3]));
  LED led_257 (.in(eater_rom_1_p2[13]));
  LED led_258 (.in(eater_rom_1_p2[13]));
  LED led_259 (.in(eater_rom_1_p2[12]));
  LED led_260 (.in(eater_rom_1_p2[12]));
  LED led_261 (.in(eater_rom_1_p2[13]));
  LED led_262 (.in(eater_rom_1_p2[13]));
  LED led_263 (.in(eater_rom_1_p2[12]));
  LED led_264 (.in(eater_rom_1_p2[12]));
  LED led_265 (.in(eater_rom_1_p2[9]));
  LED led_266 (.in(eater_rom_1_p2[9]));
  LED led_267 (.in(eater_rom_1_p2[8]));
  LED led_268 (.in(eater_rom_1_p2[8]));
  LED led_269 (.in(eater_rom_1_p2[9]));
  LED led_270 (.in(eater_rom_1_p2[9]));
  LED led_271 (.in(eater_rom_1_p2[8]));
  LED led_272 (.in(eater_rom_1_p2[8]));
  LED led_273 (.in(eater_rom_1_p2[5]));
  LED led_274 (.in(eater_rom_1_p2[5]));
  LED led_275 (.in(eater_rom_1_p2[4]));
  LED led_276 (.in(eater_rom_1_p2[4]));
  LED led_277 (.in(eater_rom_1_p2[5]));
  LED led_278 (.in(eater_rom_1_p2[5]));
  LED led_279 (.in(eater_rom_1_p2[4]));
  LED led_280 (.in(eater_rom_1_p2[4]));
  LED led_281 (.in(eater_rom_1_p2[1]));
  LED led_282 (.in(eater_rom_1_p2[1]));
  LED led_283 (.in(eater_rom_1_p2[0]));
  LED led_284 (.in(eater_rom_1_p2[0]));
  LED led_285 (.in(eater_rom_1_p2[1]));
  LED led_286 (.in(eater_rom_1_p2[1]));
  LED led_287 (.in(eater_rom_1_p2[0]));
  LED led_288 (.in(eater_rom_1_p2[0]));
  CREATOR_6 creator_6_2 (.x(in_2), .F3(creator_6_2_f3), .F2(creator_6_2_f2), .F0(creator_6_2_f0), .F1(creator_6_2_f1));
  LED led_289 (.in(eater_rom_1_p2[13]));
  LED led_290 (.in(eater_rom_1_p2[13]));
  LED led_291 (.in(eater_rom_1_p2[14]));
  LED led_292 (.in(eater_rom_1_p2[14]));
  LED led_293 (.in(eater_rom_1_p2[13]));
  LED led_294 (.in(eater_rom_1_p2[13]));
  LED led_295 (.in(eater_rom_1_p2[14]));
  LED led_296 (.in(eater_rom_1_p2[14]));
  LED led_297 (.in(eater_rom_1_p2[9]));
  LED led_298 (.in(eater_rom_1_p2[9]));
  LED led_299 (.in(eater_rom_1_p2[10]));
  LED led_300 (.in(eater_rom_1_p2[10]));
  LED led_301 (.in(eater_rom_1_p2[9]));
  LED led_302 (.in(eater_rom_1_p2[9]));
  LED led_303 (.in(eater_rom_1_p2[10]));
  LED led_304 (.in(eater_rom_1_p2[10]));
  LED led_305 (.in(eater_rom_1_p2[5]));
  LED led_306 (.in(eater_rom_1_p2[5]));
  LED led_307 (.in(eater_rom_1_p2[6]));
  LED led_308 (.in(eater_rom_1_p2[6]));
  LED led_309 (.in(eater_rom_1_p2[5]));
  LED led_310 (.in(eater_rom_1_p2[5]));
  LED led_311 (.in(eater_rom_1_p2[6]));
  LED led_312 (.in(eater_rom_1_p2[6]));
  LED led_313 (.in(eater_rom_1_p2[1]));
  LED led_314 (.in(eater_rom_1_p2[1]));
  LED led_315 (.in(eater_rom_1_p2[2]));
  LED led_316 (.in(eater_rom_1_p2[2]));
  LED led_317 (.in(eater_rom_1_p2[1]));
  LED led_318 (.in(eater_rom_1_p2[1]));
  LED led_319 (.in(eater_rom_1_p2[2]));
  LED led_320 (.in(eater_rom_1_p2[2]));
  LED led_321 (.in(eater_rom_1_p2[15]));
  LED led_322 (.in(eater_rom_1_p2[15]));
  LED led_323 (.in(eater_rom_1_p2[15]));
  LED led_324 (.in(eater_rom_1_p2[15]));
  LED led_325 (.in(eater_rom_1_p2[11]));
  LED led_326 (.in(eater_rom_1_p2[11]));
  LED led_327 (.in(eater_rom_1_p2[11]));
  LED led_328 (.in(eater_rom_1_p2[11]));
  LED led_329 (.in(eater_rom_1_p2[7]));
  LED led_330 (.in(eater_rom_1_p2[7]));
  LED led_331 (.in(eater_rom_1_p2[7]));
  LED led_332 (.in(eater_rom_1_p2[7]));
  LED led_333 (.in(eater_rom_1_p2[3]));
  LED led_334 (.in(eater_rom_1_p2[3]));
  LED led_335 (.in(eater_rom_1_p2[3]));
  LED led_336 (.in(eater_rom_1_p2[3]));
  LED led_337 (.in(undriven_5[3]));
  LED led_338 (.in(undriven_5[3]));
  LED led_339 (.in(undriven_5[3]));
  LED led_340 (.in(undriven_5[3]));
  LED led_341 (.in(undriven_4[3]));
  LED led_342 (.in(undriven_4[3]));
  LED led_343 (.in(undriven_4[3]));
  LED led_344 (.in(undriven_4[3]));
  LED led_345 (.in(undriven_3[3]));
  LED led_346 (.in(undriven_3[3]));
  LED led_347 (.in(undriven_3[3]));
  LED led_348 (.in(undriven_3[3]));
  LED led_349 (.in(undriven_2[3]));
  LED led_350 (.in(undriven_2[3]));
  LED led_351 (.in(undriven_2[3]));
  LED led_352 (.in(undriven_2[3]));
  LED led_353 (.in(undriven_5[2]));
  LED led_354 (.in(undriven_5[2]));
  LED led_355 (.in(undriven_5[1]));
  LED led_356 (.in(undriven_5[1]));
  LED led_357 (.in(undriven_5[2]));
  LED led_358 (.in(undriven_5[2]));
  LED led_359 (.in(undriven_5[1]));
  LED led_360 (.in(undriven_5[1]));
  LED led_361 (.in(undriven_4[2]));
  LED led_362 (.in(undriven_4[2]));
  LED led_363 (.in(undriven_4[1]));
  LED led_364 (.in(undriven_4[1]));
  LED led_365 (.in(undriven_4[2]));
  LED led_366 (.in(undriven_4[2]));
  LED led_367 (.in(undriven_4[1]));
  LED led_368 (.in(undriven_4[1]));
  LED led_369 (.in(undriven_3[2]));
  LED led_370 (.in(undriven_3[2]));
  LED led_371 (.in(undriven_3[1]));
  LED led_372 (.in(undriven_3[1]));
  LED led_373 (.in(undriven_3[2]));
  LED led_374 (.in(undriven_3[2]));
  LED led_375 (.in(undriven_3[1]));
  LED led_376 (.in(undriven_3[1]));
  LED led_377 (.in(undriven_2[2]));
  LED led_378 (.in(undriven_2[2]));
  LED led_379 (.in(undriven_2[1]));
  LED led_380 (.in(undriven_2[1]));
  LED led_381 (.in(undriven_2[2]));
  LED led_382 (.in(undriven_2[2]));
  LED led_383 (.in(undriven_2[1]));
  LED led_384 (.in(undriven_2[1]));
  LED led_385 (.in(undriven_5[0]));
  LED led_386 (.in(undriven_5[0]));
  LED led_387 (.in(undriven_5[1]));
  LED led_388 (.in(undriven_5[1]));
  LED led_389 (.in(undriven_5[0]));
  LED led_390 (.in(undriven_5[0]));
  LED led_391 (.in(undriven_5[1]));
  LED led_392 (.in(undriven_5[1]));
  LED led_393 (.in(undriven_4[0]));
  LED led_394 (.in(undriven_4[0]));
  LED led_395 (.in(undriven_4[1]));
  LED led_396 (.in(undriven_4[1]));
  LED led_397 (.in(undriven_4[0]));
  LED led_398 (.in(undriven_4[0]));
  LED led_399 (.in(undriven_4[1]));
  LED led_400 (.in(undriven_4[1]));
  LED led_401 (.in(undriven_3[0]));
  LED led_402 (.in(undriven_3[0]));
  LED led_403 (.in(undriven_3[1]));
  LED led_404 (.in(undriven_3[1]));
  LED led_405 (.in(undriven_3[0]));
  LED led_406 (.in(undriven_3[0]));
  LED led_407 (.in(undriven_3[1]));
  LED led_408 (.in(undriven_3[1]));
  LED led_409 (.in(undriven_2[0]));
  LED led_410 (.in(undriven_2[0]));
  LED led_411 (.in(undriven_2[1]));
  LED led_412 (.in(undriven_2[1]));
  LED led_413 (.in(undriven_2[0]));
  LED led_414 (.in(undriven_2[0]));
  LED led_415 (.in(undriven_2[1]));
  LED led_416 (.in(undriven_2[1]));
  LED led_417 (.in(undriven_5[2]));
  LED led_418 (.in(undriven_5[2]));
  LED led_419 (.in(undriven_5[3]));
  LED led_420 (.in(undriven_5[3]));
  LED led_421 (.in(undriven_5[2]));
  LED led_422 (.in(undriven_5[2]));
  LED led_423 (.in(undriven_5[3]));
  LED led_424 (.in(undriven_5[3]));
  LED led_425 (.in(undriven_4[2]));
  LED led_426 (.in(undriven_4[2]));
  LED led_427 (.in(undriven_4[3]));
  LED led_428 (.in(undriven_4[3]));
  LED led_429 (.in(undriven_4[2]));
  LED led_430 (.in(undriven_4[2]));
  LED led_431 (.in(undriven_4[3]));
  LED led_432 (.in(undriven_4[3]));
  LED led_433 (.in(undriven_3[2]));
  LED led_434 (.in(undriven_3[2]));
  LED led_435 (.in(undriven_3[3]));
  LED led_436 (.in(undriven_3[3]));
  LED led_437 (.in(undriven_3[2]));
  LED led_438 (.in(undriven_3[2]));
  LED led_439 (.in(undriven_3[3]));
  LED led_440 (.in(undriven_3[3]));
  LED led_441 (.in(undriven_2[2]));
  LED led_442 (.in(undriven_2[2]));
  LED led_443 (.in(undriven_2[3]));
  LED led_444 (.in(undriven_2[3]));
  LED led_445 (.in(undriven_2[2]));
  LED led_446 (.in(undriven_2[2]));
  LED led_447 (.in(undriven_2[3]));
  LED led_448 (.in(undriven_2[3]));
  LED led_449 (.in(undriven_6));
  LED led_450 (.in(undriven_6));
  LED led_451 (.in(undriven_7));
  LED led_452 (.in(undriven_7));
  LED led_453 (.in(undriven_6));
  LED led_454 (.in(undriven_6));
  LED led_455 (.in(undriven_7));
  LED led_456 (.in(undriven_7));
  LED led_457 (.in(undriven_15));
  LED led_458 (.in(undriven_15));
  LED led_459 (.in(undriven_8));
  LED led_460 (.in(undriven_8));
  LED led_461 (.in(undriven_15));
  LED led_462 (.in(undriven_15));
  LED led_463 (.in(undriven_8));
  LED led_464 (.in(undriven_8));
  LED led_465 (.in(1'b1));
  LED led_466 (.in(1'b1));
  LED led_467 (.in(1'b1));
  LED led_468 (.in(1'b1));
  LED led_469 (.in(1'b1));
  LED led_470 (.in(1'b1));
  LED led_471 (.in(1'b1));
  LED led_472 (.in(1'b1));
  LED led_473 (.in(1'b1));
  LED led_474 (.in(1'b1));
  LED led_475 (.in(1'b1));
  LED led_476 (.in(1'b1));
  LED led_477 (.in(1'b1));
  LED led_478 (.in(1'b1));
  LED led_479 (.in(1'b1));
  LED led_480 (.in(1'b1));
  LED led_481 (.in(undriven_9));
  LED led_482 (.in(undriven_9));
  LED led_483 (.in(undriven_11));
  LED led_484 (.in(undriven_11));
  LED led_485 (.in(undriven_9));
  LED led_486 (.in(undriven_9));
  LED led_487 (.in(undriven_11));
  LED led_488 (.in(undriven_11));
  LED led_489 (.in(undriven_10));
  LED led_490 (.in(undriven_10));
  LED led_491 (.in(undriven_12));
  LED led_492 (.in(undriven_12));
  LED led_493 (.in(undriven_10));
  LED led_494 (.in(undriven_10));
  LED led_495 (.in(undriven_12));
  LED led_496 (.in(undriven_12));
  LED led_497 (.in(or_3_out));
  LED led_498 (.in(or_3_out));
  LED led_499 (.in(or_4_out));
  LED led_500 (.in(or_4_out));
  LED led_501 (.in(or_3_out));
  LED led_502 (.in(or_3_out));
  LED led_503 (.in(or_4_out));
  LED led_504 (.in(or_4_out));
  LED led_505 (.in(or_1_out));
  LED led_506 (.in(or_1_out));
  LED led_507 (.in(or_2_out));
  LED led_508 (.in(or_2_out));
  LED led_509 (.in(or_1_out));
  LED led_510 (.in(or_1_out));
  LED led_511 (.in(or_2_out));
  LED led_512 (.in(or_2_out));
  or or_1 (or_1_out, 1'b1, 1'b1);
  or or_2 (or_2_out, 1'b1, 1'b1);
  or or_3 (or_3_out, 1'b1, 1'b1);
  or or_4 (or_4_out, 1'b1, 1'b1);
  // OR_Gate or_5 has open pins: in0=undriven_15, in1=undriven_15, out=open
  // OR_Gate or_6 has open pins: in0=undriven_15, in1=undriven_15, out=open
  LED led_513 (.in(undriven_13));
  LED led_514 (.in(undriven_13));
  LED led_515 (.in(undriven_16));
  LED led_516 (.in(undriven_16));
  LED led_517 (.in(undriven_13));
  LED led_518 (.in(undriven_13));
  LED led_519 (.in(undriven_16));
  LED led_520 (.in(undriven_16));
  LED led_521 (.in(undriven_14));
  LED led_522 (.in(undriven_14));
  LED led_523 (.in(undriven_17));
  LED led_524 (.in(undriven_17));
  LED led_525 (.in(undriven_14));
  LED led_526 (.in(undriven_14));
  LED led_527 (.in(undriven_17));
  LED led_528 (.in(undriven_17));
  LED led_529 (.in(or_8_out));
  LED led_530 (.in(or_8_out));
  LED led_531 (.in(1'b1));
  LED led_532 (.in(1'b1));
  LED led_533 (.in(or_8_out));
  LED led_534 (.in(or_8_out));
  LED led_535 (.in(1'b1));
  LED led_536 (.in(1'b1));
  LED led_537 (.in(or_7_out));
  LED led_538 (.in(or_7_out));
  LED led_539 (.in(1'b1));
  LED led_540 (.in(1'b1));
  LED led_541 (.in(or_7_out));
  LED led_542 (.in(or_7_out));
  LED led_543 (.in(1'b1));
  LED led_544 (.in(1'b1));
  or or_7 (or_7_out, 1'b1, 1'b1);
  or or_8 (or_8_out, 1'b1, 1'b1);
  // OR_Gate or_9 has open pins: in0=undriven_15, in1=undriven_15, out=open
  LED led_545 (.in(undriven_18));
  LED led_546 (.in(undriven_18));
  LED led_547 (.in(undriven_18));
  LED led_548 (.in(undriven_18));
  LED led_549 (.in(undriven_19));
  LED led_550 (.in(undriven_19));
  LED led_551 (.in(undriven_19));
  LED led_552 (.in(undriven_19));
  LED led_553 (.in(1'b1));
  LED led_554 (.in(1'b1));
  LED led_555 (.in(1'b1));
  LED led_556 (.in(1'b1));
  LED led_557 (.in(1'b1));
  LED led_558 (.in(1'b1));
  LED led_559 (.in(1'b1));
  LED led_560 (.in(1'b1));
endmodule

module EATER_1 (
  input  [4:0] x,
  output L0,
  output L1,
  output L2,
  output T0,
  output T1
);

  wire and_1_out, and_2_out, and_3_out, and_4_out, and_5_out, and_6_out, and_7_out, and_8_out, and_9_out,
       and_10_out, and_11_out, and_12_out, and_13_out, and_14_out, and_15_out, and_16_out, and_17_out,
       and_18_out, and_19_out, and_20_out, or_1_out, or_2_out, or_3_out, or_4_out, or_5_out, or_6_out,
       or_7_out;

  or or_1 (or_1_out, x[1], x[2]);
  and and_1 (and_1_out, x[3], or_1_out);
  or or_2 (or_2_out, x[4], and_1_out);
  and and_2 (and_2_out, x[0], x[2]);
  or or_3 (or_3_out, x[1], ~x[3]);  // OR_Gate
  and and_3 (and_3_out, and_2_out, or_3_out);
  or or_4 (or_4_out, x[4], and_3_out, and_4_out, and_5_out);
  and and_4 (and_4_out, ~x[1], ~x[2], x[3]);  // AND_Gate
  and and_5 (and_5_out, x[1], x[2], ~x[3]);  // AND_Gate
  and and_6 (and_6_out, x[0], x[1], ~x[2], x[4]);  // AND_Gate
  and and_7 (and_7_out, x[0], ~x[1], ~x[2], x[3]);  // AND_Gate
  and and_8 (and_8_out, ~x[0], x[1], x[2], x[3]);  // AND_Gate
  or or_5 (or_5_out, and_6_out, and_7_out, and_8_out, and_9_out);
  and and_9 (and_9_out, ~x[0], ~x[1], x[2], ~x[3]);  // AND_Gate
  and and_10 (and_10_out, ~x[1], x[2], x[3]);  // AND_Gate
  and and_11 (and_11_out, ~x[0], ~x[1], x[3]);  // AND_Gate
  and and_12 (and_12_out, ~x[0], x[1], ~x[2], ~x[3]);  // AND_Gate
  or or_6 (or_6_out, and_10_out, and_11_out, and_12_out, and_13_out, and_14_out);
  and and_13 (and_13_out, x[0], x[1], ~x[3], ~x[4]);  // AND_Gate
  and and_14 (and_14_out, x[0], ~x[1], ~x[2], x[4]);  // AND_Gate
  and and_15 (and_15_out, ~x[0], ~x[2], x[4]);  // AND_Gate
  and and_16 (and_16_out, x[0], ~x[2], ~x[3], ~x[4]);  // AND_Gate
  and and_17 (and_17_out, ~x[0], ~x[1], ~x[2], x[3]);  // AND_Gate
  and and_18 (and_18_out, x[0], x[1], ~x[2], x[3]);  // AND_Gate
  or or_7 (or_7_out, and_15_out, and_16_out, and_17_out, and_18_out, and_19_out, and_20_out);
  and and_19 (and_19_out, x[0], ~x[1], x[2], x[3]);  // AND_Gate
  and and_20 (and_20_out, ~x[0], x[1], x[2], ~x[3]);  // AND_Gate
  G5 g5_1 (
    .x0(or_7_out), .x1(or_6_out), .x2(or_5_out), .x3(or_4_out), .x4(or_2_out), .y0(L0), .y1(L1), .y2(L2),
    .y3(T0), .y4(T1));
endmodule

module EATER_2 (
  input  [4:0] x,
  output C0,
  output C1,
  output C2,
  output R0,
  output R1
);

  wire and_1_out, and_2_out, and_3_out, and_4_out, and_7_out, and_10_out, and_11_out, and_12_out, and_13_out,
       and_14_out, and_15_out, and_16_out, and_17_out, and_18_out, and_19_out, and_20_out, and_21_out,
       or_1_out, or_2_out, or_4_out, or_5_out, or_6_out, or_12_out, or_14_out, xor_1_out, xor_2_out,
       xor_3_out, xor_4_out, xor_5_out, xor_7_out, xor_8_out;

  or or_1 (or_1_out, x[2], x[3]);
  and and_1 (and_1_out, x[0], x[1]);
  or or_2 (or_2_out, x[1], x[2]);
  xor xor_1 (xor_1_out, x[0], x[3]);
  xor xor_2 (xor_2_out, x[1], x[3]);
  xor xor_3 (xor_3_out, x[2], x[3]);
  and and_2 (and_2_out, ~or_1_out, x[4]);  // AND_Gate
  and and_3 (and_3_out, x[2], ~x[4]);  // AND_Gate
  and and_4 (and_4_out, x[3], ~x[4]);  // AND_Gate
  // AND_Gate and_5 is placed but not wired
  // AND_Gate and_6 is placed but not wired
  and and_7 (and_7_out, and_4_out, or_2_out);
  or or_3 (R1, and_2_out, and_7_out);
  or or_4 (or_4_out, and_2_out, and_10_out);
  // AND_Gate and_8 is placed but not wired
  // AND_Gate and_9 is placed but not wired
  and and_10 (and_10_out, and_4_out, ~or_2_out);  // AND_Gate
  or or_5 (or_5_out, x[1], x[0]);
  or or_6 (or_6_out, and_1_out, ~x[3]);  // OR_Gate
  and and_11 (and_11_out, or_5_out, and_3_out, or_6_out);
  or or_7 (R0, or_4_out, and_11_out);
  // OR_Gate or_8 is placed but not wired
  and and_12 (and_12_out, ~x[2], x[0]);  // AND_Gate
  and and_13 (and_13_out, and_12_out, xor_2_out, xor_4_out);
  // OR_Gate or_9 is placed but not wired
  // OR_Gate or_10 is placed but not wired
  xor xor_4 (xor_4_out, x[4], x[3]);
  and and_14 (and_14_out, and_3_out, ~xor_2_out, ~x[0]);  // AND_Gate
  or or_11 (C2, and_13_out, and_14_out);
  // NOR_Gate nor_1 is placed but not wired
  and and_15 (and_15_out, xor_2_out, ~x[4]);  // AND_Gate
  or or_12 (or_12_out, ~xor_3_out, xor_1_out);  // OR_Gate
  xor xor_5 (xor_5_out, x[1], x[0]);
  and and_16 (and_16_out, and_15_out, or_12_out);
  and and_17 (and_17_out, and_2_out, xor_5_out);
  or or_13 (C1, and_16_out, and_17_out);
  // NAND_Gate nand_1 is placed but not wired
  // XOR_Gate xor_6 is placed but not wired
  xor xor_7 (xor_7_out, x[4], x[0]);
  and and_18 (and_18_out, xor_7_out, ~or_1_out);  // AND_Gate
  or or_14 (or_14_out, and_18_out, and_19_out);
  xor xor_8 (xor_8_out, xor_1_out, x[2]);
  and and_19 (and_19_out, and_1_out, ~x[4], ~x[2]);  // AND_Gate
  and and_20 (and_20_out, xor_2_out, ~x[4]);  // AND_Gate
  and and_21 (and_21_out, and_20_out, xor_8_out);
  or or_15 (C0, and_21_out, or_14_out);

  // Notes on the sheet:
  //   x0x1
  //   t
  //   x0
  //   x1
  //   x2
  //   x3
  //   x4
  //   s
  //   y0
  //   y1
  //   y2
  //   w
  //   k
  //   g
  //   R1
  //   R0
  //   C2
  //   C1
  //   C0
endmodule

module EATER_3 (
  input  [4:0] x,
  output C0,
  output C1,
  output C2,
  output R0,
  output R1
);

  wire and_5_out, and_6_out, and_7_out, and_8_out, and_9_out, and_10_out, and_11_out, and_12_out, and_13_out,
       and_14_out, and_15_out, and_16_out, and_17_out, and_18_out, and_19_out, and_20_out, and_21_out,
       or_3_out, or_4_out, or_7_out, or_8_out, or_9_out, or_12_out, or_14_out, undriven, xor_1_out,
       xor_2_out, xor_3_out, xor_5_out, xor_6_out, xor_7_out, xor_8_out;

  // AND_Gate and_1 is placed but not wired
  // AND_Gate and_2 is placed but not wired
  // AND_Gate and_3 is placed but not wired
  // AND_Gate and_4 is placed but not wired
  // VARIABLES variables_1: pin names not known
  // OR_Gate or_1 is placed but not wired
  // OR_Gate or_2 is placed but not wired
  xor xor_1 (xor_1_out, x[0], x[3]);
  xor xor_2 (xor_2_out, x[1], x[3]);
  xor xor_3 (xor_3_out, x[2], x[3]);
  and and_5 (and_5_out, xor_2_out, ~x[4]);  // AND_Gate
  and and_6 (and_6_out, x[0], x[1]);
  or or_3 (or_3_out, x[2], x[3]);
  and and_7 (and_7_out, ~or_3_out, x[4]);  // AND_Gate
  and and_8 (and_8_out, x[2], ~x[4]);  // AND_Gate
  or or_4 (or_4_out, x[1], x[2]);
  and and_9 (and_9_out, x[3], ~x[4]);  // AND_Gate
  // OR_Gate or_5 is placed but not wired
  and and_10 (and_10_out, and_9_out, undriven);
  or or_6 (R1, and_7_out, and_10_out);
  or or_7 (or_7_out, and_7_out, and_11_out);
  // NOR_Gate nor_1 is placed but not wired
  // NAND_Gate nand_1 is placed but not wired
  and and_11 (and_11_out, and_9_out, ~undriven);  // AND_Gate
  or or_8 (or_8_out, x[1], x[0]);
  or or_9 (or_9_out, and_6_out, ~x[3]);  // OR_Gate
  and and_12 (and_12_out, or_8_out, and_8_out, or_9_out);
  or or_10 (R0, or_7_out, and_12_out);
  // XOR_Gate xor_4 is placed but not wired
  and and_13 (and_13_out, ~x[2], x[0]);  // AND_Gate
  and and_14 (and_14_out, and_13_out, xor_2_out, xor_5_out);
  xor xor_5 (xor_5_out, x[4], x[3]);
  and and_15 (and_15_out, and_8_out, ~xor_2_out, ~x[0]);  // AND_Gate
  or or_11 (C2, and_14_out, and_15_out);
  and and_16 (and_16_out, xor_2_out, ~x[4]);  // AND_Gate
  or or_12 (or_12_out, ~xor_3_out, xor_1_out);  // OR_Gate
  xor xor_6 (xor_6_out, x[1], x[0]);
  and and_17 (and_17_out, and_16_out, or_12_out);
  and and_18 (and_18_out, and_7_out, xor_6_out);
  or or_13 (C1, and_17_out, and_18_out);
  xor xor_7 (xor_7_out, x[4], x[0]);
  and and_19 (and_19_out, xor_7_out, ~or_3_out);  // AND_Gate
  or or_14 (or_14_out, and_19_out, and_20_out);
  xor xor_8 (xor_8_out, xor_1_out, x[2]);
  and and_20 (and_20_out, and_6_out, ~x[4], ~x[2]);  // AND_Gate
  and and_21 (and_21_out, and_5_out, xor_8_out);
  or or_15 (C0, and_21_out, or_14_out);

  // Notes on the sheet:
  //   y1
  //   y2
  //   x0
  //   x1
  //   x2
  //   x3
  //   x4
  //   y0
  //   a
  //   b
  //   c
  //   d
  //   e
  //   f
  //   g
  //   R1
  //   R0
  //   C2
  //   C1
  //   C0
endmodule

module EATER_4bit_1 (
  input  [3:0] x,
  output C0,
  output C1,
  output C2,
  output R0,
  output R1
);

  wire and_1_out, and_2_out, and_8_out, and_9_out, and_10_out, and_12_out, and_13_out, and_14_out, or_1_out,
       or_2_out, or_4_out, or_9_out, xor_1_out, xor_2_out, xor_3_out;

  or or_1 (or_1_out, x[1], x[2]);
  and and_1 (and_1_out, x[0], x[1]);
  and and_2 (and_2_out, ~or_1_out, x[3]);  // AND_Gate
  xor xor_1 (xor_1_out, x[0], x[3]);
  xor xor_2 (xor_2_out, x[1], x[3]);
  xor xor_3 (xor_3_out, x[2], x[3]);
  // AND_Gate and_3 is placed but not wired
  // AND_Gate and_4 is placed but not wired
  and and_5 (R1, or_1_out, x[3]);
  or or_2 (or_2_out, and_1_out, ~x[3]);  // OR_Gate
  or or_3 (R0, and_2_out, and_9_out);
  // AND_Gate and_6 is placed but not wired
  // AND_Gate and_7 is placed but not wired
  or or_4 (or_4_out, x[1], x[0]);
  and and_8 (and_8_out, xor_2_out, x[2], ~x[0]);  // AND_Gate
  and and_9 (and_9_out, or_2_out, x[2], or_4_out);
  // OR_Gate or_5 is placed but not wired
  and and_10 (and_10_out, and_2_out, x[0]);
  or or_6 (C2, and_8_out, and_10_out);
  and and_11 (C1, xor_2_out, or_9_out);
  // OR_Gate or_7 is placed but not wired
  // OR_Gate or_8 is placed but not wired
  or or_9 (or_9_out, ~xor_3_out, xor_1_out);  // OR_Gate
  and and_12 (and_12_out, xor_1_out, ~or_1_out);  // AND_Gate
  // NOR_Gate nor_1 is placed but not wired
  and and_13 (and_13_out, xor_2_out, ~xor_1_out, x[2]);  // AND_Gate
  and and_14 (and_14_out, ~and_1_out, x[2]);  // AND_Gate
  or or_10 (C0, and_12_out, and_13_out, and_14_out);
  // XOR_Gate xor_4 is placed but not wired
  // NAND_Gate nand_1 is placed but not wired

  // Notes on the sheet:
  //   x0
  //   x1
  //   x2
  //   x3
  //   x0x1
  //   s
  //   x3s'
  //   y0
  //   y1
  //   y2
  //   R1
  //   R0
  //   C2
  //   C1
  //   C0
endmodule

module CREATOR_1 (
  input  [4:0] x,
  output R0,
  output R1,
  output R2,
  output R3,
  output T0,
  output T1
);

  wire and_2_out, eater_1_1_l2;

  EATER_1 eater_1_1 (.x(x), .L0(R0), .L1(R3), .L2(eater_1_1_l2), .T0(T0), .T1(T1));
  and and_1 (R2, R0, R3);
  and and_2 (and_2_out, ~R0, R3);  // AND_Gate
  or or_1 (R1, eater_1_1_l2, and_2_out);
endmodule

module CREATOR_2 (
  input  [2:0] L,
  input  E,
  input  T,
  output [3:0] R
);

  wire and_1_out, and_2_out, or_1_out, or_2_out, or_3_out, or_4_out, or_5_out;

  and and_1 (and_1_out, L[1], L[0]);
  and and_2 (and_2_out, L[1], ~L[0]);  // AND_Gate
  or or_1 (or_1_out, L[2], and_2_out);
  or or_2 (or_2_out, L[0], T);
  or or_3 (or_3_out, or_1_out, T);
  or or_4 (or_4_out, and_1_out, T);
  or or_5 (or_5_out, L[2], T);
  and and_3 (R[0], or_2_out, E);
  and and_4 (R[1], or_3_out, E);
  and and_5 (R[2], or_4_out, E);
  and and_6 (R[3], or_5_out, E);

  // Notes on the sheet:
  //   CREATOR
endmodule

module CREATOR_3 (
  input  T,
  input  y,
  input  [2:0] L,
  output [3:0] R
);

  wire and_1_out, and_2_out, and_3_out;

  and and_1 (and_1_out, y, L[2]);
  and and_2 (and_2_out, y, L[1]);
  and and_3 (and_3_out, y, L[0]);
  // CREATOR_2 creator_2_1: pin names not known; wires that end beside it: T, and_1_out, and_2_out, and_3_out, R[0]
endmodule

module CREATOR_4 (
  input  [4:0] x,
  output [3:0] def1,
  output [3:0] def0,
  output [3:0] C0,
  output [3:0] C1,
  output [3:0] C2,
  output [3:0] C3
);

  wire and_1_out, and_2_out, and_3_out, and_4_out, eater_1_1_t0, eater_1_1_t1, nor_2_out, or_1_out, or_2_out;
  wire [2:0] eater_1_1_l0;

  EATER_1 eater_1_1 (
    .x(x), .L0(eater_1_1_l0[0]), .L1(eater_1_1_l0[1]), .L2(eater_1_1_l0[2]), .T0(eater_1_1_t0),
    .T1(eater_1_1_t1));
  or or_1 (or_1_out, eater_1_1_l0[0], eater_1_1_l0[1], eater_1_1_l0[2]);
  nor nor_1 (def0[2], or_1_out, eater_1_1_t0, eater_1_1_t1);
  or or_2 (or_2_out, eater_1_1_t0, eater_1_1_t1);
  nor nor_2 (nor_2_out, eater_1_1_t0, eater_1_1_t1);
  CREATOR_3 creator_3_1 (.T(or_2_out), .y(nor_2_out), .L(eater_1_1_l0), .R(C0));
  and and_1 (and_1_out, eater_1_1_t0, ~eater_1_1_t1);  // AND_Gate
  and and_2 (and_2_out, eater_1_1_t0, eater_1_1_t1);
  CREATOR_3 creator_3_2 (.T(eater_1_1_t1), .y(and_1_out), .L(eater_1_1_l0), .R(C1));
  CREATOR_3 creator_3_3 (.T(and_2_out), .y(and_3_out), .L(eater_1_1_l0), .R(C2));
  and and_3 (and_3_out, ~eater_1_1_t0, eater_1_1_t1);  // AND_Gate
  and and_4 (and_4_out, eater_1_1_t0, eater_1_1_t1);
  CREATOR_3 creator_3_4 (.T(1'b0), .y(and_4_out), .L(eater_1_1_l0), .R(C3));

  assign {def0[3], def0[1:0]} = {1'b0, {2{def0[2]}}};
  assign def1 = {3'b000, def0[2]};
endmodule

module CREATOR_5 (
  input  [4:0] x,
  output [3:0] C3,
  output [3:0] C2,
  output [3:0] def0,
  output [3:0] def1,
  output [3:0] C0,
  output [3:0] C1
);

  wire and_1_out, and_2_out, eater_1_1_t0, eater_1_1_t1, or_1_out, or_2_out;
  wire [2:0] eater_1_1_l0;

  EATER_1 eater_1_1 (
    .x(x), .L0(eater_1_1_l0[0]), .L1(eater_1_1_l0[1]), .L2(eater_1_1_l0[2]), .T0(eater_1_1_t0),
    .T1(eater_1_1_t1));
  CREATOR_2 creator_2_1 (.L(eater_1_1_l0), .E(and_1_out), .T(1'b0), .R(C3));
  CREATOR_2 creator_2_2 (.L(eater_1_1_l0), .E(eater_1_1_t1), .T(and_2_out), .R(C2));
  and and_1 (and_1_out, eater_1_1_t0, eater_1_1_t1);
  or or_1 (or_1_out, eater_1_1_t0, eater_1_1_t1);
  or or_2 (or_2_out, eater_1_1_t0, eater_1_1_t1);
  CREATOR_2 creator_2_3 (.L(eater_1_1_l0), .E(1'b1), .T(or_1_out), .R(C0));
  CREATOR_2 creator_2_4 (.L(eater_1_1_l0), .E(or_2_out), .T(eater_1_1_t1), .R(C1));
  and and_2 (and_2_out, eater_1_1_t0, eater_1_1_t1);
  nor nor_1 (def0[2], eater_1_1_l0[0], eater_1_1_l0[1], eater_1_1_l0[2], eater_1_1_t0, eater_1_1_t1);

  assign {def0[3], def0[1:0]} = {1'b0, {2{def0[2]}}};
  assign def1 = {3'b000, def0[2]};
endmodule

module CREATOR_6 (
  input  [4:0] x,
  output [3:0] F3,
  output [3:0] F2,
  output [3:0] F0,
  output [3:0] F1
);

  wire and_1_out, eater_noai_1_r0, eater_noai_1_r1, or_1_out;
  wire [2:0] eater_noai_1_c0;

  EATER_noAI eater_noai_1 (
    .n(x), .C0(eater_noai_1_c0[0]), .C1(eater_noai_1_c0[1]), .C2(eater_noai_1_c0[2]), .R0(eater_noai_1_r0),
    .R1(eater_noai_1_r1));
  and and_1 (and_1_out, eater_noai_1_r1, eater_noai_1_r0);
  or or_1 (or_1_out, eater_noai_1_r1, eater_noai_1_r0);
  CREATOR_2 creator_2_1 (.L(eater_noai_1_c0), .E(and_1_out), .T(1'b0), .R(F3));
  CREATOR_2 creator_2_2 (.L(eater_noai_1_c0), .E(eater_noai_1_r1), .T(and_1_out), .R(F2));
  CREATOR_2 creator_2_3 (.L(eater_noai_1_c0), .E(1'b1), .T(or_1_out), .R(F0));
  CREATOR_2 creator_2_4 (.L(eater_noai_1_c0), .E(or_1_out), .T(eater_noai_1_r1), .R(F1));

  // Notes on the sheet:
  //   BLACK
endmodule

module CREATOR_7 (
  input  [4:0] n,
  input  in_2,
  input  in_3,
  output [3:0] F3,
  output [3:0] F2,
  output [3:0] F0,
  output [3:0] F1
);

  wire and_8_out, and_10_out, decoder_1_out0, decoder_1_out1, eater_1_c1, eater_1_r0, eater_1_r1, nor_1_out,
       or_1_out;
  wire [3:0] and_4_out, and_11_out, and_13_out, and_14_out, bit_extender_1_out, bit_extender_2_out,
       bit_extender_3_out, eater_1_c0, or_5_out, or_6_out;

  and and_1 (and_4_out[3], 1'b1, nor_1_out);
  and and_2 (and_4_out[2], 1'b0, nor_1_out);
  EATER eater_1 (.n(n), .C0(eater_1_c0[0]), .C1(eater_1_c1), .C2(eater_1_c0[3]), .R0(eater_1_r0), .R1(eater_1_r1));
  and and_3 (and_4_out[1], 1'b0, nor_1_out);
  and and_4 (and_4_out[0], 1'b0, nor_1_out);
  and and_5 (and_11_out[3], 1'b0, nor_1_out);
  nor nor_1 (nor_1_out, eater_1_r1, eater_1_r0, eater_1_c0[3], eater_1_c1, eater_1_c0[0]);
  and and_6 (and_11_out[2], 1'b1, nor_1_out);
  and and_7 (and_11_out[1], 1'b1, nor_1_out);
  and and_8 (and_8_out, ~eater_1_c0[0], eater_1_c1);  // AND_Gate
  and and_9 (eater_1_c0[2], eater_1_c0[0], eater_1_c1);
  and and_10 (and_10_out, eater_1_r0, eater_1_r1);
  or or_1 (or_1_out, eater_1_r0, eater_1_r1);
  and and_11 (and_11_out[0], 1'b1, nor_1_out);
  or or_2 (eater_1_c0[1], and_8_out, eater_1_c0[3]);
  assign bit_extender_1_out = {{3{and_10_out}}, and_10_out};  // Bit_Extender bit_extender_1
  assign bit_extender_2_out = {{3{eater_1_r1}}, eater_1_r1};  // Bit_Extender bit_extender_2
  assign bit_extender_3_out = {{3{or_1_out}}, or_1_out};  // Bit_Extender bit_extender_3
  assign F3 = bit_extender_1_out & eater_1_c0;  // AND_Gate and_12, 4 bits wide
  assign F0 = and_11_out | bit_extender_3_out | eater_1_c0;  // OR_Gate or_3, 4 bits wide
  assign F2 = and_11_out | and_13_out;  // OR_Gate or_4, 4 bits wide
  assign and_13_out = bit_extender_2_out & or_5_out;  // AND_Gate and_13, 4 bits wide
  assign or_5_out = bit_extender_1_out | eater_1_c0;  // OR_Gate or_5, 4 bits wide
  assign or_6_out = bit_extender_2_out | eater_1_c0;  // OR_Gate or_6, 4 bits wide
  assign and_14_out = bit_extender_3_out & or_6_out;  // AND_Gate and_14, 4 bits wide
  assign F1 = and_4_out | and_14_out;  // OR_Gate or_7, 4 bits wide
  Decoder decoder_1 (.out0(decoder_1_out0), .out1(decoder_1_out1), .sel(in_3), .en(in_2));

  // Notes on the sheet:
  //   EATER
endmodule

module CREATOR_8 (
  input  [4:0] n,
  output [3:0] F3,
  output [3:0] F2,
  output [3:0] F0,
  output [3:0] F1
);

  wire and_1_out, and_3_out, eater_1_c1, eater_1_r0, eater_1_r1, nor_1_out, or_1_out;
  wire [3:0] and_7_out, and_8_out, bit_extender_1_out, bit_extender_2_out, bit_extender_3_out, eater_1_c0,
       or_4_out, or_5_out;
  wire [3:2] and_5_out;

  EATER eater_1 (.n(n), .C0(eater_1_c0[0]), .C1(eater_1_c1), .C2(eater_1_c0[3]), .R0(eater_1_r0), .R1(eater_1_r1));
  nor nor_1 (nor_1_out, eater_1_r1, eater_1_r0, eater_1_c0[3], eater_1_c1, eater_1_c0[0]);
  and and_1 (and_1_out, ~eater_1_c0[0], eater_1_c1);  // AND_Gate
  and and_2 (eater_1_c0[2], eater_1_c0[0], eater_1_c1);
  and and_3 (and_3_out, eater_1_r0, eater_1_r1);
  or or_1 (or_1_out, eater_1_r0, eater_1_r1);
  and and_4 (and_5_out[3], nor_1_out, 1'b1);
  and and_5 (and_5_out[2], nor_1_out, 1'b0);
  or or_2 (eater_1_c0[1], and_1_out, eater_1_c0[3]);
  assign bit_extender_1_out = {{3{and_3_out}}, and_3_out};  // Bit_Extender bit_extender_1
  assign bit_extender_2_out = {{3{eater_1_r1}}, eater_1_r1};  // Bit_Extender bit_extender_2
  assign bit_extender_3_out = {{3{or_1_out}}, or_1_out};  // Bit_Extender bit_extender_3
  assign F2 = {and_5_out[2], {3{and_5_out[3]}}} | and_7_out;  // OR_Gate or_3, 4 bits wide
  assign F3 = bit_extender_1_out & eater_1_c0;  // AND_Gate and_6, 4 bits wide
  assign and_7_out = bit_extender_2_out & or_4_out;  // AND_Gate and_7, 4 bits wide
  assign or_4_out = bit_extender_1_out | eater_1_c0;  // OR_Gate or_4, 4 bits wide
  assign or_5_out = bit_extender_2_out | eater_1_c0;  // OR_Gate or_5, 4 bits wide
  assign F0 = {and_5_out[2], {3{and_5_out[3]}}} | bit_extender_3_out | eater_1_c0;  // OR_Gate or_6, 4 bits wide
  assign and_8_out = bit_extender_3_out & or_5_out;  // AND_Gate and_8, 4 bits wide
  assign F1 = {and_5_out, {2{and_5_out[2]}}} | and_8_out;  // OR_Gate or_7, 4 bits wide

  // Notes on the sheet:
  //   EATER
endmodule

module G4 (
  input  [4:0] x,
  output [4:0] y
);

  wire and_1_out, and_2_out, nor_1_out;

  and and_1 (and_1_out, x[2], x[4]);
  and and_2 (and_2_out, ~x[2], x[3], x[4]);  // AND_Gate
  nor nor_1 (nor_1_out, and_2_out, and_1_out);
  and and_3 (y[0], x[0], nor_1_out);
  and and_4 (y[1], x[1], nor_1_out);
  and and_5 (y[2], x[2], nor_1_out);
  and and_6 (y[3], x[3], nor_1_out);
  and and_7 (y[4], x[4], nor_1_out);
endmodule

module G5 (
  input  x0,
  input  x1,
  input  x2,
  input  x3,
  input  x4,
  output y0,
  output y1,
  output y2,
  output y3,
  output y4
);

  wire and_1_out, and_2_out, nor_1_out;

  and and_1 (and_1_out, x2, x4);
  and and_2 (and_2_out, ~x2, x3, x4);  // AND_Gate
  nor nor_1 (nor_1_out, and_2_out, and_1_out);
  and and_3 (y0, x0, nor_1_out);
  and and_4 (y1, x1, nor_1_out);
  and and_5 (y2, x2, nor_1_out);
  and and_6 (y3, x3, nor_1_out);
  and and_7 (y4, x4, nor_1_out);
endmodule
