// Logisim project MEM.circ as structural Verilog: 5 circuits, main circuit RS
module RS (
  input  S,
  input  R,
  input  Clock,
  output Q
);

  wire nand_1_out, nand_2_out, nand_4_out;

  nand nand_1 (nand_1_out, S, Clock);
  nand nand_2 (nand_2_out, R, Clock);
  nand nand_3 (Q, nand_4_out, nand_1_out);
  nand nand_4 (nand_4_out, nand_2_out, Q);

  // Notes on the sheet:
  //   RS (reset-set) Trigger
endmodule

module D (
  input  Data,
  input  Clock,
  output Q
);

  wire not_1_out;

  not not_1 (not_1_out, Data);
  RS rs_1 (.S(Data), .R(not_1_out), .Clock(Clock), .Q(Q));

  // Notes on the sheet:
  //   D (data) Trigger
endmodule

module REG4 (
  input  [3:0] D_IN,
  input  Clock,
  output [3:0] D_OUT
);

  D d_1 (.Data(D_IN[3]), .Clock(Clock), .Q(D_OUT[3]));
  D d_2 (.Data(D_IN[2]), .Clock(Clock), .Q(D_OUT[2]));
  D d_3 (.Data(D_IN[1]), .Clock(Clock), .Q(D_OUT[1]));
  D d_4 (.Data(D_IN[0]), .Clock(Clock), .Q(D_OUT[0]));

  // Notes on the sheet:
  //   4-bit register
endmodule

module REG8 (
  input  [7:0] D_IN,
  input  Clock,
  output [7:0] D_OUT
);

  REG4 reg4_1 (.D_IN(D_IN[7:4]), .Clock(Clock), .D_OUT(D_OUT[7:4]));
  REG4 reg4_2 (.D_IN(D_IN[3:0]), .Clock(Clock), .D_OUT(D_OUT[3:0]));

  // Notes on the sheet:
  //   8-bit register
endmodule

module SRAM (
  input  [7:0] D_IN,
  input  [1:0] Address,
  input  Clock,
  output [7:0] D_OUT
);

  wire decoder_1_out0, decoder_1_out1, decoder_1_out2, decoder_1_out3;
  wire [7:0] reg8_1_d_out, reg8_2_d_out, reg8_3_d_out, reg8_4_d_out;

  Decoder #(.select(2)) decoder_1 (
    .out0(decoder_1_out0), .out1(decoder_1_out1), .out2(decoder_1_out2), .out3(decoder_1_out3),
    .sel(Address), .en(Clock));
  REG8 reg8_1 (.D_IN(D_IN), .Clock(decoder_1_out3), .D_OUT(reg8_1_d_out));
  REG8 reg8_2 (.D_IN(D_IN), .Clock(decoder_1_out2), .D_OUT(reg8_2_d_out));
  REG8 reg8_3 (.D_IN(D_IN), .Clock(decoder_1_out1), .D_OUT(reg8_3_d_out));
  REG8 reg8_4 (.D_IN(D_IN), .Clock(decoder_1_out0), .D_OUT(reg8_4_d_out));
  Multiplexer #(.select(2), .width(8)) multiplexer_1 (
    .in0(reg8_4_d_out), .in1(reg8_3_d_out), .in2(reg8_2_d_out), .in3(reg8_1_d_out), .out(D_OUT), .sel(Address));

  // Notes on the sheet:
  //   4-byte SRAM
endmodule
