// Logisim project seven-segments.circ as structural Verilog: 5 circuits, main circuit main
module main (
);

  wire showcase_1_da, showcase_1_db, showcase_1_dc, showcase_1_dd, showcase_1_de, showcase_1_df,
       showcase_1_dg, showcase_1_ha, showcase_1_hb, showcase_1_hc, showcase_1_hd, showcase_1_he,
       showcase_1_hf, showcase_1_hg, showcase_2_da, showcase_2_db, showcase_2_dc, showcase_2_dd,
       showcase_2_de, showcase_2_df, showcase_2_dg, showcase_2_ha, showcase_2_hb, showcase_2_hc,
       showcase_2_hd, showcase_2_he, showcase_2_hf, showcase_2_hg, showcase_3_da, showcase_3_db,
       showcase_3_dc, showcase_3_dd, showcase_3_de, showcase_3_df, showcase_3_dg, showcase_3_ha,
       showcase_3_hb, showcase_3_hc, showcase_3_hd, showcase_3_he, showcase_3_hf, showcase_3_hg,
       showcase_4_da, showcase_4_db, showcase_4_dc, showcase_4_dd, showcase_4_de, showcase_4_df,
       showcase_4_dg, showcase_4_ha, showcase_4_hb, showcase_4_hc, showcase_4_hd, showcase_4_he,
       showcase_4_hf, showcase_4_hg, showcase_5_da, showcase_5_db, showcase_5_dc, showcase_5_dd,
       showcase_5_de, showcase_5_df, showcase_5_dg, showcase_5_ha, showcase_5_hb, showcase_5_hc,
       showcase_5_hd, showcase_5_he, showcase_5_hf, showcase_5_hg, showcase_6_da, showcase_6_db,
       showcase_6_dc, showcase_6_dd, showcase_6_de, showcase_6_df, showcase_6_dg, showcase_6_ha,
       showcase_6_hb, showcase_6_hc, showcase_6_hd, showcase_6_he, showcase_6_hf, showcase_6_hg,
       showcase_7_da, showcase_7_db, showcase_7_dc, showcase_7_dd, showcase_7_de, showcase_7_df,
       showcase_7_dg, showcase_7_ha, showcase_7_hb, showcase_7_hc, showcase_7_hd, showcase_7_he,
       showcase_7_hf, showcase_7_hg, showcase_8_da, showcase_8_db, showcase_8_dc, showcase_8_dd,
       showcase_8_de, showcase_8_df, showcase_8_dg, showcase_8_ha, showcase_8_hb, showcase_8_hc,
       showcase_8_hd, showcase_8_he, showcase_8_hf, showcase_8_hg, showcase_9_da, showcase_9_db,
       showcase_9_dc, showcase_9_dd, showcase_9_de, showcase_9_df, showcase_9_dg, showcase_9_ha,
       showcase_9_hb, showcase_9_hc, showcase_9_hd, showcase_9_he, showcase_9_hf, showcase_9_hg,
       showcase_10_da, showcase_10_db, showcase_10_dc, showcase_10_dd, showcase_10_de, showcase_10_df,
       showcase_10_dg, showcase_10_ha, showcase_10_hb, showcase_10_hc, showcase_10_hd, showcase_10_he,
       showcase_10_hf, showcase_10_hg, showcase_11_da, showcase_11_db, showcase_11_dc, showcase_11_dd,
       showcase_11_de, showcase_11_df, showcase_11_dg, showcase_11_ha, showcase_11_hb, showcase_11_hc,
       showcase_11_hd, showcase_11_he, showcase_11_hf, showcase_11_hg, showcase_12_da, showcase_12_db,
       showcase_12_dc, showcase_12_dd, showcase_12_de, showcase_12_df, showcase_12_dg, showcase_12_ha,
       showcase_12_hb, showcase_12_hc, showcase_12_hd, showcase_12_he, showcase_12_hf, showcase_12_hg,
       showcase_13_da, showcase_13_db, showcase_13_dc, showcase_13_dd, showcase_13_de, showcase_13_df,
       showcase_13_dg, showcase_13_ha, showcase_13_hb, showcase_13_hc, showcase_13_hd, showcase_13_he,
       showcase_13_hf, showcase_13_hg, showcase_14_da, showcase_14_db, showcase_14_dc, showcase_14_dd,
       showcase_14_de, showcase_14_df, showcase_14_dg, showcase_14_ha, showcase_14_hb, showcase_14_hc,
       showcase_14_hd, showcase_14_he, showcase_14_hf, showcase_14_hg, showcase_15_da, showcase_15_db,
       showcase_15_dc, showcase_15_dd, showcase_15_de, showcase_15_df, showcase_15_dg, showcase_15_ha,
       showcase_15_hb, showcase_15_hc, showcase_15_hd, showcase_15_he, showcase_15_hf, showcase_15_hg,
       showcase_16_da, showcase_16_db, showcase_16_dc, showcase_16_dd, showcase_16_de, showcase_16_df,
       showcase_16_dg, showcase_16_ha, showcase_16_hb, showcase_16_hc, showcase_16_hd, showcase_16_he,
       showcase_16_hf, showcase_16_hg;

  LED led_1 (.in(showcase_1_da));
  LED led_2 (.in(showcase_1_da));
  LED led_3 (.in(showcase_1_df));
  LED led_4 (.in(showcase_1_df));
  LED led_5 (.in(showcase_1_df));
  LED led_6 (.in(showcase_1_dg));
  LED led_7 (.in(showcase_1_dg));
  LED led_8 (.in(showcase_1_de));
  LED led_9 (.in(showcase_1_de));
  LED led_10 (.in(showcase_1_de));
  LED led_11 (.in(showcase_1_dd));
  LED led_12 (.in(showcase_1_dd));
  LED led_13 (.in(showcase_2_da));
  LED led_14 (.in(showcase_2_da));
  LED led_15 (.in(showcase_2_df));
  LED led_16 (.in(showcase_2_df));
  LED led_17 (.in(showcase_2_df));
  LED led_18 (.in(showcase_2_dg));
  LED led_19 (.in(showcase_2_dg));
  LED led_20 (.in(showcase_2_de));
  LED led_21 (.in(showcase_2_de));
  LED led_22 (.in(showcase_2_de));
  LED led_23 (.in(showcase_2_dd));
  LED led_24 (.in(showcase_2_dd));
  LED led_25 (.in(showcase_3_da));
  LED led_26 (.in(showcase_3_da));
  LED led_27 (.in(showcase_3_df));
  LED led_28 (.in(showcase_3_df));
  LED led_29 (.in(showcase_3_df));
  LED led_30 (.in(showcase_3_dg));
  LED led_31 (.in(showcase_3_dg));
  LED led_32 (.in(showcase_3_de));
  LED led_33 (.in(showcase_3_de));
  LED led_34 (.in(showcase_3_de));
  LED led_35 (.in(showcase_3_dd));
  LED led_36 (.in(showcase_3_dd));
  LED led_37 (.in(showcase_4_da));
  LED led_38 (.in(showcase_4_da));
  LED led_39 (.in(showcase_4_df));
  LED led_40 (.in(showcase_4_df));
  LED led_41 (.in(showcase_4_df));
  LED led_42 (.in(showcase_4_dg));
  LED led_43 (.in(showcase_4_dg));
  LED led_44 (.in(showcase_4_de));
  LED led_45 (.in(showcase_4_de));
  LED led_46 (.in(showcase_4_de));
  LED led_47 (.in(showcase_4_dd));
  LED led_48 (.in(showcase_4_dd));
  LED led_49 (.in(showcase_1_da));
  Hex_Digit_Display hex_digit_display_1 (.value(4'b0000));  // open: dp
  LED led_50 (.in(showcase_1_db));
  LED led_51 (.in(showcase_1_hf));
  LED led_52 (.in(showcase_1_db));
  LED led_53 (.in(showcase_1_hf));
  SHOWCASE showcase_1 (
    .Da(showcase_1_da), .Db(showcase_1_db), .Dg(showcase_1_dg), .Df(showcase_1_df), .De(showcase_1_de),
    .Dc(showcase_1_dc), .Dd(showcase_1_dd), .n(4'b0000), .Ha(showcase_1_ha), .Hf(showcase_1_hf),
    .Hg(showcase_1_hg), .Hb(showcase_1_hb), .Hc(showcase_1_hc), .He(showcase_1_he), .Hd(showcase_1_hd));
  LED led_54 (.in(showcase_1_db));
  LED led_55 (.in(showcase_1_hf));
  LED led_56 (.in(showcase_1_dg));
  LED led_57 (.in(showcase_1_dc));
  LED led_58 (.in(showcase_1_he));
  LED led_59 (.in(showcase_1_dc));
  LED led_60 (.in(showcase_1_he));
  LED led_61 (.in(showcase_1_dc));
  LED led_62 (.in(showcase_1_he));
  LED led_63 (.in(showcase_1_dd));
  LED led_64 (.in(showcase_2_da));
  Hex_Digit_Display hex_digit_display_2 (.value(4'b0100));  // open: dp
  LED led_65 (.in(showcase_2_db));
  LED led_66 (.in(showcase_2_hf));
  LED led_67 (.in(showcase_2_db));
  LED led_68 (.in(showcase_2_hf));
  SHOWCASE showcase_2 (
    .Da(showcase_2_da), .Db(showcase_2_db), .Dg(showcase_2_dg), .Df(showcase_2_df), .De(showcase_2_de),
    .Dc(showcase_2_dc), .Dd(showcase_2_dd), .n(4'b0100), .Ha(showcase_2_ha), .Hf(showcase_2_hf),
    .Hg(showcase_2_hg), .Hb(showcase_2_hb), .Hc(showcase_2_hc), .He(showcase_2_he), .Hd(showcase_2_hd));
  LED led_69 (.in(showcase_2_db));
  LED led_70 (.in(showcase_2_hf));
  LED led_71 (.in(showcase_2_dg));
  LED led_72 (.in(showcase_2_dc));
  LED led_73 (.in(showcase_2_he));
  LED led_74 (.in(showcase_2_dc));
  LED led_75 (.in(showcase_2_he));
  LED led_76 (.in(showcase_2_dc));
  LED led_77 (.in(showcase_2_he));
  LED led_78 (.in(showcase_2_dd));
  LED led_79 (.in(showcase_3_da));
  Hex_Digit_Display hex_digit_display_3 (.value(4'b1000));  // open: dp
  LED led_80 (.in(showcase_3_db));
  LED led_81 (.in(showcase_3_hf));
  LED led_82 (.in(showcase_3_db));
  LED led_83 (.in(showcase_3_hf));
  SHOWCASE showcase_3 (
    .Da(showcase_3_da), .Db(showcase_3_db), .Dg(showcase_3_dg), .Df(showcase_3_df), .De(showcase_3_de),
    .Dc(showcase_3_dc), .Dd(showcase_3_dd), .n(4'b1000), .Ha(showcase_3_ha), .Hf(showcase_3_hf),
    .Hg(showcase_3_hg), .Hb(showcase_3_hb), .Hc(showcase_3_hc), .He(showcase_3_he), .Hd(showcase_3_hd));
  LED led_84 (.in(showcase_3_db));
  LED led_85 (.in(showcase_3_hf));
  LED led_86 (.in(showcase_3_dg));
  LED led_87 (.in(showcase_3_dc));
  LED led_88 (.in(showcase_3_he));
  LED led_89 (.in(showcase_3_dc));
  LED led_90 (.in(showcase_3_he));
  LED led_91 (.in(showcase_3_dc));
  LED led_92 (.in(showcase_3_he));
  LED led_93 (.in(showcase_3_dd));
  LED led_94 (.in(showcase_4_da));
  Hex_Digit_Display hex_digit_display_4 (.value(4'b1100));  // open: dp
  LED led_95 (.in(showcase_4_db));
  LED led_96 (.in(showcase_4_hf));
  LED led_97 (.in(showcase_4_db));
  LED led_98 (.in(showcase_4_hf));
  SHOWCASE showcase_4 (
    .Da(showcase_4_da), .Db(showcase_4_db), .Dg(showcase_4_dg), .Df(showcase_4_df), .De(showcase_4_de),
    .Dc(showcase_4_dc), .Dd(showcase_4_dd), .n(4'b1100), .Ha(showcase_4_ha), .Hf(showcase_4_hf),
    .Hg(showcase_4_hg), .Hb(showcase_4_hb), .Hc(showcase_4_hc), .He(showcase_4_he), .Hd(showcase_4_hd));
  LED led_99 (.in(showcase_4_db));
  LED led_100 (.in(showcase_4_hf));
  LED led_101 (.in(showcase_4_dg));
  LED led_102 (.in(showcase_4_dc));
  LED led_103 (.in(showcase_4_he));
  LED led_104 (.in(showcase_4_dc));
  LED led_105 (.in(showcase_4_he));
  LED led_106 (.in(showcase_4_dc));
  LED led_107 (.in(showcase_4_he));
  LED led_108 (.in(showcase_4_dd));
  LED led_109 (.in(showcase_1_ha));
  LED led_110 (.in(showcase_1_ha));
  LED led_111 (.in(showcase_1_ha));
  LED led_112 (.in(showcase_1_hb));
  LED led_113 (.in(showcase_1_hb));
  LED led_114 (.in(showcase_1_hb));
  LED led_115 (.in(showcase_1_hg));
  LED led_116 (.in(showcase_1_hg));
  LED led_117 (.in(showcase_1_hg));
  LED led_118 (.in(showcase_1_hc));
  LED led_119 (.in(showcase_1_hc));
  LED led_120 (.in(showcase_1_hc));
  LED led_121 (.in(showcase_1_hd));
  LED led_122 (.in(showcase_1_hd));
  LED led_123 (.in(showcase_1_hd));
  LED led_124 (.in(showcase_2_ha));
  LED led_125 (.in(showcase_2_ha));
  LED led_126 (.in(showcase_2_ha));
  LED led_127 (.in(showcase_2_hb));
  LED led_128 (.in(showcase_2_hb));
  LED led_129 (.in(showcase_2_hb));
  LED led_130 (.in(showcase_2_hg));
  LED led_131 (.in(showcase_2_hg));
  LED led_132 (.in(showcase_2_hg));
  LED led_133 (.in(showcase_2_hc));
  LED led_134 (.in(showcase_2_hc));
  LED led_135 (.in(showcase_2_hc));
  LED led_136 (.in(showcase_2_hd));
  LED led_137 (.in(showcase_2_hd));
  LED led_138 (.in(showcase_2_hd));
  LED led_139 (.in(showcase_3_ha));
  LED led_140 (.in(showcase_3_ha));
  LED led_141 (.in(showcase_3_ha));
  LED led_142 (.in(showcase_3_hb));
  LED led_143 (.in(showcase_3_hb));
  LED led_144 (.in(showcase_3_hb));
  LED led_145 (.in(showcase_3_hg));
  LED led_146 (.in(showcase_3_hg));
  LED led_147 (.in(showcase_3_hg));
  LED led_148 (.in(showcase_3_hc));
  LED led_149 (.in(showcase_3_hc));
  LED led_150 (.in(showcase_3_hc));
  LED led_151 (.in(showcase_3_hd));
  LED led_152 (.in(showcase_3_hd));
  LED led_153 (.in(showcase_3_hd));
  LED led_154 (.in(showcase_4_ha));
  LED led_155 (.in(showcase_4_ha));
  LED led_156 (.in(showcase_4_ha));
  LED led_157 (.in(showcase_4_hb));
  LED led_158 (.in(showcase_4_hb));
  LED led_159 (.in(showcase_4_hb));
  LED led_160 (.in(showcase_4_hg));
  LED led_161 (.in(showcase_4_hg));
  LED led_162 (.in(showcase_4_hg));
  LED led_163 (.in(showcase_4_hc));
  LED led_164 (.in(showcase_4_hc));
  LED led_165 (.in(showcase_4_hc));
  LED led_166 (.in(showcase_4_hd));
  LED led_167 (.in(showcase_4_hd));
  LED led_168 (.in(showcase_4_hd));
  LED led_169 (.in(showcase_5_da));
  LED led_170 (.in(showcase_5_da));
  LED led_171 (.in(showcase_5_df));
  LED led_172 (.in(showcase_5_df));
  LED led_173 (.in(showcase_5_df));
  LED led_174 (.in(showcase_5_dg));
  LED led_175 (.in(showcase_5_dg));
  LED led_176 (.in(showcase_5_de));
  LED led_177 (.in(showcase_5_de));
  LED led_178 (.in(showcase_5_de));
  LED led_179 (.in(showcase_5_dd));
  LED led_180 (.in(showcase_5_dd));
  LED led_181 (.in(showcase_6_da));
  LED led_182 (.in(showcase_6_da));
  LED led_183 (.in(showcase_6_df));
  LED led_184 (.in(showcase_6_df));
  LED led_185 (.in(showcase_6_df));
  LED led_186 (.in(showcase_6_dg));
  LED led_187 (.in(showcase_6_dg));
  LED led_188 (.in(showcase_6_de));
  LED led_189 (.in(showcase_6_de));
  LED led_190 (.in(showcase_6_de));
  LED led_191 (.in(showcase_6_dd));
  LED led_192 (.in(showcase_6_dd));
  LED led_193 (.in(showcase_7_da));
  LED led_194 (.in(showcase_7_da));
  LED led_195 (.in(showcase_7_df));
  LED led_196 (.in(showcase_7_df));
  LED led_197 (.in(showcase_7_df));
  LED led_198 (.in(showcase_7_dg));
  LED led_199 (.in(showcase_7_dg));
  LED led_200 (.in(showcase_7_de));
  LED led_201 (.in(showcase_7_de));
  LED led_202 (.in(showcase_7_de));
  LED led_203 (.in(showcase_7_dd));
  LED led_204 (.in(showcase_7_dd));
  LED led_205 (.in(showcase_8_da));
  LED led_206 (.in(showcase_8_da));
  LED led_207 (.in(showcase_8_df));
  LED led_208 (.in(showcase_8_df));
  LED led_209 (.in(showcase_8_df));
  LED led_210 (.in(showcase_8_dg));
  LED led_211 (.in(showcase_8_dg));
  LED led_212 (.in(showcase_8_de));
  LED led_213 (.in(showcase_8_de));
  LED led_214 (.in(showcase_8_de));
  LED led_215 (.in(showcase_8_dd));
  LED led_216 (.in(showcase_8_dd));
  LED led_217 (.in(showcase_5_da));
  Hex_Digit_Display hex_digit_display_5 (.value(4'b0001));  // open: dp
  LED led_218 (.in(showcase_5_db));
  LED led_219 (.in(showcase_5_db));
  SHOWCASE showcase_5 (
    .Da(showcase_5_da), .Db(showcase_5_db), .Dg(showcase_5_dg), .Df(showcase_5_df), .De(showcase_5_de),
    .Dc(showcase_5_dc), .Dd(showcase_5_dd), .n(4'b0001), .Ha(showcase_5_ha), .Hf(showcase_5_hf),
    .Hg(showcase_5_hg), .Hb(showcase_5_hb), .Hc(showcase_5_hc), .He(showcase_5_he), .Hd(showcase_5_hd));
  LED led_220 (.in(showcase_5_db));
  LED led_221 (.in(showcase_5_dg));
  LED led_222 (.in(showcase_5_dc));
  LED led_223 (.in(showcase_5_dc));
  LED led_224 (.in(showcase_5_dc));
  LED led_225 (.in(showcase_5_dd));
  LED led_226 (.in(showcase_6_da));
  Hex_Digit_Display hex_digit_display_6 (.value(4'b0101));  // open: dp
  LED led_227 (.in(showcase_6_db));
  LED led_228 (.in(showcase_6_db));
  SHOWCASE showcase_6 (
    .Da(showcase_6_da), .Db(showcase_6_db), .Dg(showcase_6_dg), .Df(showcase_6_df), .De(showcase_6_de),
    .Dc(showcase_6_dc), .Dd(showcase_6_dd), .n(4'b0101), .Ha(showcase_6_ha), .Hf(showcase_6_hf),
    .Hg(showcase_6_hg), .Hb(showcase_6_hb), .Hc(showcase_6_hc), .He(showcase_6_he), .Hd(showcase_6_hd));
  LED led_229 (.in(showcase_6_db));
  LED led_230 (.in(showcase_6_dg));
  LED led_231 (.in(showcase_6_dc));
  LED led_232 (.in(showcase_6_dc));
  LED led_233 (.in(showcase_6_dc));
  LED led_234 (.in(showcase_6_dd));
  LED led_235 (.in(showcase_7_da));
  Hex_Digit_Display hex_digit_display_7 (.value(4'b1001));  // open: dp
  LED led_236 (.in(showcase_7_db));
  LED led_237 (.in(showcase_7_db));
  SHOWCASE showcase_7 (
    .Da(showcase_7_da), .Db(showcase_7_db), .Dg(showcase_7_dg), .Df(showcase_7_df), .De(showcase_7_de),
    .Dc(showcase_7_dc), .Dd(showcase_7_dd), .n(4'b1001), .Ha(showcase_7_ha), .Hf(showcase_7_hf),
    .Hg(showcase_7_hg), .Hb(showcase_7_hb), .Hc(showcase_7_hc), .He(showcase_7_he), .Hd(showcase_7_hd));
  LED led_238 (.in(showcase_7_db));
  LED led_239 (.in(showcase_7_dg));
  LED led_240 (.in(showcase_7_dc));
  LED led_241 (.in(showcase_7_dc));
  LED led_242 (.in(showcase_7_dc));
  LED led_243 (.in(showcase_7_dd));
  LED led_244 (.in(showcase_8_da));
  Hex_Digit_Display hex_digit_display_8 (.value(4'b1101));  // open: dp
  LED led_245 (.in(showcase_8_db));
  LED led_246 (.in(showcase_8_db));
  SHOWCASE showcase_8 (
    .Da(showcase_8_da), .Db(showcase_8_db), .Dg(showcase_8_dg), .Df(showcase_8_df), .De(showcase_8_de),
    .Dc(showcase_8_dc), .Dd(showcase_8_dd), .n(4'b1101), .Ha(showcase_8_ha), .Hf(showcase_8_hf),
    .Hg(showcase_8_hg), .Hb(showcase_8_hb), .Hc(showcase_8_hc), .He(showcase_8_he), .Hd(showcase_8_hd));
  LED led_247 (.in(showcase_8_db));
  LED led_248 (.in(showcase_8_dg));
  LED led_249 (.in(showcase_8_dc));
  LED led_250 (.in(showcase_8_dc));
  LED led_251 (.in(showcase_8_dc));
  LED led_252 (.in(showcase_8_dd));
  LED led_253 (.in(showcase_5_ha));
  LED led_254 (.in(showcase_5_ha));
  LED led_255 (.in(showcase_5_ha));
  LED led_256 (.in(showcase_5_hf));
  LED led_257 (.in(showcase_5_hf));
  LED led_258 (.in(showcase_5_hf));
  LED led_259 (.in(showcase_5_hg));
  LED led_260 (.in(showcase_5_hg));
  LED led_261 (.in(showcase_5_hg));
  LED led_262 (.in(showcase_5_he));
  LED led_263 (.in(showcase_5_he));
  LED led_264 (.in(showcase_5_he));
  LED led_265 (.in(showcase_5_hd));
  LED led_266 (.in(showcase_5_hd));
  LED led_267 (.in(showcase_5_hd));
  LED led_268 (.in(showcase_6_ha));
  LED led_269 (.in(showcase_6_ha));
  LED led_270 (.in(showcase_6_ha));
  LED led_271 (.in(showcase_6_hf));
  LED led_272 (.in(showcase_6_hf));
  LED led_273 (.in(showcase_6_hf));
  LED led_274 (.in(showcase_6_hg));
  LED led_275 (.in(showcase_6_hg));
  LED led_276 (.in(showcase_6_hg));
  LED led_277 (.in(showcase_6_he));
  LED led_278 (.in(showcase_6_he));
  LED led_279 (.in(showcase_6_he));
  LED led_280 (.in(showcase_6_hd));
  LED led_281 (.in(showcase_6_hd));
  LED led_282 (.in(showcase_6_hd));
  LED led_283 (.in(showcase_7_ha));
  LED led_284 (.in(showcase_7_ha));
  LED led_285 (.in(showcase_7_ha));
  LED led_286 (.in(showcase_7_hf));
  LED led_287 (.in(showcase_7_hf));
  LED led_288 (.in(showcase_7_hf));
  LED led_289 (.in(showcase_7_hg));
  LED led_290 (.in(showcase_7_hg));
  LED led_291 (.in(showcase_7_hg));
  LED led_292 (.in(showcase_7_he));
  LED led_293 (.in(showcase_7_he));
  LED led_294 (.in(showcase_7_he));
  LED led_295 (.in(showcase_7_hd));
  LED led_296 (.in(showcase_7_hd));
  LED led_297 (.in(showcase_7_hd));
  LED led_298 (.in(showcase_8_ha));
  LED led_299 (.in(showcase_8_ha));
  LED led_300 (.in(showcase_8_ha));
  LED led_301 (.in(showcase_8_hf));
  LED led_302 (.in(showcase_8_hf));
  LED led_303 (.in(showcase_8_hf));
  LED led_304 (.in(showcase_8_hg));
  LED led_305 (.in(showcase_8_hg));
  LED led_306 (.in(showcase_8_hg));
  LED led_307 (.in(showcase_8_he));
  LED led_308 (.in(showcase_8_he));
  LED led_309 (.in(showcase_8_he));
  LED led_310 (.in(showcase_8_hd));
  LED led_311 (.in(showcase_8_hd));
  LED led_312 (.in(showcase_8_hd));
  LED led_313 (.in(showcase_9_da));
  LED led_314 (.in(showcase_5_hb));
  LED led_315 (.in(showcase_9_df));
  LED led_316 (.in(showcase_5_hb));
  LED led_317 (.in(showcase_9_df));
  LED led_318 (.in(showcase_5_hb));
  LED led_319 (.in(showcase_9_df));
  LED led_320 (.in(showcase_9_dg));
  LED led_321 (.in(showcase_5_hc));
  LED led_322 (.in(showcase_9_de));
  LED led_323 (.in(showcase_5_hc));
  LED led_324 (.in(showcase_9_de));
  LED led_325 (.in(showcase_5_hc));
  LED led_326 (.in(showcase_9_de));
  LED led_327 (.in(showcase_9_dd));
  LED led_328 (.in(showcase_10_da));
  LED led_329 (.in(showcase_6_hb));
  LED led_330 (.in(showcase_10_df));
  LED led_331 (.in(showcase_6_hb));
  LED led_332 (.in(showcase_10_df));
  LED led_333 (.in(showcase_6_hb));
  LED led_334 (.in(showcase_10_df));
  LED led_335 (.in(showcase_10_dg));
  LED led_336 (.in(showcase_6_hc));
  LED led_337 (.in(showcase_10_de));
  LED led_338 (.in(showcase_6_hc));
  LED led_339 (.in(showcase_10_de));
  LED led_340 (.in(showcase_6_hc));
  LED led_341 (.in(showcase_10_de));
  LED led_342 (.in(showcase_10_dd));
  LED led_343 (.in(showcase_11_da));
  LED led_344 (.in(showcase_7_hb));
  LED led_345 (.in(showcase_11_df));
  LED led_346 (.in(showcase_7_hb));
  LED led_347 (.in(showcase_11_df));
  LED led_348 (.in(showcase_7_hb));
  LED led_349 (.in(showcase_11_df));
  LED led_350 (.in(showcase_11_dg));
  LED led_351 (.in(showcase_7_hc));
  LED led_352 (.in(showcase_11_de));
  LED led_353 (.in(showcase_7_hc));
  LED led_354 (.in(showcase_11_de));
  LED led_355 (.in(showcase_7_hc));
  LED led_356 (.in(showcase_11_de));
  LED led_357 (.in(showcase_11_dd));
  LED led_358 (.in(showcase_12_da));
  LED led_359 (.in(showcase_8_hb));
  LED led_360 (.in(showcase_12_df));
  LED led_361 (.in(showcase_8_hb));
  LED led_362 (.in(showcase_12_df));
  LED led_363 (.in(showcase_8_hb));
  LED led_364 (.in(showcase_12_df));
  LED led_365 (.in(showcase_12_dg));
  LED led_366 (.in(showcase_8_hc));
  LED led_367 (.in(showcase_12_de));
  LED led_368 (.in(showcase_8_hc));
  LED led_369 (.in(showcase_12_de));
  LED led_370 (.in(showcase_8_hc));
  LED led_371 (.in(showcase_12_de));
  LED led_372 (.in(showcase_12_dd));
  LED led_373 (.in(showcase_9_da));
  LED led_374 (.in(showcase_9_da));
  Hex_Digit_Display hex_digit_display_9 (.value(4'b0010));  // open: dp
  LED led_375 (.in(showcase_9_db));
  LED led_376 (.in(showcase_9_db));
  LED led_377 (.in(showcase_9_db));
  LED led_378 (.in(showcase_9_dg));
  LED led_379 (.in(showcase_9_dg));
  LED led_380 (.in(showcase_9_dc));
  LED led_381 (.in(showcase_9_dc));
  LED led_382 (.in(showcase_9_dc));
  LED led_383 (.in(showcase_9_dd));
  LED led_384 (.in(showcase_9_dd));
  LED led_385 (.in(showcase_10_da));
  LED led_386 (.in(showcase_10_da));
  Hex_Digit_Display hex_digit_display_10 (.value(4'b0110));  // open: dp
  LED led_387 (.in(showcase_10_db));
  LED led_388 (.in(showcase_10_db));
  LED led_389 (.in(showcase_10_db));
  LED led_390 (.in(showcase_10_dg));
  LED led_391 (.in(showcase_10_dg));
  LED led_392 (.in(showcase_10_dc));
  LED led_393 (.in(showcase_10_dc));
  LED led_394 (.in(showcase_10_dc));
  LED led_395 (.in(showcase_10_dd));
  LED led_396 (.in(showcase_10_dd));
  LED led_397 (.in(showcase_11_da));
  LED led_398 (.in(showcase_11_da));
  Hex_Digit_Display hex_digit_display_11 (.value(4'b1010));  // open: dp
  LED led_399 (.in(showcase_11_db));
  LED led_400 (.in(showcase_11_db));
  LED led_401 (.in(showcase_11_db));
  LED led_402 (.in(showcase_11_dg));
  LED led_403 (.in(showcase_11_dg));
  LED led_404 (.in(showcase_11_dc));
  LED led_405 (.in(showcase_11_dc));
  LED led_406 (.in(showcase_11_dc));
  LED led_407 (.in(showcase_11_dd));
  LED led_408 (.in(showcase_11_dd));
  LED led_409 (.in(showcase_12_da));
  LED led_410 (.in(showcase_12_da));
  Hex_Digit_Display hex_digit_display_12 (.value(4'b1110));  // open: dp
  LED led_411 (.in(showcase_12_db));
  LED led_412 (.in(showcase_12_db));
  LED led_413 (.in(showcase_12_db));
  LED led_414 (.in(showcase_12_dg));
  LED led_415 (.in(showcase_12_dg));
  LED led_416 (.in(showcase_12_dc));
  LED led_417 (.in(showcase_12_dc));
  LED led_418 (.in(showcase_12_dc));
  LED led_419 (.in(showcase_12_dd));
  LED led_420 (.in(showcase_12_dd));
  LED led_421 (.in(showcase_9_ha));
  LED led_422 (.in(showcase_9_ha));
  LED led_423 (.in(showcase_9_ha));
  LED led_424 (.in(showcase_9_hf));
  LED led_425 (.in(showcase_9_hf));
  SHOWCASE showcase_9 (
    .Da(showcase_9_da), .Db(showcase_9_db), .Dg(showcase_9_dg), .Df(showcase_9_df), .De(showcase_9_de),
    .Dc(showcase_9_dc), .Dd(showcase_9_dd), .n(4'b0010), .Ha(showcase_9_ha), .Hf(showcase_9_hf),
    .Hg(showcase_9_hg), .Hb(showcase_9_hb), .Hc(showcase_9_hc), .He(showcase_9_he), .Hd(showcase_9_hd));
  LED led_426 (.in(showcase_9_hf));
  LED led_427 (.in(showcase_9_hg));
  LED led_428 (.in(showcase_9_hg));
  LED led_429 (.in(showcase_9_hg));
  LED led_430 (.in(showcase_9_he));
  LED led_431 (.in(showcase_9_he));
  LED led_432 (.in(showcase_9_he));
  LED led_433 (.in(showcase_9_hd));
  LED led_434 (.in(showcase_9_hd));
  LED led_435 (.in(showcase_9_hd));
  LED led_436 (.in(showcase_10_ha));
  LED led_437 (.in(showcase_10_ha));
  LED led_438 (.in(showcase_10_ha));
  LED led_439 (.in(showcase_10_hf));
  LED led_440 (.in(showcase_10_hf));
  SHOWCASE showcase_10 (
    .Da(showcase_10_da), .Db(showcase_10_db), .Dg(showcase_10_dg), .Df(showcase_10_df), .De(showcase_10_de),
    .Dc(showcase_10_dc), .Dd(showcase_10_dd), .n(4'b0110), .Ha(showcase_10_ha), .Hf(showcase_10_hf),
    .Hg(showcase_10_hg), .Hb(showcase_10_hb), .Hc(showcase_10_hc), .He(showcase_10_he), .Hd(showcase_10_hd));
  LED led_441 (.in(showcase_10_hf));
  LED led_442 (.in(showcase_10_hg));
  LED led_443 (.in(showcase_10_hg));
  LED led_444 (.in(showcase_10_hg));
  LED led_445 (.in(showcase_10_he));
  LED led_446 (.in(showcase_10_he));
  LED led_447 (.in(showcase_10_he));
  LED led_448 (.in(showcase_10_hd));
  LED led_449 (.in(showcase_10_hd));
  LED led_450 (.in(showcase_10_hd));
  LED led_451 (.in(showcase_11_ha));
  LED led_452 (.in(showcase_11_ha));
  LED led_453 (.in(showcase_11_ha));
  LED led_454 (.in(showcase_11_hf));
  LED led_455 (.in(showcase_11_hf));
  SHOWCASE showcase_11 (
    .Da(showcase_11_da), .Db(showcase_11_db), .Dg(showcase_11_dg), .Df(showcase_11_df), .De(showcase_11_de),
    .Dc(showcase_11_dc), .Dd(showcase_11_dd), .n(4'b1010), .Ha(showcase_11_ha), .Hf(showcase_11_hf),
    .Hg(showcase_11_hg), .Hb(showcase_11_hb), .Hc(showcase_11_hc), .He(showcase_11_he), .Hd(showcase_11_hd));
  LED led_456 (.in(showcase_11_hf));
  LED led_457 (.in(showcase_11_hg));
  LED led_458 (.in(showcase_11_hg));
  LED led_459 (.in(showcase_11_hg));
  LED led_460 (.in(showcase_11_he));
  LED led_461 (.in(showcase_11_he));
  LED led_462 (.in(showcase_11_he));
  LED led_463 (.in(showcase_11_hd));
  LED led_464 (.in(showcase_11_hd));
  LED led_465 (.in(showcase_11_hd));
  LED led_466 (.in(showcase_12_ha));
  LED led_467 (.in(showcase_12_ha));
  LED led_468 (.in(showcase_12_ha));
  LED led_469 (.in(showcase_12_hf));
  LED led_470 (.in(showcase_12_hf));
  SHOWCASE showcase_12 (
    .Da(showcase_12_da), .Db(showcase_12_db), .Dg(showcase_12_dg), .Df(showcase_12_df), .De(showcase_12_de),
    .Dc(showcase_12_dc), .Dd(showcase_12_dd), .n(4'b1110), .Ha(showcase_12_ha), .Hf(showcase_12_hf),
    .Hg(showcase_12_hg), .Hb(showcase_12_hb), .Hc(showcase_12_hc), .He(showcase_12_he), .Hd(showcase_12_hd));
  LED led_471 (.in(showcase_12_hf));
  LED led_472 (.in(showcase_12_hg));
  LED led_473 (.in(showcase_12_hg));
  LED led_474 (.in(showcase_12_hg));
  LED led_475 (.in(showcase_12_he));
  LED led_476 (.in(showcase_12_he));
  LED led_477 (.in(showcase_12_he));
  LED led_478 (.in(showcase_12_hd));
  LED led_479 (.in(showcase_12_hd));
  LED led_480 (.in(showcase_12_hd));
  LED led_481 (.in(showcase_13_da));
  LED led_482 (.in(showcase_9_hb));
  LED led_483 (.in(showcase_13_df));
  LED led_484 (.in(showcase_9_hb));
  LED led_485 (.in(showcase_13_df));
  LED led_486 (.in(showcase_9_hb));
  LED led_487 (.in(showcase_13_df));
  LED led_488 (.in(showcase_13_dg));
  LED led_489 (.in(showcase_9_hc));
  LED led_490 (.in(showcase_13_de));
  LED led_491 (.in(showcase_9_hc));
  LED led_492 (.in(showcase_13_de));
  LED led_493 (.in(showcase_9_hc));
  LED led_494 (.in(showcase_13_de));
  LED led_495 (.in(showcase_13_dd));
  LED led_496 (.in(showcase_14_da));
  LED led_497 (.in(showcase_10_hb));
  LED led_498 (.in(showcase_14_df));
  LED led_499 (.in(showcase_10_hb));
  LED led_500 (.in(showcase_14_df));
  LED led_501 (.in(showcase_10_hb));
  LED led_502 (.in(showcase_14_df));
  LED led_503 (.in(showcase_14_dg));
  LED led_504 (.in(showcase_10_hc));
  LED led_505 (.in(showcase_14_de));
  LED led_506 (.in(showcase_10_hc));
  LED led_507 (.in(showcase_14_de));
  LED led_508 (.in(showcase_10_hc));
  LED led_509 (.in(showcase_14_de));
  LED led_510 (.in(showcase_14_dd));
  LED led_511 (.in(showcase_15_da));
  LED led_512 (.in(showcase_11_hb));
  LED led_513 (.in(showcase_15_df));
  LED led_514 (.in(showcase_11_hb));
  LED led_515 (.in(showcase_15_df));
  LED led_516 (.in(showcase_11_hb));
  LED led_517 (.in(showcase_15_df));
  LED led_518 (.in(showcase_15_dg));
  LED led_519 (.in(showcase_11_hc));
  LED led_520 (.in(showcase_15_de));
  LED led_521 (.in(showcase_11_hc));
  LED led_522 (.in(showcase_15_de));
  LED led_523 (.in(showcase_11_hc));
  LED led_524 (.in(showcase_15_de));
  LED led_525 (.in(showcase_15_dd));
  LED led_526 (.in(showcase_16_da));
  LED led_527 (.in(showcase_12_hb));
  LED led_528 (.in(showcase_16_df));
  LED led_529 (.in(showcase_12_hb));
  LED led_530 (.in(showcase_16_df));
  LED led_531 (.in(showcase_12_hb));
  LED led_532 (.in(showcase_16_df));
  LED led_533 (.in(showcase_16_dg));
  LED led_534 (.in(showcase_12_hc));
  LED led_535 (.in(showcase_16_de));
  LED led_536 (.in(showcase_12_hc));
  LED led_537 (.in(showcase_16_de));
  LED led_538 (.in(showcase_12_hc));
  LED led_539 (.in(showcase_16_de));
  LED led_540 (.in(showcase_16_dd));
  LED led_541 (.in(showcase_13_da));
  LED led_542 (.in(showcase_13_da));
  Hex_Digit_Display hex_digit_display_13 (.value(4'b0011));  // open: dp
  LED led_543 (.in(showcase_13_db));
  LED led_544 (.in(showcase_13_db));
  LED led_545 (.in(showcase_13_db));
  LED led_546 (.in(showcase_13_dg));
  LED led_547 (.in(showcase_13_dg));
  LED led_548 (.in(showcase_13_dc));
  LED led_549 (.in(showcase_13_dc));
  LED led_550 (.in(showcase_13_dc));
  LED led_551 (.in(showcase_13_dd));
  LED led_552 (.in(showcase_13_dd));
  LED led_553 (.in(showcase_14_da));
  LED led_554 (.in(showcase_14_da));
  Hex_Digit_Display hex_digit_display_14 (.value(4'b0111));  // open: dp
  LED led_555 (.in(showcase_14_db));
  LED led_556 (.in(showcase_14_db));
  LED led_557 (.in(showcase_14_db));
  LED led_558 (.in(showcase_14_dg));
  LED led_559 (.in(showcase_14_dg));
  LED led_560 (.in(showcase_14_dc));
  LED led_561 (.in(showcase_14_dc));
  LED led_562 (.in(showcase_14_dc));
  LED led_563 (.in(showcase_14_dd));
  LED led_564 (.in(showcase_14_dd));
  LED led_565 (.in(showcase_15_da));
  LED led_566 (.in(showcase_15_da));
  Hex_Digit_Display hex_digit_display_15 (.value(4'b1011));  // open: dp
  LED led_567 (.in(showcase_15_db));
  LED led_568 (.in(showcase_15_db));
  LED led_569 (.in(showcase_15_db));
  LED led_570 (.in(showcase_15_dg));
  LED led_571 (.in(showcase_15_dg));
  LED led_572 (.in(showcase_15_dc));
  LED led_573 (.in(showcase_15_dc));
  LED led_574 (.in(showcase_15_dc));
  LED led_575 (.in(showcase_15_dd));
  LED led_576 (.in(showcase_15_dd));
  LED led_577 (.in(showcase_16_da));
  LED led_578 (.in(showcase_16_da));
  Hex_Digit_Display hex_digit_display_16 (.value(4'b1111));  // open: dp
  LED led_579 (.in(showcase_16_db));
  LED led_580 (.in(showcase_16_db));
  LED led_581 (.in(showcase_16_db));
  LED led_582 (.in(showcase_16_dg));
  LED led_583 (.in(showcase_16_dg));
  LED led_584 (.in(showcase_16_dc));
  LED led_585 (.in(showcase_16_dc));
  LED led_586 (.in(showcase_16_dc));
  LED led_587 (.in(showcase_16_dd));
  LED led_588 (.in(showcase_16_dd));
  LED led_589 (.in(showcase_13_ha));
  LED led_590 (.in(showcase_13_ha));
  LED led_591 (.in(showcase_13_hf));
  LED led_592 (.in(showcase_13_hf));
  SHOWCASE showcase_13 (
    .Da(showcase_13_da), .Db(showcase_13_db), .Dg(showcase_13_dg), .Df(showcase_13_df), .De(showcase_13_de),
    .Dc(showcase_13_dc), .Dd(showcase_13_dd), .n(4'b0011), .Ha(showcase_13_ha), .Hf(showcase_13_hf),
    .Hg(showcase_13_hg), .Hb(showcase_13_hb), .Hc(showcase_13_hc), .He(showcase_13_he), .Hd(showcase_13_hd));
  LED led_593 (.in(showcase_13_hf));
  LED led_594 (.in(showcase_13_hg));
  LED led_595 (.in(showcase_13_hg));
  LED led_596 (.in(showcase_13_he));
  LED led_597 (.in(showcase_13_he));
  LED led_598 (.in(showcase_13_he));
  LED led_599 (.in(showcase_13_hd));
  LED led_600 (.in(showcase_13_hd));
  LED led_601 (.in(showcase_14_ha));
  LED led_602 (.in(showcase_14_ha));
  LED led_603 (.in(showcase_14_hf));
  LED led_604 (.in(showcase_14_hf));
  SHOWCASE showcase_14 (
    .Da(showcase_14_da), .Db(showcase_14_db), .Dg(showcase_14_dg), .Df(showcase_14_df), .De(showcase_14_de),
    .Dc(showcase_14_dc), .Dd(showcase_14_dd), .n(4'b0111), .Ha(showcase_14_ha), .Hf(showcase_14_hf),
    .Hg(showcase_14_hg), .Hb(showcase_14_hb), .Hc(showcase_14_hc), .He(showcase_14_he), .Hd(showcase_14_hd));
  LED led_605 (.in(showcase_14_hf));
  LED led_606 (.in(showcase_14_hg));
  LED led_607 (.in(showcase_14_hg));
  LED led_608 (.in(showcase_14_he));
  LED led_609 (.in(showcase_14_he));
  LED led_610 (.in(showcase_14_he));
  LED led_611 (.in(showcase_14_hd));
  LED led_612 (.in(showcase_14_hd));
  LED led_613 (.in(showcase_15_ha));
  LED led_614 (.in(showcase_15_ha));
  LED led_615 (.in(showcase_15_hf));
  LED led_616 (.in(showcase_15_hf));
  SHOWCASE showcase_15 (
    .Da(showcase_15_da), .Db(showcase_15_db), .Dg(showcase_15_dg), .Df(showcase_15_df), .De(showcase_15_de),
    .Dc(showcase_15_dc), .Dd(showcase_15_dd), .n(4'b1011), .Ha(showcase_15_ha), .Hf(showcase_15_hf),
    .Hg(showcase_15_hg), .Hb(showcase_15_hb), .Hc(showcase_15_hc), .He(showcase_15_he), .Hd(showcase_15_hd));
  LED led_617 (.in(showcase_15_hf));
  LED led_618 (.in(showcase_15_hg));
  LED led_619 (.in(showcase_15_hg));
  LED led_620 (.in(showcase_15_he));
  LED led_621 (.in(showcase_15_he));
  LED led_622 (.in(showcase_15_he));
  LED led_623 (.in(showcase_15_hd));
  LED led_624 (.in(showcase_15_hd));
  LED led_625 (.in(showcase_16_ha));
  LED led_626 (.in(showcase_16_ha));
  LED led_627 (.in(showcase_16_hf));
  LED led_628 (.in(showcase_16_hf));
  SHOWCASE showcase_16 (
    .Da(showcase_16_da), .Db(showcase_16_db), .Dg(showcase_16_dg), .Df(showcase_16_df), .De(showcase_16_de),
    .Dc(showcase_16_dc), .Dd(showcase_16_dd), .n(4'b1111), .Ha(showcase_16_ha), .Hf(showcase_16_hf),
    .Hg(showcase_16_hg), .Hb(showcase_16_hb), .Hc(showcase_16_hc), .He(showcase_16_he), .Hd(showcase_16_hd));
  LED led_629 (.in(showcase_16_hf));
  LED led_630 (.in(showcase_16_hg));
  LED led_631 (.in(showcase_16_hg));
  LED led_632 (.in(showcase_16_he));
  LED led_633 (.in(showcase_16_he));
  LED led_634 (.in(showcase_16_he));
  LED led_635 (.in(showcase_16_hd));
  LED led_636 (.in(showcase_16_hd));
  LED led_637 (.in(showcase_13_ha));
  LED led_638 (.in(showcase_13_hb));
  LED led_639 (.in(showcase_13_hb));
  LED led_640 (.in(showcase_13_hb));
  LED led_641 (.in(showcase_13_hg));
  LED led_642 (.in(showcase_13_hc));
  LED led_643 (.in(showcase_13_hc));
  LED led_644 (.in(showcase_13_hc));
  LED led_645 (.in(showcase_13_hd));
  LED led_646 (.in(showcase_14_ha));
  LED led_647 (.in(showcase_14_hb));
  LED led_648 (.in(showcase_14_hb));
  LED led_649 (.in(showcase_14_hb));
  LED led_650 (.in(showcase_14_hg));
  LED led_651 (.in(showcase_14_hc));
  LED led_652 (.in(showcase_14_hc));
  LED led_653 (.in(showcase_14_hc));
  LED led_654 (.in(showcase_14_hd));
  LED led_655 (.in(showcase_15_ha));
  LED led_656 (.in(showcase_15_hb));
  LED led_657 (.in(showcase_15_hb));
  LED led_658 (.in(showcase_15_hb));
  LED led_659 (.in(showcase_15_hg));
  LED led_660 (.in(showcase_15_hc));
  LED led_661 (.in(showcase_15_hc));
  LED led_662 (.in(showcase_15_hc));
  LED led_663 (.in(showcase_15_hd));
  LED led_664 (.in(showcase_16_ha));
  LED led_665 (.in(showcase_16_hb));
  LED led_666 (.in(showcase_16_hb));
  LED led_667 (.in(showcase_16_hb));
  LED led_668 (.in(showcase_16_hg));
  LED led_669 (.in(showcase_16_hc));
  LED led_670 (.in(showcase_16_hc));
  LED led_671 (.in(showcase_16_hc));
  LED led_672 (.in(showcase_16_hd));
endmodule

module DEC (
  input  [3:0] n,
  output a,
  output f,
  output g,
  output b,
  output c,
  output e,
  output d
);

  wire and_1_out, or_1_out, or_2_out, or_3_out, or_5_out, or_6_out, or_7_out, xor_1_out, xor_2_out;

  xor xor_1 (xor_1_out, n[0], n[1]);
  or or_1 (or_1_out, n[2], n[3]);
  or or_2 (or_2_out, or_1_out, n[1]);
  and and_1 (and_1_out, n[2], n[1], n[0]);
  or or_3 (or_3_out, n[1], n[0]);
  and and_2 (g, or_2_out, ~and_1_out);  // AND_Gate
  or or_4 (f, or_1_out, ~or_3_out);  // OR_Gate
  or or_5 (or_5_out, ~n[2], n[1]);  // OR_Gate
  and and_3 (e, ~n[0], or_5_out);  // AND_Gate
  or or_6 (or_6_out, or_1_out, n[1], ~n[0]);  // OR_Gate
  or or_7 (or_7_out, xor_1_out, ~n[2]);  // OR_Gate
  and and_4 (d, or_6_out, or_7_out);
  or or_8 (c, n[2], ~n[1], n[0]);  // OR_Gate
  nand nand_1 (b, xor_1_out, n[2]);
  xor xor_2 (xor_2_out, n[2], n[0]);
  or or_9 (a, n[3], ~xor_2_out, n[1]);  // OR_Gate

  // Notes on the sheet:
  //   𝛼
  //   𝛽
  //   g
  //   f
  //   e
  //   d
  //   c
  //   b
  //   a
endmodule

module HEX (
  input  [3:0] n,
  output a,
  output f,
  output g,
  output b,
  output c,
  output e,
  output d
);

  wire and_1_out, and_2_out, and_3_out, and_4_out, and_5_out, and_6_out, and_7_out, and_8_out, and_9_out,
       and_10_out, and_11_out, and_12_out, and_13_out, and_14_out, and_15_out, nor_1_out, or_1_out, or_2_out,
       or_4_out, or_6_out, or_8_out, or_10_out, or_13_out, or_14_out, or_15_out, xor_1_out, xor_2_out,
       xor_3_out, xor_4_out;

  xor xor_1 (xor_1_out, n[1], n[3]);
  or or_1 (or_1_out, n[1], ~n[2]);  // OR_Gate
  nor nor_1 (nor_1_out, n[0], n[3]);
  xor xor_2 (xor_2_out, n[2], n[3]);
  and and_1 (and_1_out, n[0], n[2]);
  and and_2 (and_2_out, ~and_1_out, n[1]);  // AND_Gate
  or or_2 (or_2_out, ~n[2], n[0]);  // OR_Gate
  and and_3 (and_3_out, ~n[3], n[2], ~n[1]);  // AND_Gate
  and and_4 (and_4_out, or_2_out, n[3]);
  or or_3 (g, and_2_out, and_4_out, and_3_out);
  and and_5 (and_5_out, n[3], n[1]);
  or or_4 (or_4_out, n[1], n[0]);
  or or_5 (f, and_5_out, xor_2_out, ~or_4_out);  // OR_Gate
  or or_6 (or_6_out, n[2], n[1]);
  and and_6 (and_6_out, or_1_out, ~n[0]);  // AND_Gate
  and and_7 (and_7_out, or_6_out, n[3]);
  or or_7 (e, and_6_out, and_7_out);
  or or_8 (or_8_out, and_1_out, n[3]);
  and and_8 (and_8_out, or_8_out, ~n[1]);  // AND_Gate
  and and_9 (and_9_out, nor_1_out, ~n[2]);  // AND_Gate
  xor xor_3 (xor_3_out, n[2], n[0]);
  and and_10 (and_10_out, n[1], xor_3_out);
  or or_9 (d, and_8_out, and_9_out, and_10_out);
  or or_10 (or_10_out, ~n[1], n[0]);  // OR_Gate
  and and_11 (and_11_out, ~n[1], n[0]);  // AND_Gate
  and and_12 (and_12_out, or_10_out, ~n[2]);  // AND_Gate
  or or_11 (c, and_12_out, xor_2_out, and_11_out);
  and and_13 (and_13_out, nor_1_out, ~n[1]);  // AND_Gate
  and and_14 (and_14_out, xor_1_out, n[0]);
  or or_12 (b, and_13_out, and_14_out, ~or_13_out);  // OR_Gate
  and and_15 (and_15_out, n[3], n[1], n[0]);
  or or_13 (or_13_out, n[2], and_15_out);
  or or_14 (or_14_out, xor_1_out, n[2], ~n[0]);  // OR_Gate
  xor xor_4 (xor_4_out, n[3], n[0]);
  or or_15 (or_15_out, or_1_out, xor_4_out);
  and and_16 (a, or_15_out, or_14_out);

  // Notes on the sheet:
  //   𝛼
  //   𝛽
  //   𝛾
  //   𝛿
  //   𝜀
  //   g
  //   f
  //   e
  //   d
  //   c
  //   b
  //   a
endmodule

module SHOWCASE (
  input  [3:0] n,
  output Ha,
  output Da,
  output Hf,
  output Db,
  output Hg,
  output Dg,
  output Hb,
  output Df,
  output Hc,
  output De,
  output He,
  output Dc,
  output Hd,
  output Dd
);

  DEC dec_1 (.n(n), .a(Da), .f(Df), .g(Dg), .b(Db), .c(Dc), .e(De), .d(Dd));
  HEX hex_1 (.n(n), .a(Ha), .f(Hf), .g(Hg), .b(Hb), .c(Hc), .e(He), .d(Hd));
endmodule

module LEDS (
  input  a,
  input  b,
  input  c,
  input  d,
  input  e,
  input  f,
  input  g,
  output out_8,
  output out_9,
  output out_10,
  output out_11,
  output out_12,
  output out_13,
  output out_14
);

  wire undriven, undriven_2, undriven_3, undriven_4, undriven_5, undriven_6, undriven_7;

  LED led_1 (.in(f));
  LED led_2 (.in(f));
  LED led_3 (.in(f));
  LED led_4 (.in(e));
  LED led_5 (.in(e));
  LED led_6 (.in(e));
  LED led_7 (.in(a));
  LED led_8 (.in(a));
  LED led_9 (.in(a));
  LED led_10 (.in(b));
  LED led_11 (.in(b));
  LED led_12 (.in(b));
  LED led_13 (.in(g));
  LED led_14 (.in(g));
  LED led_15 (.in(g));
  LED led_16 (.in(c));
  LED led_17 (.in(c));
  LED led_18 (.in(c));
  LED led_19 (.in(d));
  LED led_20 (.in(d));
  LED led_21 (.in(d));
  LED led_22 (.in(undriven_3));
  LED led_23 (.in(undriven));
  LED led_24 (.in(undriven));
  LED led_25 (.in(undriven));
  LED led_26 (.in(undriven_4));
  LED led_27 (.in(undriven_2));
  LED led_28 (.in(undriven_2));
  LED led_29 (.in(undriven_2));
  LED led_30 (.in(undriven_5));
  LED led_31 (.in(f));
  LED led_32 (.in(f));
  LED led_33 (.in(f));
  LED led_34 (.in(e));
  LED led_35 (.in(e));
  LED led_36 (.in(e));
  LED led_37 (.in(undriven_3));
  LED led_38 (.in(undriven_3));
  LED led_39 (.in(undriven_6));
  LED led_40 (.in(undriven_6));
  LED led_41 (.in(undriven_6));
  LED led_42 (.in(undriven_4));
  LED led_43 (.in(undriven_4));
  LED led_44 (.in(undriven_7));
  LED led_45 (.in(undriven_7));
  LED led_46 (.in(undriven_7));
  LED led_47 (.in(undriven_5));
  LED led_48 (.in(undriven_5));
  LED led_49 (.in(a));
  LED led_50 (.in(a));
  LED led_51 (.in(a));
  LED led_52 (.in(b));
  LED led_53 (.in(b));
  LED led_54 (.in(b));
  LED led_55 (.in(g));
  LED led_56 (.in(g));
  LED led_57 (.in(g));
  LED led_58 (.in(c));
  LED led_59 (.in(c));
  LED led_60 (.in(c));
  LED led_61 (.in(d));
  LED led_62 (.in(d));
  LED led_63 (.in(d));
  LED led_64 (.in(f));
  LED led_65 (.in(f));
  LED led_66 (.in(f));
  LED led_67 (.in(e));
  LED led_68 (.in(e));
  LED led_69 (.in(e));
  LED led_70 (.in(a));
  LED led_71 (.in(a));
  LED led_72 (.in(a));
  LED led_73 (.in(b));
  LED led_74 (.in(b));
  LED led_75 (.in(b));
  LED led_76 (.in(g));
  LED led_77 (.in(g));
  LED led_78 (.in(g));
  LED led_79 (.in(c));
  LED led_80 (.in(c));
  LED led_81 (.in(c));
  LED led_82 (.in(d));
  LED led_83 (.in(d));
  LED led_84 (.in(d));
  LED led_85 (.in(a));
  LED led_86 (.in(a));
  LED led_87 (.in(a));
  LED led_88 (.in(f));
  LED led_89 (.in(f));
  LED led_90 (.in(f));
  LED led_91 (.in(g));
  LED led_92 (.in(g));
  LED led_93 (.in(g));
  LED led_94 (.in(e));
  LED led_95 (.in(e));
  LED led_96 (.in(e));
  LED led_97 (.in(d));
  LED led_98 (.in(d));
  LED led_99 (.in(d));
  LED led_100 (.in(b));
  LED led_101 (.in(b));
  LED led_102 (.in(b));
  LED led_103 (.in(c));
  LED led_104 (.in(c));
  LED led_105 (.in(c));
  LED led_106 (.in(f));
  LED led_107 (.in(f));
  LED led_108 (.in(f));
  LED led_109 (.in(e));
  LED led_110 (.in(e));
  LED led_111 (.in(e));
  LED led_112 (.in(a));
  LED led_113 (.in(a));
  LED led_114 (.in(a));
  LED led_115 (.in(b));
  LED led_116 (.in(b));
  LED led_117 (.in(b));
  LED led_118 (.in(g));
  LED led_119 (.in(g));
  LED led_120 (.in(g));
  LED led_121 (.in(c));
  LED led_122 (.in(c));
  LED led_123 (.in(c));
  LED led_124 (.in(d));
  LED led_125 (.in(d));
  LED led_126 (.in(d));
  LED led_127 (.in(a));
  LED led_128 (.in(f));
  LED led_129 (.in(f));
  LED led_130 (.in(f));
  LED led_131 (.in(g));
  LED led_132 (.in(e));
  LED led_133 (.in(e));
  LED led_134 (.in(e));
  LED led_135 (.in(d));
  LED led_136 (.in(a));
  LED led_137 (.in(a));
  LED led_138 (.in(b));
  LED led_139 (.in(b));
  LED led_140 (.in(b));
  LED led_141 (.in(g));
  LED led_142 (.in(g));
  LED led_143 (.in(c));
  LED led_144 (.in(c));
  LED led_145 (.in(c));
  LED led_146 (.in(d));
  LED led_147 (.in(d));
  LED led_148 (.in(a));
  LED led_149 (.in(a));
  LED led_150 (.in(a));
  LED led_151 (.in(f));
  LED led_152 (.in(f));
  LED led_153 (.in(f));
  LED led_154 (.in(g));
  LED led_155 (.in(g));
  LED led_156 (.in(g));
  LED led_157 (.in(e));
  LED led_158 (.in(e));
  LED led_159 (.in(e));
  LED led_160 (.in(d));
  LED led_161 (.in(d));
  LED led_162 (.in(d));
  LED led_163 (.in(b));
  LED led_164 (.in(b));
  LED led_165 (.in(b));
  LED led_166 (.in(c));
  LED led_167 (.in(c));
  LED led_168 (.in(c));

  assign out_8 = a;
  assign out_9 = b;
  assign out_10 = c;
  assign out_11 = d;
  assign out_12 = e;
  assign out_13 = f;
  assign out_14 = g;

  // Notes on the sheet:
  //   dcbafge
  //   dcbafge
  //   cdbafge
  //   bafgedc
  //   abfgecd
  //   afgbced
  //   afgbced
  //   afgbced
  //   afgbced
  //   afgbced
endmodule
