// Logisim project tests.circ as structural Verilog: 9 circuits, main circuit main
module main (
  input  [3:0] in_1
);

  wire dnf_1_a, dnf_1_b, dnf_1_c, dnf_1_d, dnf_1_e, dnf_1_f, dnf_1_g, hyb_1_a, hyb_1_b, hyb_1_c, hyb_1_d,
       hyb_1_e, hyb_1_f, hyb_1_g;

  DNF dnf_1 (
    .x0(in_1[0]), .x1(in_1[1]), .x2(in_1[2]), .x3(in_1[3]), .a(dnf_1_a), .f(dnf_1_f), .g(dnf_1_g),
    .b(dnf_1_b), .c(dnf_1_c), .e(dnf_1_e), .d(dnf_1_d));
  HYB hyb_1 (
    .x0(in_1[0]), .x1(in_1[1]), .x2(in_1[2]), .x3(in_1[3]), .a(hyb_1_a), .f(hyb_1_f), .g(hyb_1_g),
    .b(hyb_1_b), .c(hyb_1_c), .e(hyb_1_e), .d(hyb_1_d));
  LED led_1 (.in(dnf_1_a));
  LED led_2 (.in(dnf_1_a));
  LED led_3 (.in(dnf_1_f));
  LED led_4 (.in(dnf_1_f));
  LED led_5 (.in(dnf_1_f));
  LED led_6 (.in(dnf_1_g));
  LED led_7 (.in(dnf_1_g));
  LED led_8 (.in(dnf_1_e));
  LED led_9 (.in(dnf_1_e));
  LED led_10 (.in(dnf_1_e));
  LED led_11 (.in(dnf_1_d));
  LED led_12 (.in(dnf_1_d));
  LED led_13 (.in(hyb_1_a));
  LED led_14 (.in(hyb_1_a));
  LED led_15 (.in(hyb_1_f));
  LED led_16 (.in(hyb_1_f));
  LED led_17 (.in(hyb_1_f));
  LED led_18 (.in(hyb_1_g));
  LED led_19 (.in(hyb_1_g));
  LED led_20 (.in(hyb_1_e));
  LED led_21 (.in(hyb_1_e));
  LED led_22 (.in(hyb_1_e));
  LED led_23 (.in(hyb_1_d));
  LED led_24 (.in(hyb_1_d));
  LED led_25 (.in(dnf_1_a));
  LED led_26 (.in(dnf_1_b));
  LED led_27 (.in(dnf_1_b));
  LED led_28 (.in(dnf_1_b));
  LED led_29 (.in(dnf_1_g));
  LED led_30 (.in(dnf_1_c));
  LED led_31 (.in(dnf_1_c));
  LED led_32 (.in(dnf_1_c));
  LED led_33 (.in(dnf_1_d));
  LED led_34 (.in(hyb_1_a));
  LED led_35 (.in(hyb_1_b));
  LED led_36 (.in(hyb_1_b));
  LED led_37 (.in(hyb_1_b));
  LED led_38 (.in(hyb_1_g));
  LED led_39 (.in(hyb_1_c));
  LED led_40 (.in(hyb_1_c));
  LED led_41 (.in(hyb_1_c));
  LED led_42 (.in(hyb_1_d));
endmodule

module CHECKING (
  input  [3:0] in_1,
  input  [3:0] in_2,
  input  [3:0] in_3,
  input  [3:0] in_4,
  input  [3:0] in_5,
  input  [3:0] in_6,
  input  [3:0] in_7,
  input  [3:0] in_8,
  input  [3:0] in_9,
  input  [3:0] in_10,
  input  [3:0] in_11
);

  wire showcase_1_da, showcase_1_db, showcase_1_dc, showcase_1_dd, showcase_1_de, showcase_1_df,
       showcase_1_dg, showcase_1_ha, showcase_1_hb, showcase_1_hc, showcase_1_hd, showcase_1_he,
       showcase_1_hf, showcase_1_hg, showcase_2_da, showcase_2_db, showcase_2_dc, showcase_2_dd,
       showcase_2_de, showcase_2_df, showcase_2_dg, showcase_2_ha, showcase_2_hb, showcase_2_hc,
       showcase_2_hd, showcase_2_he, showcase_2_hf, showcase_2_hg, showcase_3_da, showcase_3_db,
       showcase_3_dc, showcase_3_dd, showcase_3_de, showcase_3_df, showcase_3_dg, showcase_3_ha,
       showcase_3_hb, showcase_3_hc, showcase_3_hd, showcase_3_he, showcase_3_hf, showcase_3_hg,
       showcase_4_da, showcase_4_db, showcase_4_dc, showcase_4_dd, showcase_4_de, showcase_4_df,
       showcase_4_dg, showcase_4_ha, showcase_4_hb, showcase_4_hc, showcase_4_hd, showcase_4_he,
       showcase_4_hf, showcase_4_hg, showcase_5_da, showcase_5_db, showcase_5_dc, showcase_5_dd,
       showcase_5_de, showcase_5_df, showcase_5_dg, showcase_5_ha, showcase_5_hb, showcase_5_hc,
       showcase_5_hd, showcase_5_he, showcase_5_hf, showcase_5_hg, showcase_6_da, showcase_6_db,
       showcase_6_dc, showcase_6_dd, showcase_6_de, showcase_6_df, showcase_6_dg, showcase_6_ha,
       showcase_6_hb, showcase_6_hc, showcase_6_hd, showcase_6_he, showcase_6_hf, showcase_6_hg,
       showcase_7_da, showcase_7_db, showcase_7_dc, showcase_7_dd, showcase_7_de, showcase_7_df,
       showcase_7_dg, showcase_7_ha, showcase_7_hb, showcase_7_hc, showcase_7_hd, showcase_7_he,
       showcase_7_hf, showcase_7_hg, showcase_8_da, showcase_8_db, showcase_8_dc, showcase_8_dd,
       showcase_8_de, showcase_8_df, showcase_8_dg, showcase_8_ha, showcase_8_hb, showcase_8_hc,
       showcase_8_hd, showcase_8_he, showcase_8_hf, showcase_8_hg, showcase_9_da, showcase_9_db,
       showcase_9_dc, showcase_9_dd, showcase_9_de, showcase_9_df, showcase_9_dg, showcase_9_ha,
       showcase_9_hb, showcase_9_hc, showcase_9_hd, showcase_9_he, showcase_9_hf, showcase_9_hg,
       showcase_10_da, showcase_10_db, showcase_10_dc, showcase_10_dd, showcase_10_de, showcase_10_df,
       showcase_10_dg, showcase_10_ha, showcase_10_hb, showcase_10_hc, showcase_10_hd, showcase_10_he,
       showcase_10_hf, showcase_10_hg, showcase_11_da, showcase_11_db, showcase_11_dc, showcase_11_dd,
       showcase_11_de, showcase_11_df, showcase_11_dg, showcase_11_ha, showcase_11_hb, showcase_11_hc,
       showcase_11_hd, showcase_11_he, showcase_11_hf, showcase_11_hg;

  LED led_1 (.in(showcase_1_da));
  LED led_2 (.in(showcase_1_da));
  LED led_3 (.in(showcase_1_df));
  LED led_4 (.in(showcase_1_df));
  LED led_5 (.in(showcase_1_df));
  LED led_6 (.in(showcase_1_dg));
  LED led_7 (.in(showcase_1_dg));
  LED led_8 (.in(showcase_1_de));
  LED led_9 (.in(showcase_1_de));
  LED led_10 (.in(showcase_1_de));
  LED led_11 (.in(showcase_1_dd));
  LED led_12 (.in(showcase_1_dd));
  LED led_13 (.in(showcase_2_da));
  LED led_14 (.in(showcase_2_da));
  LED led_15 (.in(showcase_2_df));
  LED led_16 (.in(showcase_2_df));
  LED led_17 (.in(showcase_2_df));
  LED led_18 (.in(showcase_2_dg));
  LED led_19 (.in(showcase_2_dg));
  LED led_20 (.in(showcase_2_de));
  LED led_21 (.in(showcase_2_de));
  LED led_22 (.in(showcase_2_de));
  LED led_23 (.in(showcase_2_dd));
  LED led_24 (.in(showcase_2_dd));
  LED led_25 (.in(showcase_3_da));
  LED led_26 (.in(showcase_3_da));
  LED led_27 (.in(showcase_3_df));
  LED led_28 (.in(showcase_3_df));
  LED led_29 (.in(showcase_3_df));
  LED led_30 (.in(showcase_3_dg));
  LED led_31 (.in(showcase_3_dg));
  LED led_32 (.in(showcase_3_de));
  LED led_33 (.in(showcase_3_de));
  LED led_34 (.in(showcase_3_de));
  LED led_35 (.in(showcase_3_dd));
  LED led_36 (.in(showcase_3_dd));
  LED led_37 (.in(showcase_1_da));
  LED led_38 (.in(showcase_1_db));
  LED led_39 (.in(showcase_1_hf));
  LED led_40 (.in(showcase_1_db));
  LED led_41 (.in(showcase_1_hf));
  SHOWCASE showcase_1 (
    .Da(showcase_1_da), .Db(showcase_1_db), .Dg(showcase_1_dg), .Df(showcase_1_df), .De(showcase_1_de),
    .Dc(showcase_1_dc), .Dd(showcase_1_dd), .x(in_1), .Ha(showcase_1_ha), .Hf(showcase_1_hf),
    .Hg(showcase_1_hg), .Hb(showcase_1_hb), .Hc(showcase_1_hc), .He(showcase_1_he), .Hd(showcase_1_hd));
  LED led_42 (.in(showcase_1_db));
  LED led_43 (.in(showcase_1_hf));
  LED led_44 (.in(showcase_1_dg));
  LED led_45 (.in(showcase_1_dc));
  LED led_46 (.in(showcase_1_he));
  LED led_47 (.in(showcase_1_dc));
  LED led_48 (.in(showcase_1_he));
  LED led_49 (.in(showcase_1_dc));
  LED led_50 (.in(showcase_1_he));
  LED led_51 (.in(showcase_1_dd));
  LED led_52 (.in(showcase_2_da));
  LED led_53 (.in(showcase_2_db));
  LED led_54 (.in(showcase_2_hf));
  LED led_55 (.in(showcase_2_db));
  LED led_56 (.in(showcase_2_hf));
  SHOWCASE showcase_2 (
    .Da(showcase_2_da), .Db(showcase_2_db), .Dg(showcase_2_dg), .Df(showcase_2_df), .De(showcase_2_de),
    .Dc(showcase_2_dc), .Dd(showcase_2_dd), .x(in_4), .Ha(showcase_2_ha), .Hf(showcase_2_hf),
    .Hg(showcase_2_hg), .Hb(showcase_2_hb), .Hc(showcase_2_hc), .He(showcase_2_he), .Hd(showcase_2_hd));
  LED led_57 (.in(showcase_2_db));
  LED led_58 (.in(showcase_2_hf));
  LED led_59 (.in(showcase_2_dg));
  LED led_60 (.in(showcase_2_dc));
  LED led_61 (.in(showcase_2_he));
  LED led_62 (.in(showcase_2_dc));
  LED led_63 (.in(showcase_2_he));
  LED led_64 (.in(showcase_2_dc));
  LED led_65 (.in(showcase_2_he));
  LED led_66 (.in(showcase_2_dd));
  LED led_67 (.in(showcase_3_da));
  LED led_68 (.in(showcase_3_db));
  LED led_69 (.in(showcase_3_hf));
  LED led_70 (.in(showcase_3_db));
  LED led_71 (.in(showcase_3_hf));
  SHOWCASE showcase_3 (
    .Da(showcase_3_da), .Db(showcase_3_db), .Dg(showcase_3_dg), .Df(showcase_3_df), .De(showcase_3_de),
    .Dc(showcase_3_dc), .Dd(showcase_3_dd), .x(in_7), .Ha(showcase_3_ha), .Hf(showcase_3_hf),
    .Hg(showcase_3_hg), .Hb(showcase_3_hb), .Hc(showcase_3_hc), .He(showcase_3_he), .Hd(showcase_3_hd));
  LED led_72 (.in(showcase_3_db));
  LED led_73 (.in(showcase_3_hf));
  LED led_74 (.in(showcase_3_dg));
  LED led_75 (.in(showcase_3_dc));
  LED led_76 (.in(showcase_3_he));
  LED led_77 (.in(showcase_3_dc));
  LED led_78 (.in(showcase_3_he));
  LED led_79 (.in(showcase_3_dc));
  LED led_80 (.in(showcase_3_he));
  LED led_81 (.in(showcase_3_dd));
  LED led_82 (.in(showcase_1_ha));
  LED led_83 (.in(showcase_1_ha));
  LED led_84 (.in(showcase_1_ha));
  LED led_85 (.in(showcase_1_hb));
  LED led_86 (.in(showcase_1_hb));
  LED led_87 (.in(showcase_1_hb));
  LED led_88 (.in(showcase_1_hg));
  LED led_89 (.in(showcase_1_hg));
  LED led_90 (.in(showcase_1_hg));
  LED led_91 (.in(showcase_1_hc));
  LED led_92 (.in(showcase_1_hc));
  LED led_93 (.in(showcase_1_hc));
  LED led_94 (.in(showcase_1_hd));
  LED led_95 (.in(showcase_1_hd));
  LED led_96 (.in(showcase_1_hd));
  LED led_97 (.in(showcase_2_ha));
  LED led_98 (.in(showcase_2_ha));
  LED led_99 (.in(showcase_2_ha));
  LED led_100 (.in(showcase_2_hb));
  LED led_101 (.in(showcase_2_hb));
  LED led_102 (.in(showcase_2_hb));
  LED led_103 (.in(showcase_2_hg));
  LED led_104 (.in(showcase_2_hg));
  LED led_105 (.in(showcase_2_hg));
  LED led_106 (.in(showcase_2_hc));
  LED led_107 (.in(showcase_2_hc));
  LED led_108 (.in(showcase_2_hc));
  LED led_109 (.in(showcase_2_hd));
  LED led_110 (.in(showcase_2_hd));
  LED led_111 (.in(showcase_2_hd));
  LED led_112 (.in(showcase_3_ha));
  LED led_113 (.in(showcase_3_ha));
  LED led_114 (.in(showcase_3_ha));
  LED led_115 (.in(showcase_3_hb));
  LED led_116 (.in(showcase_3_hb));
  LED led_117 (.in(showcase_3_hb));
  LED led_118 (.in(showcase_3_hg));
  LED led_119 (.in(showcase_3_hg));
  LED led_120 (.in(showcase_3_hg));
  LED led_121 (.in(showcase_3_hc));
  LED led_122 (.in(showcase_3_hc));
  LED led_123 (.in(showcase_3_hc));
  LED led_124 (.in(showcase_3_hd));
  LED led_125 (.in(showcase_3_hd));
  LED led_126 (.in(showcase_3_hd));
  LED led_127 (.in(showcase_4_da));
  LED led_128 (.in(showcase_4_da));
  LED led_129 (.in(showcase_4_df));
  LED led_130 (.in(showcase_4_df));
  LED led_131 (.in(showcase_4_df));
  LED led_132 (.in(showcase_4_dg));
  LED led_133 (.in(showcase_4_dg));
  LED led_134 (.in(showcase_4_de));
  LED led_135 (.in(showcase_4_de));
  LED led_136 (.in(showcase_4_de));
  LED led_137 (.in(showcase_4_dd));
  LED led_138 (.in(showcase_4_dd));
  LED led_139 (.in(showcase_5_da));
  LED led_140 (.in(showcase_5_da));
  LED led_141 (.in(showcase_5_df));
  LED led_142 (.in(showcase_5_df));
  LED led_143 (.in(showcase_5_df));
  LED led_144 (.in(showcase_5_dg));
  LED led_145 (.in(showcase_5_dg));
  LED led_146 (.in(showcase_5_de));
  LED led_147 (.in(showcase_5_de));
  LED led_148 (.in(showcase_5_de));
  LED led_149 (.in(showcase_5_dd));
  LED led_150 (.in(showcase_5_dd));
  LED led_151 (.in(showcase_6_da));
  LED led_152 (.in(showcase_6_da));
  LED led_153 (.in(showcase_6_df));
  LED led_154 (.in(showcase_6_df));
  LED led_155 (.in(showcase_6_df));
  LED led_156 (.in(showcase_6_dg));
  LED led_157 (.in(showcase_6_dg));
  LED led_158 (.in(showcase_6_de));
  LED led_159 (.in(showcase_6_de));
  LED led_160 (.in(showcase_6_de));
  LED led_161 (.in(showcase_6_dd));
  LED led_162 (.in(showcase_6_dd));
  LED led_163 (.in(showcase_7_da));
  LED led_164 (.in(showcase_7_da));
  LED led_165 (.in(showcase_7_df));
  LED led_166 (.in(showcase_7_df));
  LED led_167 (.in(showcase_7_df));
  LED led_168 (.in(showcase_7_dg));
  LED led_169 (.in(showcase_7_dg));
  LED led_170 (.in(showcase_7_de));
  LED led_171 (.in(showcase_7_de));
  LED led_172 (.in(showcase_7_de));
  LED led_173 (.in(showcase_7_dd));
  LED led_174 (.in(showcase_7_dd));
  LED led_175 (.in(showcase_8_da));
  LED led_176 (.in(showcase_8_da));
  LED led_177 (.in(showcase_8_df));
  LED led_178 (.in(showcase_8_df));
  LED led_179 (.in(showcase_8_df));
  LED led_180 (.in(showcase_8_dg));
  LED led_181 (.in(showcase_8_dg));
  LED led_182 (.in(showcase_8_de));
  LED led_183 (.in(showcase_8_de));
  LED led_184 (.in(showcase_8_de));
  LED led_185 (.in(showcase_8_dd));
  LED led_186 (.in(showcase_8_dd));
  LED led_187 (.in(showcase_4_da));
  LED led_188 (.in(showcase_4_db));
  LED led_189 (.in(showcase_4_db));
  SHOWCASE showcase_4 (
    .Da(showcase_4_da), .Db(showcase_4_db), .Dg(showcase_4_dg), .Df(showcase_4_df), .De(showcase_4_de),
    .Dc(showcase_4_dc), .Dd(showcase_4_dd), .x(in_2), .Ha(showcase_4_ha), .Hf(showcase_4_hf),
    .Hg(showcase_4_hg), .Hb(showcase_4_hb), .Hc(showcase_4_hc), .He(showcase_4_he), .Hd(showcase_4_hd));
  LED led_190 (.in(showcase_4_db));
  LED led_191 (.in(showcase_4_dg));
  LED led_192 (.in(showcase_4_dc));
  LED led_193 (.in(showcase_4_dc));
  LED led_194 (.in(showcase_4_dc));
  LED led_195 (.in(showcase_4_dd));
  LED led_196 (.in(showcase_5_da));
  LED led_197 (.in(showcase_5_db));
  LED led_198 (.in(showcase_5_db));
  SHOWCASE showcase_5 (
    .Da(showcase_5_da), .Db(showcase_5_db), .Dg(showcase_5_dg), .Df(showcase_5_df), .De(showcase_5_de),
    .Dc(showcase_5_dc), .Dd(showcase_5_dd), .x(in_5), .Ha(showcase_5_ha), .Hf(showcase_5_hf),
    .Hg(showcase_5_hg), .Hb(showcase_5_hb), .Hc(showcase_5_hc), .He(showcase_5_he), .Hd(showcase_5_hd));
  LED led_199 (.in(showcase_5_db));
  LED led_200 (.in(showcase_5_dg));
  LED led_201 (.in(showcase_5_dc));
  LED led_202 (.in(showcase_5_dc));
  LED led_203 (.in(showcase_5_dc));
  LED led_204 (.in(showcase_5_dd));
  LED led_205 (.in(showcase_6_da));
  LED led_206 (.in(showcase_6_db));
  LED led_207 (.in(showcase_6_db));
  SHOWCASE showcase_6 (
    .Da(showcase_6_da), .Db(showcase_6_db), .Dg(showcase_6_dg), .Df(showcase_6_df), .De(showcase_6_de),
    .Dc(showcase_6_dc), .Dd(showcase_6_dd), .x(in_8), .Ha(showcase_6_ha), .Hf(showcase_6_hf),
    .Hg(showcase_6_hg), .Hb(showcase_6_hb), .Hc(showcase_6_hc), .He(showcase_6_he), .Hd(showcase_6_hd));
  LED led_208 (.in(showcase_6_db));
  LED led_209 (.in(showcase_6_dg));
  LED led_210 (.in(showcase_6_dc));
  LED led_211 (.in(showcase_6_dc));
  LED led_212 (.in(showcase_6_dc));
  LED led_213 (.in(showcase_6_dd));
  LED led_214 (.in(showcase_7_da));
  LED led_215 (.in(showcase_7_db));
  LED led_216 (.in(showcase_7_db));
  SHOWCASE showcase_7 (
    .Da(showcase_7_da), .Db(showcase_7_db), .Dg(showcase_7_dg), .Df(showcase_7_df), .De(showcase_7_de),
    .Dc(showcase_7_dc), .Dd(showcase_7_dd), .x(in_10), .Ha(showcase_7_ha), .Hf(showcase_7_hf),
    .Hg(showcase_7_hg), .Hb(showcase_7_hb), .Hc(showcase_7_hc), .He(showcase_7_he), .Hd(showcase_7_hd));
  LED led_217 (.in(showcase_7_db));
  LED led_218 (.in(showcase_7_dg));
  LED led_219 (.in(showcase_7_dc));
  LED led_220 (.in(showcase_7_dc));
  LED led_221 (.in(showcase_7_dc));
  LED led_222 (.in(showcase_7_dd));
  LED led_223 (.in(showcase_8_da));
  LED led_224 (.in(showcase_8_db));
  LED led_225 (.in(showcase_8_db));
  SHOWCASE showcase_8 (
    .Da(showcase_8_da), .Db(showcase_8_db), .Dg(showcase_8_dg), .Df(showcase_8_df), .De(showcase_8_de),
    .Dc(showcase_8_dc), .Dd(showcase_8_dd), .x(in_11), .Ha(showcase_8_ha), .Hf(showcase_8_hf),
    .Hg(showcase_8_hg), .Hb(showcase_8_hb), .Hc(showcase_8_hc), .He(showcase_8_he), .Hd(showcase_8_hd));
  LED led_226 (.in(showcase_8_db));
  LED led_227 (.in(showcase_8_dg));
  LED led_228 (.in(showcase_8_dc));
  LED led_229 (.in(showcase_8_dc));
  LED led_230 (.in(showcase_8_dc));
  LED led_231 (.in(showcase_8_dd));
  LED led_232 (.in(showcase_4_ha));
  LED led_233 (.in(showcase_4_ha));
  LED led_234 (.in(showcase_4_ha));
  LED led_235 (.in(showcase_4_hf));
  LED led_236 (.in(showcase_4_hf));
  LED led_237 (.in(showcase_4_hf));
  LED led_238 (.in(showcase_4_hg));
  LED led_239 (.in(showcase_4_hg));
  LED led_240 (.in(showcase_4_hg));
  LED led_241 (.in(showcase_4_he));
  LED led_242 (.in(showcase_4_he));
  LED led_243 (.in(showcase_4_he));
  LED led_244 (.in(showcase_4_hd));
  LED led_245 (.in(showcase_4_hd));
  LED led_246 (.in(showcase_4_hd));
  LED led_247 (.in(showcase_5_ha));
  LED led_248 (.in(showcase_5_ha));
  LED led_249 (.in(showcase_5_ha));
  LED led_250 (.in(showcase_5_hf));
  LED led_251 (.in(showcase_5_hf));
  LED led_252 (.in(showcase_5_hf));
  LED led_253 (.in(showcase_5_hg));
  LED led_254 (.in(showcase_5_hg));
  LED led_255 (.in(showcase_5_hg));
  LED led_256 (.in(showcase_5_he));
  LED led_257 (.in(showcase_5_he));
  LED led_258 (.in(showcase_5_he));
  LED led_259 (.in(showcase_5_hd));
  LED led_260 (.in(showcase_5_hd));
  LED led_261 (.in(showcase_5_hd));
  LED led_262 (.in(showcase_6_ha));
  LED led_263 (.in(showcase_6_ha));
  LED led_264 (.in(showcase_6_ha));
  LED led_265 (.in(showcase_6_hf));
  LED led_266 (.in(showcase_6_hf));
  LED led_267 (.in(showcase_6_hf));
  LED led_268 (.in(showcase_6_hg));
  LED led_269 (.in(showcase_6_hg));
  LED led_270 (.in(showcase_6_hg));
  LED led_271 (.in(showcase_6_he));
  LED led_272 (.in(showcase_6_he));
  LED led_273 (.in(showcase_6_he));
  LED led_274 (.in(showcase_6_hd));
  LED led_275 (.in(showcase_6_hd));
  LED led_276 (.in(showcase_6_hd));
  LED led_277 (.in(showcase_7_ha));
  LED led_278 (.in(showcase_7_ha));
  LED led_279 (.in(showcase_7_ha));
  LED led_280 (.in(showcase_7_hf));
  LED led_281 (.in(showcase_7_hf));
  LED led_282 (.in(showcase_7_hf));
  LED led_283 (.in(showcase_7_hg));
  LED led_284 (.in(showcase_7_hg));
  LED led_285 (.in(showcase_7_hg));
  LED led_286 (.in(showcase_7_he));
  LED led_287 (.in(showcase_7_he));
  LED led_288 (.in(showcase_7_he));
  LED led_289 (.in(showcase_7_hd));
  LED led_290 (.in(showcase_7_hd));
  LED led_291 (.in(showcase_7_hd));
  LED led_292 (.in(showcase_8_ha));
  LED led_293 (.in(showcase_8_ha));
  LED led_294 (.in(showcase_8_ha));
  LED led_295 (.in(showcase_8_hf));
  LED led_296 (.in(showcase_8_hf));
  LED led_297 (.in(showcase_8_hf));
  LED led_298 (.in(showcase_8_hg));
  LED led_299 (.in(showcase_8_hg));
  LED led_300 (.in(showcase_8_hg));
  LED led_301 (.in(showcase_8_he));
  LED led_302 (.in(showcase_8_he));
  LED led_303 (.in(showcase_8_he));
  LED led_304 (.in(showcase_8_hd));
  LED led_305 (.in(showcase_8_hd));
  LED led_306 (.in(showcase_8_hd));
  LED led_307 (.in(showcase_9_da));
  LED led_308 (.in(showcase_4_hb));
  LED led_309 (.in(showcase_9_df));
  LED led_310 (.in(showcase_4_hb));
  LED led_311 (.in(showcase_9_df));
  LED led_312 (.in(showcase_4_hb));
  LED led_313 (.in(showcase_9_df));
  LED led_314 (.in(showcase_9_dg));
  LED led_315 (.in(showcase_4_hc));
  LED led_316 (.in(showcase_9_de));
  LED led_317 (.in(showcase_4_hc));
  LED led_318 (.in(showcase_9_de));
  LED led_319 (.in(showcase_4_hc));
  LED led_320 (.in(showcase_9_de));
  LED led_321 (.in(showcase_9_dd));
  LED led_322 (.in(showcase_10_da));
  LED led_323 (.in(showcase_5_hb));
  LED led_324 (.in(showcase_10_df));
  LED led_325 (.in(showcase_5_hb));
  LED led_326 (.in(showcase_10_df));
  LED led_327 (.in(showcase_5_hb));
  LED led_328 (.in(showcase_10_df));
  LED led_329 (.in(showcase_10_dg));
  LED led_330 (.in(showcase_5_hc));
  LED led_331 (.in(showcase_10_de));
  LED led_332 (.in(showcase_5_hc));
  LED led_333 (.in(showcase_10_de));
  LED led_334 (.in(showcase_5_hc));
  LED led_335 (.in(showcase_10_de));
  LED led_336 (.in(showcase_10_dd));
  LED led_337 (.in(showcase_11_da));
  LED led_338 (.in(showcase_6_hb));
  LED led_339 (.in(showcase_11_df));
  LED led_340 (.in(showcase_6_hb));
  LED led_341 (.in(showcase_11_df));
  LED led_342 (.in(showcase_6_hb));
  LED led_343 (.in(showcase_11_df));
  LED led_344 (.in(showcase_11_dg));
  LED led_345 (.in(showcase_6_hc));
  LED led_346 (.in(showcase_11_de));
  LED led_347 (.in(showcase_6_hc));
  LED led_348 (.in(showcase_11_de));
  LED led_349 (.in(showcase_6_hc));
  LED led_350 (.in(showcase_11_de));
  LED led_351 (.in(showcase_11_dd));
  LED led_352 (.in(showcase_7_hb));
  LED led_353 (.in(showcase_7_hb));
  LED led_354 (.in(showcase_7_hb));
  LED led_355 (.in(showcase_7_hc));
  LED led_356 (.in(showcase_7_hc));
  LED led_357 (.in(showcase_7_hc));
  LED led_358 (.in(showcase_8_hb));
  LED led_359 (.in(showcase_8_hb));
  LED led_360 (.in(showcase_8_hb));
  LED led_361 (.in(showcase_8_hc));
  LED led_362 (.in(showcase_8_hc));
  LED led_363 (.in(showcase_8_hc));
  LED led_364 (.in(showcase_9_da));
  LED led_365 (.in(showcase_9_da));
  LED led_366 (.in(showcase_9_db));
  LED led_367 (.in(showcase_9_db));
  LED led_368 (.in(showcase_9_db));
  LED led_369 (.in(showcase_9_dg));
  LED led_370 (.in(showcase_9_dg));
  LED led_371 (.in(showcase_9_dc));
  LED led_372 (.in(showcase_9_dc));
  LED led_373 (.in(showcase_9_dc));
  LED led_374 (.in(showcase_9_dd));
  LED led_375 (.in(showcase_9_dd));
  LED led_376 (.in(showcase_10_da));
  LED led_377 (.in(showcase_10_da));
  LED led_378 (.in(showcase_10_db));
  LED led_379 (.in(showcase_10_db));
  LED led_380 (.in(showcase_10_db));
  LED led_381 (.in(showcase_10_dg));
  LED led_382 (.in(showcase_10_dg));
  LED led_383 (.in(showcase_10_dc));
  LED led_384 (.in(showcase_10_dc));
  LED led_385 (.in(showcase_10_dc));
  LED led_386 (.in(showcase_10_dd));
  LED led_387 (.in(showcase_10_dd));
  LED led_388 (.in(showcase_11_da));
  LED led_389 (.in(showcase_11_da));
  LED led_390 (.in(showcase_11_db));
  LED led_391 (.in(showcase_11_db));
  LED led_392 (.in(showcase_11_db));
  LED led_393 (.in(showcase_11_dg));
  LED led_394 (.in(showcase_11_dg));
  LED led_395 (.in(showcase_11_dc));
  LED led_396 (.in(showcase_11_dc));
  LED led_397 (.in(showcase_11_dc));
  LED led_398 (.in(showcase_11_dd));
  LED led_399 (.in(showcase_11_dd));
  LED led_400 (.in(showcase_9_ha));
  LED led_401 (.in(showcase_9_ha));
  LED led_402 (.in(showcase_9_ha));
  LED led_403 (.in(showcase_9_hf));
  LED led_404 (.in(showcase_9_hf));
  SHOWCASE showcase_9 (
    .Da(showcase_9_da), .Db(showcase_9_db), .Dg(showcase_9_dg), .Df(showcase_9_df), .De(showcase_9_de),
    .Dc(showcase_9_dc), .Dd(showcase_9_dd), .x(in_3), .Ha(showcase_9_ha), .Hf(showcase_9_hf),
    .Hg(showcase_9_hg), .Hb(showcase_9_hb), .Hc(showcase_9_hc), .He(showcase_9_he), .Hd(showcase_9_hd));
  LED led_405 (.in(showcase_9_hf));
  LED led_406 (.in(showcase_9_hg));
  LED led_407 (.in(showcase_9_hg));
  LED led_408 (.in(showcase_9_hg));
  LED led_409 (.in(showcase_9_he));
  LED led_410 (.in(showcase_9_he));
  LED led_411 (.in(showcase_9_he));
  LED led_412 (.in(showcase_9_hd));
  LED led_413 (.in(showcase_9_hd));
  LED led_414 (.in(showcase_9_hd));
  LED led_415 (.in(showcase_10_ha));
  LED led_416 (.in(showcase_10_ha));
  LED led_417 (.in(showcase_10_ha));
  LED led_418 (.in(showcase_10_hf));
  LED led_419 (.in(showcase_10_hf));
  SHOWCASE showcase_10 (
    .Da(showcase_10_da), .Db(showcase_10_db), .Dg(showcase_10_dg), .Df(showcase_10_df), .De(showcase_10_de),
    .Dc(showcase_10_dc), .Dd(showcase_10_dd), .x(in_6), .Ha(showcase_10_ha), .Hf(showcase_10_hf),
    .Hg(showcase_10_hg), .Hb(showcase_10_hb), .Hc(showcase_10_hc), .He(showcase_10_he), .Hd(showcase_10_hd));
  LED led_420 (.in(showcase_10_hf));
  LED led_421 (.in(showcase_10_hg));
  LED led_422 (.in(showcase_10_hg));
  LED led_423 (.in(showcase_10_hg));
  LED led_424 (.in(showcase_10_he));
  LED led_425 (.in(showcase_10_he));
  LED led_426 (.in(showcase_10_he));
  LED led_427 (.in(showcase_10_hd));
  LED led_428 (.in(showcase_10_hd));
  LED led_429 (.in(showcase_10_hd));
  LED led_430 (.in(showcase_11_ha));
  LED led_431 (.in(showcase_11_ha));
  LED led_432 (.in(showcase_11_ha));
  LED led_433 (.in(showcase_11_hf));
  LED led_434 (.in(showcase_11_hf));
  SHOWCASE showcase_11 (
    .Da(showcase_11_da), .Db(showcase_11_db), .Dg(showcase_11_dg), .Df(showcase_11_df), .De(showcase_11_de),
    .Dc(showcase_11_dc), .Dd(showcase_11_dd), .x(in_9), .Ha(showcase_11_ha), .Hf(showcase_11_hf),
    .Hg(showcase_11_hg), .Hb(showcase_11_hb), .Hc(showcase_11_hc), .He(showcase_11_he), .Hd(showcase_11_hd));
  LED led_435 (.in(showcase_11_hf));
  LED led_436 (.in(showcase_11_hg));
  LED led_437 (.in(showcase_11_hg));
  LED led_438 (.in(showcase_11_hg));
  LED led_439 (.in(showcase_11_he));
  LED led_440 (.in(showcase_11_he));
  LED led_441 (.in(showcase_11_he));
  LED led_442 (.in(showcase_11_hd));
  LED led_443 (.in(showcase_11_hd));
  LED led_444 (.in(showcase_11_hd));
  LED led_445 (.in(showcase_9_hb));
  LED led_446 (.in(showcase_9_hb));
  LED led_447 (.in(showcase_9_hb));
  LED led_448 (.in(showcase_9_hc));
  LED led_449 (.in(showcase_9_hc));
  LED led_450 (.in(showcase_9_hc));
  LED led_451 (.in(showcase_10_hb));
  LED led_452 (.in(showcase_10_hb));
  LED led_453 (.in(showcase_10_hb));
  LED led_454 (.in(showcase_10_hc));
  LED led_455 (.in(showcase_10_hc));
  LED led_456 (.in(showcase_10_hc));
  LED led_457 (.in(showcase_11_hb));
  LED led_458 (.in(showcase_11_hb));
  LED led_459 (.in(showcase_11_hb));
  LED led_460 (.in(showcase_11_hc));
  LED led_461 (.in(showcase_11_hc));
  LED led_462 (.in(showcase_11_hc));
endmodule

module HYB (
  input  x0,
  input  x1,
  input  x2,
  input  x3,
  output a,
  output f,
  output g,
  output b,
  output c,
  output e,
  output d
);

  wire and_2_out, and_4_out, or_4_out, or_5_out, or_6_out, or_7_out, or_8_out, or_10_out, xor_1_out,
       xor_2_out, xor_3_out;

  xor xor_1 (xor_1_out, x0, x2);
  or or_1 (a, x1, x3, ~xor_1_out);  // OR_Gate
  xor xor_2 (xor_2_out, x0, x1);
  or or_2 (b, ~x2, ~xor_2_out);  // OR_Gate
  or or_3 (c, x0, ~x1, x2);  // OR_Gate
  xor xor_3 (xor_3_out, x0, x1);
  or or_4 (or_4_out, ~x1, xor_3_out);  // OR_Gate
  or or_5 (or_5_out, ~x0, x1, x2, x3);  // OR_Gate
  and and_1 (d, or_4_out, or_5_out);
  and and_2 (and_2_out, ~x0, x2);  // AND_Gate
  or or_6 (or_6_out, x1, ~x2);  // OR_Gate
  and and_3 (e, ~x0, or_6_out);  // AND_Gate
  or or_7 (or_7_out, ~x0, x2);  // OR_Gate
  or or_8 (or_8_out, ~x0, ~x1, ~x2);  // OR_Gate
  and and_4 (and_4_out, ~x1, or_7_out);  // AND_Gate
  or or_9 (f, x3, and_2_out, and_4_out);
  and and_5 (g, or_8_out, or_10_out);
  or or_10 (or_10_out, x1, x2, x3);
endmodule

module DNF_abcdefg (
  input  x0,
  input  x1,
  input  x2,
  input  x3,
  output a,
  output b,
  output c,
  output d,
  output e,
  output f,
  output g
);

  wire and_2_out, and_3_out, and_4_out, and_5_out, and_6_out, and_7_out, and_8_out, and_9_out, and_10_out,
       and_11_out, and_12_out, and_13_out, and_14_out, and_15_out, and_16_out, and_17_out, xor_1_out;

  xor xor_1 (xor_1_out, x0, x2);
  // NOT_Gate not_1 has open pins: in=xor_1_out, out=open
  // NOT_Gate not_2 has open pins: in=x2, out=open
  // AND_Gate and_1 has open pins: in0=x0, in1=x1, out=open
  // NAND_Gate nand_1 has open pins: in0=x0, in1=x1, out=open
  // XOR_Gate xor_2 has open pins: in0=x0, in1=x1, out=open
  and and_2 (and_2_out, x0, x2);
  or or_1 (a, x1, x3, and_2_out);
  and and_3 (and_3_out, x0, x1);
  and and_4 (and_4_out, x0, ~x2);  // AND_Gate
  or or_2 (b, x3, and_3_out, and_4_out, and_6_out, and_5_out);
  and and_5 (and_5_out, ~x0, ~x1, x2);  // AND_Gate
  and and_6 (and_6_out, x1, ~x2);  // AND_Gate
  and and_7 (and_7_out, ~x0, x1);  // AND_Gate
  or or_3 (c, x0, x2, x3);
  and and_8 (and_8_out, ~x0, x3);  // AND_Gate
  and and_9 (and_9_out, x1, ~x2);  // AND_Gate
  or or_4 (d, and_7_out, and_8_out, and_9_out, and_10_out);
  and and_10 (and_10_out, x0, ~x1, x2);  // AND_Gate
  and and_11 (and_11_out, ~x0, x1);  // AND_Gate
  and and_12 (and_12_out, ~x0, x3);  // AND_Gate
  or or_5 (e, and_11_out, and_12_out);
  and and_13 (and_13_out, ~x0, x2);  // AND_Gate
  and and_14 (and_14_out, ~x1, x2);  // AND_Gate
  or or_6 (f, x3, and_13_out, and_14_out);
  and and_15 (and_15_out, ~x0, x2);  // AND_Gate
  and and_16 (and_16_out, ~x1, x2);  // AND_Gate
  and and_17 (and_17_out, x1, ~x2);  // AND_Gate
  or or_7 (g, x3, and_15_out, and_16_out, and_17_out);
endmodule

module CNF (
  input  x0,
  input  x1,
  input  x2,
  input  x3,
  output a,
  output b,
  output c,
  output d,
  output e,
  output f,
  output g
);

  wire and_2_out, and_4_out, and_5_out, and_6_out, and_7_out, and_8_out, nand_1_out, nand_2_out, nand_3_out,
       nand_4_out, nand_5_out, or_1_out, or_2_out;

  or or_1 (or_1_out, x0, x1, x3);
  and and_1 (a, or_1_out, or_2_out);
  or or_2 (or_2_out, x1, x2, x3);
  and and_2 (and_2_out, x0, x2);
  or or_3 (b, and_2_out, nand_1_out);
  and and_3 (c, x0, x3);
  nand nand_1 (nand_1_out, x0, x1, x2, x3);
  and and_4 (and_4_out, x0, x1, x2);
  and and_5 (and_5_out, x0, ~x1, ~x2);  // AND_Gate
  nor nor_1 (d, and_4_out, and_5_out, nand_2_out);
  and and_6 (and_6_out, ~x1, x2);  // AND_Gate
  nand nand_2 (nand_2_out, x0, x1, x3);
  nor nor_2 (e, x0, and_6_out, nand_3_out);
  and and_7 (and_7_out, x0, x1);
  nand nand_3 (nand_3_out, x1, x2, x3);
  nand nand_4 (nand_4_out, x2, x3);
  or or_4 (f, and_7_out, nand_4_out);
  and and_8 (and_8_out, x0, x1, x2);
  nand nand_5 (nand_5_out, x1, x2, x3);
  or or_5 (g, and_8_out, nand_5_out);
endmodule

module LEDS (
  input  a,
  input  b,
  input  c,
  input  [3:0] in_4,
  input  [3:0] in_5,
  input  d,
  input  e,
  input  f,
  input  g,
  input  [3:0] in_10,
  input  [3:0] in_11,
  input  [3:0] in_12,
  input  [3:0] in_13,
  input  [3:0] in_14,
  input  [3:0] in_15,
  input  [3:0] in_16,
  input  [3:0] in_17,
  output out_18,
  output out_19,
  output out_20,
  output out_21,
  output out_22,
  output out_23,
  output out_24
);

  wire dnf_1_a, dnf_1_b, dnf_1_c, dnf_1_d, dnf_1_e, dnf_1_f, dnf_1_g, dnf_2_a, dnf_2_b, dnf_2_c, dnf_2_d,
       dnf_2_e, dnf_2_f, dnf_2_g, dnf_3_a, dnf_3_b, dnf_3_c, dnf_3_d, dnf_3_e, dnf_3_f, dnf_3_g, dnf_4_a,
       dnf_4_b, dnf_4_c, dnf_4_d, dnf_4_e, dnf_4_f, dnf_4_g, dnf_5_a, dnf_5_b, dnf_5_c, dnf_5_d, dnf_5_e,
       dnf_5_f, dnf_5_g, dnf_6_a, dnf_6_b, dnf_6_c, dnf_6_d, dnf_6_e, dnf_6_f, dnf_6_g, dnf_7_a, dnf_7_b,
       dnf_7_c, dnf_7_d, dnf_7_e, dnf_7_f, dnf_7_g, dnf_8_a, dnf_8_b, dnf_8_c, dnf_8_d, dnf_8_e, dnf_8_f,
       dnf_8_g, dnf_9_a, dnf_9_b, dnf_9_c, dnf_9_d, dnf_9_e, dnf_9_f, dnf_9_g, dnf_10_a, dnf_10_b, dnf_10_c,
       dnf_10_d, dnf_10_e, dnf_10_f, dnf_10_g, hyb_1_a, hyb_1_b, hyb_1_c, hyb_1_d, hyb_1_e, hyb_1_f, hyb_1_g,
       hyb_2_a, hyb_2_b, hyb_2_c, hyb_2_d, hyb_2_e, hyb_2_f, hyb_2_g, hyb_3_a, hyb_3_b, hyb_3_c, hyb_3_d,
       hyb_3_e, hyb_3_f, hyb_3_g, hyb_4_a, hyb_4_b, hyb_4_c, hyb_4_d, hyb_4_e, hyb_4_f, hyb_4_g, hyb_5_a,
       hyb_5_b, hyb_5_c, hyb_5_d, hyb_5_e, hyb_5_f, hyb_5_g, hyb_6_a, hyb_6_b, hyb_6_c, hyb_6_d, hyb_6_e,
       hyb_6_f, hyb_6_g, hyb_7_a, hyb_7_b, hyb_7_c, hyb_7_d, hyb_7_e, hyb_7_f, hyb_7_g, hyb_8_a, hyb_8_b,
       hyb_8_c, hyb_8_d, hyb_8_e, hyb_8_f, hyb_8_g, hyb_9_a, hyb_9_b, hyb_9_c, hyb_9_d, hyb_9_e, hyb_9_f,
       hyb_9_g, hyb_10_a, hyb_10_b, hyb_10_c, hyb_10_d, hyb_10_e, hyb_10_f, hyb_10_g, undriven, undriven_2,
       undriven_3, undriven_4, undriven_5, undriven_6, undriven_7;

  LED led_1 (.in(f));
  LED led_2 (.in(f));
  LED led_3 (.in(f));
  LED led_4 (.in(e));
  LED led_5 (.in(e));
  LED led_6 (.in(e));
  LED led_7 (.in(a));
  LED led_8 (.in(a));
  LED led_9 (.in(a));
  LED led_10 (.in(b));
  LED led_11 (.in(b));
  LED led_12 (.in(b));
  LED led_13 (.in(g));
  LED led_14 (.in(g));
  LED led_15 (.in(g));
  LED led_16 (.in(c));
  LED led_17 (.in(c));
  LED led_18 (.in(c));
  LED led_19 (.in(d));
  LED led_20 (.in(d));
  LED led_21 (.in(d));
  LED led_22 (.in(undriven_3));
  LED led_23 (.in(undriven));
  LED led_24 (.in(undriven));
  LED led_25 (.in(undriven));
  LED led_26 (.in(undriven_4));
  LED led_27 (.in(undriven_2));
  LED led_28 (.in(undriven_2));
  LED led_29 (.in(undriven_2));
  LED led_30 (.in(undriven_5));
  LED led_31 (.in(f));
  LED led_32 (.in(f));
  LED led_33 (.in(f));
  LED led_34 (.in(e));
  LED led_35 (.in(e));
  LED led_36 (.in(e));
  LED led_37 (.in(undriven_3));
  LED led_38 (.in(undriven_3));
  LED led_39 (.in(undriven_6));
  LED led_40 (.in(undriven_6));
  LED led_41 (.in(undriven_6));
  LED led_42 (.in(undriven_4));
  LED led_43 (.in(undriven_4));
  LED led_44 (.in(undriven_7));
  LED led_45 (.in(undriven_7));
  LED led_46 (.in(undriven_7));
  LED led_47 (.in(undriven_5));
  LED led_48 (.in(undriven_5));
  LED led_49 (.in(a));
  LED led_50 (.in(a));
  LED led_51 (.in(a));
  LED led_52 (.in(b));
  LED led_53 (.in(b));
  LED led_54 (.in(b));
  LED led_55 (.in(g));
  LED led_56 (.in(g));
  LED led_57 (.in(g));
  LED led_58 (.in(c));
  LED led_59 (.in(c));
  LED led_60 (.in(c));
  LED led_61 (.in(d));
  LED led_62 (.in(d));
  LED led_63 (.in(d));
  LED led_64 (.in(f));
  LED led_65 (.in(f));
  LED led_66 (.in(f));
  LED led_67 (.in(e));
  LED led_68 (.in(e));
  LED led_69 (.in(e));
  LED led_70 (.in(a));
  LED led_71 (.in(a));
  LED led_72 (.in(a));
  LED led_73 (.in(b));
  LED led_74 (.in(b));
  LED led_75 (.in(b));
  LED led_76 (.in(g));
  LED led_77 (.in(g));
  LED led_78 (.in(g));
  LED led_79 (.in(c));
  LED led_80 (.in(c));
  LED led_81 (.in(c));
  LED led_82 (.in(d));
  LED led_83 (.in(d));
  LED led_84 (.in(d));
  LED led_85 (.in(a));
  LED led_86 (.in(a));
  LED led_87 (.in(a));
  LED led_88 (.in(f));
  LED led_89 (.in(f));
  LED led_90 (.in(f));
  LED led_91 (.in(g));
  LED led_92 (.in(g));
  LED led_93 (.in(g));
  LED led_94 (.in(e));
  LED led_95 (.in(e));
  LED led_96 (.in(e));
  LED led_97 (.in(d));
  LED led_98 (.in(d));
  LED led_99 (.in(d));
  LED led_100 (.in(b));
  LED led_101 (.in(b));
  LED led_102 (.in(b));
  LED led_103 (.in(c));
  LED led_104 (.in(c));
  LED led_105 (.in(c));
  LED led_106 (.in(f));
  LED led_107 (.in(f));
  LED led_108 (.in(f));
  LED led_109 (.in(e));
  LED led_110 (.in(e));
  LED led_111 (.in(e));
  LED led_112 (.in(a));
  LED led_113 (.in(a));
  LED led_114 (.in(a));
  LED led_115 (.in(b));
  LED led_116 (.in(b));
  LED led_117 (.in(b));
  LED led_118 (.in(g));
  LED led_119 (.in(g));
  LED led_120 (.in(g));
  LED led_121 (.in(c));
  LED led_122 (.in(c));
  LED led_123 (.in(c));
  LED led_124 (.in(d));
  LED led_125 (.in(d));
  LED led_126 (.in(d));
  LED led_127 (.in(a));
  LED led_128 (.in(f));
  LED led_129 (.in(f));
  LED led_130 (.in(f));
  LED led_131 (.in(g));
  LED led_132 (.in(e));
  LED led_133 (.in(e));
  LED led_134 (.in(e));
  LED led_135 (.in(d));
  LED led_136 (.in(a));
  LED led_137 (.in(a));
  LED led_138 (.in(b));
  LED led_139 (.in(b));
  LED led_140 (.in(b));
  LED led_141 (.in(g));
  LED led_142 (.in(g));
  LED led_143 (.in(c));
  LED led_144 (.in(c));
  LED led_145 (.in(c));
  LED led_146 (.in(d));
  LED led_147 (.in(d));
  LED led_148 (.in(a));
  LED led_149 (.in(a));
  LED led_150 (.in(f));
  LED led_151 (.in(f));
  LED led_152 (.in(f));
  LED led_153 (.in(g));
  LED led_154 (.in(g));
  LED led_155 (.in(e));
  LED led_156 (.in(e));
  LED led_157 (.in(e));
  LED led_158 (.in(d));
  LED led_159 (.in(d));
  LED led_160 (.in(a));
  LED led_161 (.in(b));
  LED led_162 (.in(b));
  LED led_163 (.in(b));
  LED led_164 (.in(g));
  LED led_165 (.in(c));
  LED led_166 (.in(c));
  LED led_167 (.in(c));
  LED led_168 (.in(d));
  LED led_169 (.in(dnf_1_a));
  LED led_170 (.in(dnf_1_a));
  LED led_171 (.in(dnf_1_f));
  LED led_172 (.in(dnf_1_f));
  DNF dnf_1 (
    .x0(in_4[0]), .x1(in_4[1]), .x2(in_4[2]), .x3(in_4[3]), .a(dnf_1_a), .f(dnf_1_f), .g(dnf_1_g),
    .b(dnf_1_b), .c(dnf_1_c), .e(dnf_1_e), .d(dnf_1_d));
  LED led_173 (.in(dnf_1_f));
  LED led_174 (.in(dnf_1_g));
  LED led_175 (.in(dnf_1_g));
  LED led_176 (.in(dnf_1_e));
  LED led_177 (.in(dnf_1_e));
  LED led_178 (.in(dnf_1_e));
  LED led_179 (.in(dnf_1_d));
  LED led_180 (.in(dnf_1_d));
  HYB hyb_1 (
    .x0(in_4[0]), .x1(in_4[1]), .x2(in_4[2]), .x3(in_4[3]), .a(hyb_1_a), .f(hyb_1_f), .g(hyb_1_g),
    .b(hyb_1_b), .c(hyb_1_c), .e(hyb_1_e), .d(hyb_1_d));
  LED led_181 (.in(dnf_2_a));
  LED led_182 (.in(dnf_2_a));
  LED led_183 (.in(dnf_2_f));
  LED led_184 (.in(dnf_2_f));
  DNF dnf_2 (
    .x0(in_10[0]), .x1(in_10[1]), .x2(in_10[2]), .x3(in_10[3]), .a(dnf_2_a), .f(dnf_2_f), .g(dnf_2_g),
    .b(dnf_2_b), .c(dnf_2_c), .e(dnf_2_e), .d(dnf_2_d));
  LED led_185 (.in(dnf_2_f));
  LED led_186 (.in(dnf_2_g));
  LED led_187 (.in(dnf_2_g));
  LED led_188 (.in(dnf_2_e));
  LED led_189 (.in(dnf_2_e));
  LED led_190 (.in(dnf_2_e));
  LED led_191 (.in(dnf_2_d));
  LED led_192 (.in(dnf_2_d));
  HYB hyb_2 (
    .x0(in_10[0]), .x1(in_10[1]), .x2(in_10[2]), .x3(in_10[3]), .a(hyb_2_a), .f(hyb_2_f), .g(hyb_2_g),
    .b(hyb_2_b), .c(hyb_2_c), .e(hyb_2_e), .d(hyb_2_d));
  LED led_193 (.in(dnf_3_a));
  LED led_194 (.in(dnf_3_a));
  LED led_195 (.in(dnf_3_f));
  LED led_196 (.in(dnf_3_f));
  DNF dnf_3 (
    .x0(in_12[0]), .x1(in_12[1]), .x2(in_12[2]), .x3(in_12[3]), .a(dnf_3_a), .f(dnf_3_f), .g(dnf_3_g),
    .b(dnf_3_b), .c(dnf_3_c), .e(dnf_3_e), .d(dnf_3_d));
  LED led_197 (.in(dnf_3_f));
  LED led_198 (.in(dnf_3_g));
  LED led_199 (.in(dnf_3_g));
  LED led_200 (.in(dnf_3_e));
  LED led_201 (.in(dnf_3_e));
  LED led_202 (.in(dnf_3_e));
  LED led_203 (.in(dnf_3_d));
  LED led_204 (.in(dnf_3_d));
  HYB hyb_3 (
    .x0(in_12[0]), .x1(in_12[1]), .x2(in_12[2]), .x3(in_12[3]), .a(hyb_3_a), .f(hyb_3_f), .g(hyb_3_g),
    .b(hyb_3_b), .c(hyb_3_c), .e(hyb_3_e), .d(hyb_3_d));
  LED led_205 (.in(dnf_4_a));
  LED led_206 (.in(dnf_4_a));
  LED led_207 (.in(dnf_4_f));
  LED led_208 (.in(dnf_4_f));
  DNF dnf_4 (
    .x0(in_14[0]), .x1(in_14[1]), .x2(in_14[2]), .x3(in_14[3]), .a(dnf_4_a), .f(dnf_4_f), .g(dnf_4_g),
    .b(dnf_4_b), .c(dnf_4_c), .e(dnf_4_e), .d(dnf_4_d));
  LED led_209 (.in(dnf_4_f));
  LED led_210 (.in(dnf_4_g));
  LED led_211 (.in(dnf_4_g));
  LED led_212 (.in(dnf_4_e));
  LED led_213 (.in(dnf_4_e));
  LED led_214 (.in(dnf_4_e));
  LED led_215 (.in(dnf_4_d));
  LED led_216 (.in(dnf_4_d));
  HYB hyb_4 (
    .x0(in_14[0]), .x1(in_14[1]), .x2(in_14[2]), .x3(in_14[3]), .a(hyb_4_a), .f(hyb_4_f), .g(hyb_4_g),
    .b(hyb_4_b), .c(hyb_4_c), .e(hyb_4_e), .d(hyb_4_d));
  LED led_217 (.in(dnf_5_a));
  LED led_218 (.in(dnf_5_a));
  LED led_219 (.in(dnf_5_f));
  LED led_220 (.in(dnf_5_f));
  DNF dnf_5 (
    .x0(in_16[0]), .x1(in_16[1]), .x2(in_16[2]), .x3(in_16[3]), .a(dnf_5_a), .f(dnf_5_f), .g(dnf_5_g),
    .b(dnf_5_b), .c(dnf_5_c), .e(dnf_5_e), .d(dnf_5_d));
  LED led_221 (.in(dnf_5_f));
  LED led_222 (.in(dnf_5_g));
  LED led_223 (.in(dnf_5_g));
  LED led_224 (.in(dnf_5_e));
  LED led_225 (.in(dnf_5_e));
  LED led_226 (.in(dnf_5_e));
  LED led_227 (.in(dnf_5_d));
  LED led_228 (.in(dnf_5_d));
  HYB hyb_5 (
    .x0(in_16[0]), .x1(in_16[1]), .x2(in_16[2]), .x3(in_16[3]), .a(hyb_5_a), .f(hyb_5_f), .g(hyb_5_g),
    .b(hyb_5_b), .c(hyb_5_c), .e(hyb_5_e), .d(hyb_5_d));
  LED led_229 (.in(dnf_1_a));
  LED led_230 (.in(dnf_1_b));
  LED led_231 (.in(dnf_1_b));
  LED led_232 (.in(dnf_1_b));
  LED led_233 (.in(dnf_1_g));
  LED led_234 (.in(dnf_1_c));
  LED led_235 (.in(dnf_1_c));
  LED led_236 (.in(hyb_1_a));
  LED led_237 (.in(dnf_1_c));
  LED led_238 (.in(hyb_1_f));
  LED led_239 (.in(dnf_1_d));
  LED led_240 (.in(hyb_1_f));
  LED led_241 (.in(hyb_1_f));
  LED led_242 (.in(hyb_1_g));
  LED led_243 (.in(hyb_1_e));
  LED led_244 (.in(dnf_2_a));
  LED led_245 (.in(hyb_1_e));
  LED led_246 (.in(hyb_1_e));
  LED led_247 (.in(dnf_2_b));
  LED led_248 (.in(dnf_2_b));
  LED led_249 (.in(hyb_1_d));
  LED led_250 (.in(dnf_2_b));
  LED led_251 (.in(dnf_2_g));
  LED led_252 (.in(dnf_2_c));
  LED led_253 (.in(dnf_2_c));
  LED led_254 (.in(hyb_2_a));
  LED led_255 (.in(dnf_2_c));
  LED led_256 (.in(hyb_2_f));
  LED led_257 (.in(dnf_2_d));
  LED led_258 (.in(hyb_2_f));
  LED led_259 (.in(hyb_2_f));
  LED led_260 (.in(hyb_2_g));
  LED led_261 (.in(hyb_2_e));
  LED led_262 (.in(dnf_3_a));
  LED led_263 (.in(hyb_2_e));
  LED led_264 (.in(hyb_2_e));
  LED led_265 (.in(dnf_3_b));
  LED led_266 (.in(dnf_3_b));
  LED led_267 (.in(hyb_2_d));
  LED led_268 (.in(dnf_3_b));
  LED led_269 (.in(dnf_3_g));
  LED led_270 (.in(dnf_3_c));
  LED led_271 (.in(dnf_3_c));
  LED led_272 (.in(hyb_3_a));
  LED led_273 (.in(dnf_3_c));
  LED led_274 (.in(hyb_3_f));
  LED led_275 (.in(dnf_3_d));
  LED led_276 (.in(hyb_3_f));
  LED led_277 (.in(hyb_3_f));
  LED led_278 (.in(hyb_3_g));
  LED led_279 (.in(hyb_3_e));
  LED led_280 (.in(dnf_4_a));
  LED led_281 (.in(hyb_3_e));
  LED led_282 (.in(hyb_3_e));
  LED led_283 (.in(dnf_4_b));
  LED led_284 (.in(dnf_4_b));
  LED led_285 (.in(hyb_3_d));
  LED led_286 (.in(dnf_4_b));
  LED led_287 (.in(dnf_4_g));
  LED led_288 (.in(dnf_4_c));
  LED led_289 (.in(dnf_4_c));
  LED led_290 (.in(hyb_4_a));
  LED led_291 (.in(dnf_4_c));
  LED led_292 (.in(hyb_4_f));
  LED led_293 (.in(dnf_4_d));
  LED led_294 (.in(hyb_4_f));
  LED led_295 (.in(hyb_4_f));
  LED led_296 (.in(hyb_4_g));
  LED led_297 (.in(hyb_4_e));
  LED led_298 (.in(dnf_5_a));
  LED led_299 (.in(hyb_4_e));
  LED led_300 (.in(hyb_4_e));
  LED led_301 (.in(dnf_5_b));
  LED led_302 (.in(dnf_5_b));
  LED led_303 (.in(hyb_4_d));
  LED led_304 (.in(dnf_5_b));
  LED led_305 (.in(dnf_5_g));
  LED led_306 (.in(dnf_5_c));
  LED led_307 (.in(dnf_5_c));
  LED led_308 (.in(hyb_5_a));
  LED led_309 (.in(dnf_5_c));
  LED led_310 (.in(hyb_5_f));
  LED led_311 (.in(dnf_5_d));
  LED led_312 (.in(hyb_5_f));
  LED led_313 (.in(hyb_5_f));
  LED led_314 (.in(hyb_5_g));
  LED led_315 (.in(hyb_5_e));
  LED led_316 (.in(hyb_5_e));
  LED led_317 (.in(hyb_5_e));
  LED led_318 (.in(hyb_5_d));
  LED led_319 (.in(hyb_1_a));
  LED led_320 (.in(hyb_1_a));
  LED led_321 (.in(hyb_1_b));
  LED led_322 (.in(hyb_1_b));
  LED led_323 (.in(hyb_1_b));
  LED led_324 (.in(hyb_1_g));
  LED led_325 (.in(hyb_1_g));
  LED led_326 (.in(hyb_1_c));
  LED led_327 (.in(hyb_1_c));
  LED led_328 (.in(hyb_1_c));
  LED led_329 (.in(hyb_1_d));
  LED led_330 (.in(hyb_1_d));
  LED led_331 (.in(hyb_2_a));
  LED led_332 (.in(hyb_2_a));
  LED led_333 (.in(hyb_2_b));
  LED led_334 (.in(hyb_2_b));
  LED led_335 (.in(hyb_2_b));
  LED led_336 (.in(hyb_2_g));
  LED led_337 (.in(hyb_2_g));
  LED led_338 (.in(hyb_2_c));
  LED led_339 (.in(hyb_2_c));
  LED led_340 (.in(hyb_2_c));
  LED led_341 (.in(hyb_2_d));
  LED led_342 (.in(hyb_2_d));
  LED led_343 (.in(hyb_3_a));
  LED led_344 (.in(hyb_3_a));
  LED led_345 (.in(hyb_3_b));
  LED led_346 (.in(hyb_3_b));
  LED led_347 (.in(hyb_3_b));
  LED led_348 (.in(hyb_3_g));
  LED led_349 (.in(hyb_3_g));
  LED led_350 (.in(hyb_3_c));
  LED led_351 (.in(hyb_3_c));
  LED led_352 (.in(hyb_3_c));
  LED led_353 (.in(hyb_3_d));
  LED led_354 (.in(hyb_3_d));
  LED led_355 (.in(hyb_4_a));
  LED led_356 (.in(hyb_4_a));
  LED led_357 (.in(hyb_4_b));
  LED led_358 (.in(hyb_4_b));
  LED led_359 (.in(hyb_4_b));
  LED led_360 (.in(hyb_4_g));
  LED led_361 (.in(hyb_4_g));
  LED led_362 (.in(hyb_4_c));
  LED led_363 (.in(hyb_4_c));
  LED led_364 (.in(hyb_4_c));
  LED led_365 (.in(hyb_4_d));
  LED led_366 (.in(hyb_4_d));
  LED led_367 (.in(hyb_5_a));
  LED led_368 (.in(hyb_5_a));
  LED led_369 (.in(hyb_5_b));
  LED led_370 (.in(hyb_5_b));
  LED led_371 (.in(hyb_5_b));
  LED led_372 (.in(hyb_5_g));
  LED led_373 (.in(hyb_5_g));
  LED led_374 (.in(hyb_5_c));
  LED led_375 (.in(hyb_5_c));
  LED led_376 (.in(hyb_5_c));
  LED led_377 (.in(hyb_5_d));
  LED led_378 (.in(hyb_5_d));
  LED led_379 (.in(dnf_6_a));
  LED led_380 (.in(dnf_6_a));
  LED led_381 (.in(dnf_6_f));
  LED led_382 (.in(dnf_6_f));
  DNF dnf_6 (
    .x0(in_5[0]), .x1(in_5[1]), .x2(in_5[2]), .x3(in_5[3]), .a(dnf_6_a), .f(dnf_6_f), .g(dnf_6_g),
    .b(dnf_6_b), .c(dnf_6_c), .e(dnf_6_e), .d(dnf_6_d));
  LED led_383 (.in(dnf_6_f));
  LED led_384 (.in(dnf_6_g));
  LED led_385 (.in(dnf_6_g));
  LED led_386 (.in(dnf_6_e));
  LED led_387 (.in(dnf_6_e));
  LED led_388 (.in(dnf_6_e));
  LED led_389 (.in(dnf_6_d));
  LED led_390 (.in(dnf_6_d));
  HYB hyb_6 (
    .x0(in_5[0]), .x1(in_5[1]), .x2(in_5[2]), .x3(in_5[3]), .a(hyb_6_a), .f(hyb_6_f), .g(hyb_6_g),
    .b(hyb_6_b), .c(hyb_6_c), .e(hyb_6_e), .d(hyb_6_d));
  LED led_391 (.in(dnf_7_a));
  LED led_392 (.in(dnf_7_a));
  LED led_393 (.in(dnf_7_f));
  LED led_394 (.in(dnf_7_f));
  DNF dnf_7 (
    .x0(in_11[0]), .x1(in_11[1]), .x2(in_11[2]), .x3(in_11[3]), .a(dnf_7_a), .f(dnf_7_f), .g(dnf_7_g),
    .b(dnf_7_b), .c(dnf_7_c), .e(dnf_7_e), .d(dnf_7_d));
  LED led_395 (.in(dnf_7_f));
  LED led_396 (.in(dnf_7_g));
  LED led_397 (.in(dnf_7_g));
  LED led_398 (.in(dnf_7_e));
  LED led_399 (.in(dnf_7_e));
  LED led_400 (.in(dnf_7_e));
  LED led_401 (.in(dnf_7_d));
  LED led_402 (.in(dnf_7_d));
  HYB hyb_7 (
    .x0(in_11[0]), .x1(in_11[1]), .x2(in_11[2]), .x3(in_11[3]), .a(hyb_7_a), .f(hyb_7_f), .g(hyb_7_g),
    .b(hyb_7_b), .c(hyb_7_c), .e(hyb_7_e), .d(hyb_7_d));
  LED led_403 (.in(dnf_8_a));
  LED led_404 (.in(dnf_8_a));
  LED led_405 (.in(dnf_8_f));
  LED led_406 (.in(dnf_8_f));
  DNF dnf_8 (
    .x0(in_13[0]), .x1(in_13[1]), .x2(in_13[2]), .x3(in_13[3]), .a(dnf_8_a), .f(dnf_8_f), .g(dnf_8_g),
    .b(dnf_8_b), .c(dnf_8_c), .e(dnf_8_e), .d(dnf_8_d));
  LED led_407 (.in(dnf_8_f));
  LED led_408 (.in(dnf_8_g));
  LED led_409 (.in(dnf_8_g));
  LED led_410 (.in(dnf_8_e));
  LED led_411 (.in(dnf_8_e));
  LED led_412 (.in(dnf_8_e));
  LED led_413 (.in(dnf_8_d));
  LED led_414 (.in(dnf_8_d));
  HYB hyb_8 (
    .x0(in_13[0]), .x1(in_13[1]), .x2(in_13[2]), .x3(in_13[3]), .a(hyb_8_a), .f(hyb_8_f), .g(hyb_8_g),
    .b(hyb_8_b), .c(hyb_8_c), .e(hyb_8_e), .d(hyb_8_d));
  LED led_415 (.in(dnf_9_a));
  LED led_416 (.in(dnf_9_a));
  LED led_417 (.in(dnf_9_f));
  LED led_418 (.in(dnf_9_f));
  DNF dnf_9 (
    .x0(in_15[0]), .x1(in_15[1]), .x2(in_15[2]), .x3(in_15[3]), .a(dnf_9_a), .f(dnf_9_f), .g(dnf_9_g),
    .b(dnf_9_b), .c(dnf_9_c), .e(dnf_9_e), .d(dnf_9_d));
  LED led_419 (.in(dnf_9_f));
  LED led_420 (.in(dnf_9_g));
  LED led_421 (.in(dnf_9_g));
  LED led_422 (.in(dnf_9_e));
  LED led_423 (.in(dnf_9_e));
  LED led_424 (.in(dnf_9_e));
  LED led_425 (.in(dnf_9_d));
  LED led_426 (.in(dnf_9_d));
  HYB hyb_9 (
    .x0(in_15[0]), .x1(in_15[1]), .x2(in_15[2]), .x3(in_15[3]), .a(hyb_9_a), .f(hyb_9_f), .g(hyb_9_g),
    .b(hyb_9_b), .c(hyb_9_c), .e(hyb_9_e), .d(hyb_9_d));
  LED led_427 (.in(dnf_10_a));
  LED led_428 (.in(dnf_10_a));
  LED led_429 (.in(dnf_10_f));
  LED led_430 (.in(dnf_10_f));
  DNF dnf_10 (
    .x0(in_17[0]), .x1(in_17[1]), .x2(in_17[2]), .x3(in_17[3]), .a(dnf_10_a), .f(dnf_10_f), .g(dnf_10_g),
    .b(dnf_10_b), .c(dnf_10_c), .e(dnf_10_e), .d(dnf_10_d));
  LED led_431 (.in(dnf_10_f));
  LED led_432 (.in(dnf_10_g));
  LED led_433 (.in(dnf_10_g));
  LED led_434 (.in(dnf_10_e));
  LED led_435 (.in(dnf_10_e));
  LED led_436 (.in(dnf_10_e));
  LED led_437 (.in(dnf_10_d));
  LED led_438 (.in(dnf_10_d));
  HYB hyb_10 (
    .x0(in_17[0]), .x1(in_17[1]), .x2(in_17[2]), .x3(in_17[3]), .a(hyb_10_a), .f(hyb_10_f), .g(hyb_10_g),
    .b(hyb_10_b), .c(hyb_10_c), .e(hyb_10_e), .d(hyb_10_d));
  LED led_439 (.in(dnf_6_a));
  LED led_440 (.in(dnf_6_b));
  LED led_441 (.in(dnf_6_b));
  LED led_442 (.in(dnf_6_b));
  LED led_443 (.in(dnf_6_g));
  LED led_444 (.in(dnf_6_c));
  LED led_445 (.in(dnf_6_c));
  LED led_446 (.in(hyb_6_a));
  LED led_447 (.in(dnf_6_c));
  LED led_448 (.in(hyb_6_f));
  LED led_449 (.in(dnf_6_d));
  LED led_450 (.in(hyb_6_f));
  LED led_451 (.in(hyb_6_f));
  LED led_452 (.in(hyb_6_g));
  LED led_453 (.in(hyb_6_e));
  LED led_454 (.in(dnf_7_a));
  LED led_455 (.in(hyb_6_e));
  LED led_456 (.in(hyb_6_e));
  LED led_457 (.in(dnf_7_b));
  LED led_458 (.in(dnf_7_b));
  LED led_459 (.in(hyb_6_d));
  LED led_460 (.in(dnf_7_b));
  LED led_461 (.in(dnf_7_g));
  LED led_462 (.in(dnf_7_c));
  LED led_463 (.in(dnf_7_c));
  LED led_464 (.in(hyb_7_a));
  LED led_465 (.in(dnf_7_c));
  LED led_466 (.in(hyb_7_f));
  LED led_467 (.in(dnf_7_d));
  LED led_468 (.in(hyb_7_f));
  LED led_469 (.in(hyb_7_f));
  LED led_470 (.in(hyb_7_g));
  LED led_471 (.in(hyb_7_e));
  LED led_472 (.in(dnf_8_a));
  LED led_473 (.in(hyb_7_e));
  LED led_474 (.in(hyb_7_e));
  LED led_475 (.in(dnf_8_b));
  LED led_476 (.in(dnf_8_b));
  LED led_477 (.in(hyb_7_d));
  LED led_478 (.in(dnf_8_b));
  LED led_479 (.in(dnf_8_g));
  LED led_480 (.in(dnf_8_c));
  LED led_481 (.in(dnf_8_c));
  LED led_482 (.in(hyb_8_a));
  LED led_483 (.in(dnf_8_c));
  LED led_484 (.in(hyb_8_f));
  LED led_485 (.in(dnf_8_d));
  LED led_486 (.in(hyb_8_f));
  LED led_487 (.in(hyb_8_f));
  LED led_488 (.in(hyb_8_g));
  LED led_489 (.in(hyb_8_e));
  LED led_490 (.in(dnf_9_a));
  LED led_491 (.in(hyb_8_e));
  LED led_492 (.in(hyb_8_e));
  LED led_493 (.in(dnf_9_b));
  LED led_494 (.in(dnf_9_b));
  LED led_495 (.in(hyb_8_d));
  LED led_496 (.in(dnf_9_b));
  LED led_497 (.in(dnf_9_g));
  LED led_498 (.in(dnf_9_c));
  LED led_499 (.in(dnf_9_c));
  LED led_500 (.in(hyb_9_a));
  LED led_501 (.in(dnf_9_c));
  LED led_502 (.in(hyb_9_f));
  LED led_503 (.in(dnf_9_d));
  LED led_504 (.in(hyb_9_f));
  LED led_505 (.in(hyb_9_f));
  LED led_506 (.in(hyb_9_g));
  LED led_507 (.in(hyb_9_e));
  LED led_508 (.in(dnf_10_a));
  LED led_509 (.in(hyb_9_e));
  LED led_510 (.in(hyb_9_e));
  LED led_511 (.in(dnf_10_b));
  LED led_512 (.in(dnf_10_b));
  LED led_513 (.in(hyb_9_d));
  LED led_514 (.in(dnf_10_b));
  LED led_515 (.in(dnf_10_g));
  LED led_516 (.in(dnf_10_c));
  LED led_517 (.in(dnf_10_c));
  LED led_518 (.in(hyb_10_a));
  LED led_519 (.in(dnf_10_c));
  LED led_520 (.in(hyb_10_f));
  LED led_521 (.in(dnf_10_d));
  LED led_522 (.in(hyb_10_f));
  LED led_523 (.in(hyb_10_f));
  LED led_524 (.in(hyb_10_g));
  LED led_525 (.in(hyb_10_e));
  LED led_526 (.in(hyb_10_e));
  LED led_527 (.in(hyb_10_e));
  LED led_528 (.in(hyb_10_d));
  LED led_529 (.in(hyb_6_a));
  LED led_530 (.in(hyb_6_a));
  LED led_531 (.in(hyb_6_b));
  LED led_532 (.in(hyb_6_b));
  LED led_533 (.in(hyb_6_b));
  LED led_534 (.in(hyb_6_g));
  LED led_535 (.in(hyb_6_g));
  LED led_536 (.in(hyb_6_c));
  LED led_537 (.in(hyb_6_c));
  LED led_538 (.in(hyb_6_c));
  LED led_539 (.in(hyb_6_d));
  LED led_540 (.in(hyb_6_d));
  LED led_541 (.in(hyb_7_a));
  LED led_542 (.in(hyb_7_a));
  LED led_543 (.in(hyb_7_b));
  LED led_544 (.in(hyb_7_b));
  LED led_545 (.in(hyb_7_b));
  LED led_546 (.in(hyb_7_g));
  LED led_547 (.in(hyb_7_g));
  LED led_548 (.in(hyb_7_c));
  LED led_549 (.in(hyb_7_c));
  LED led_550 (.in(hyb_7_c));
  LED led_551 (.in(hyb_7_d));
  LED led_552 (.in(hyb_7_d));
  LED led_553 (.in(hyb_8_a));
  LED led_554 (.in(hyb_8_a));
  LED led_555 (.in(hyb_8_b));
  LED led_556 (.in(hyb_8_b));
  LED led_557 (.in(hyb_8_b));
  LED led_558 (.in(hyb_8_g));
  LED led_559 (.in(hyb_8_g));
  LED led_560 (.in(hyb_8_c));
  LED led_561 (.in(hyb_8_c));
  LED led_562 (.in(hyb_8_c));
  LED led_563 (.in(hyb_8_d));
  LED led_564 (.in(hyb_8_d));
  LED led_565 (.in(hyb_9_a));
  LED led_566 (.in(hyb_9_a));
  LED led_567 (.in(hyb_9_b));
  LED led_568 (.in(hyb_9_b));
  LED led_569 (.in(hyb_9_b));
  LED led_570 (.in(hyb_9_g));
  LED led_571 (.in(hyb_9_g));
  LED led_572 (.in(hyb_9_c));
  LED led_573 (.in(hyb_9_c));
  LED led_574 (.in(hyb_9_c));
  LED led_575 (.in(hyb_9_d));
  LED led_576 (.in(hyb_9_d));
  LED led_577 (.in(hyb_10_a));
  LED led_578 (.in(hyb_10_a));
  LED led_579 (.in(hyb_10_b));
  LED led_580 (.in(hyb_10_b));
  LED led_581 (.in(hyb_10_b));
  LED led_582 (.in(hyb_10_g));
  LED led_583 (.in(hyb_10_g));
  LED led_584 (.in(hyb_10_c));
  LED led_585 (.in(hyb_10_c));
  LED led_586 (.in(hyb_10_c));
  LED led_587 (.in(hyb_10_d));
  LED led_588 (.in(hyb_10_d));

  assign out_18 = a;
  assign out_19 = b;
  assign out_20 = c;
  assign out_21 = d;
  assign out_22 = e;
  assign out_23 = f;
  assign out_24 = g;

  // Notes on the sheet:
  //   dcbafge
  //   dcbafge
  //   cdbafge
  //   bafgedc
  //   abfgecd
  //   afgbced
  //   afgbced
endmodule

module DNF (
  input  x0,
  input  x1,
  input  x2,
  input  x3,
  output a,
  output f,
  output g,
  output b,
  output c,
  output e,
  output d
);

  wire and_1_out, and_2_out, and_3_out, and_4_out, and_5_out, and_6_out, and_7_out, and_8_out, and_9_out,
       and_10_out, and_11_out, and_12_out, and_13_out, and_14_out, and_15_out, and_16_out;

  and and_1 (and_1_out, x0, x2);
  or or_1 (a, x1, x3, and_1_out);
  and and_2 (and_2_out, x0, x1);
  and and_3 (and_3_out, x0, ~x2);  // AND_Gate
  and and_4 (and_4_out, x1, ~x2);  // AND_Gate
  and and_5 (and_5_out, ~x0, ~x1, x2);  // AND_Gate
  or or_2 (b, x3, and_2_out, and_3_out, and_4_out, and_5_out);
  or or_3 (c, x0, x2, x3);
  and and_6 (and_6_out, ~x0, x1);  // AND_Gate
  and and_7 (and_7_out, ~x0, x3);  // AND_Gate
  and and_8 (and_8_out, x1, ~x2);  // AND_Gate
  or or_4 (d, and_6_out, and_7_out, and_8_out, and_9_out);
  and and_9 (and_9_out, x0, ~x1, x2);  // AND_Gate
  and and_10 (and_10_out, ~x0, x1);  // AND_Gate
  and and_11 (and_11_out, ~x0, x3);  // AND_Gate
  or or_5 (e, and_10_out, and_11_out);
  and and_12 (and_12_out, ~x0, x2);  // AND_Gate
  and and_13 (and_13_out, ~x1, x2);  // AND_Gate
  or or_6 (f, x3, and_12_out, and_13_out);
  and and_14 (and_14_out, ~x0, x2);  // AND_Gate
  and and_15 (and_15_out, ~x1, x2);  // AND_Gate
  or or_7 (g, x3, and_14_out, and_15_out, and_16_out);
  and and_16 (and_16_out, x1, ~x2);  // AND_Gate
endmodule

module SHOWCASE (
  input  [3:0] x,
  output Ha,
  output Hf,
  output Da,
  output Hg,
  output Db,
  output Hb,
  output Dg,
  output Hc,
  output Df,
  output He,
  output De,
  output Hd,
  output Dc,
  output Dd
);

  DNF dnf_1 (.x0(x[0]), .x1(x[1]), .x2(x[2]), .x3(x[3]), .a(Da), .f(Df), .g(Dg), .b(Db), .c(Dc), .e(De), .d(Dd));
  HYB hyb_1 (.x0(x[0]), .x1(x[1]), .x2(x[2]), .x3(x[3]), .a(Ha), .f(Hf), .g(Hg), .b(Hb), .c(Hc), .e(He), .d(Hd));
endmodule

module MAYA_IDEA (
  input  in_1,
  input  [3:0] in_2,
  input  [3:0] in_3,
  input  [3:0] in_4,
  input  [3:0] in_5,
  input  [3:0] in_6,
  input  [3:0] in_7,
  input  [3:0] in_8,
  input  [3:0] in_9,
  input  [3:0] in_10,
  input  [3:0] in_11,
  input  [3:0] in_12,
  input  [3:0] in_13,
  input  [3:0] in_14,
  input  [3:0] in_15,
  input  [3:0] in_16,
  input  [3:0] in_17,
  input  in_18,
  input  in_19,
  input  [3:0] in_20,
  input  [3:0] in_21,
  input  [3:0] in_22,
  input  [3:0] in_23,
  input  [3:0] in_24,
  input  [3:0] in_25,
  input  [3:0] in_26,
  output [3:0] out_27,
  output [3:0] out_28
);

  wire undriven, undriven_2, undriven_3, undriven_4, undriven_5, undriven_6, undriven_7, undriven_8,
       undriven_9, undriven_10, undriven_11, undriven_12, undriven_13, undriven_14, undriven_15, undriven_16,
       undriven_17, undriven_18, undriven_19, undriven_20, undriven_21, undriven_22, undriven_23,
       undriven_24, undriven_25, undriven_26, undriven_27, undriven_28, undriven_29, undriven_30,
       undriven_31, undriven_32;

  LED led_1 (.in(undriven));
  LED led_2 (.in(undriven));
  LED led_3 (.in(undriven_3));
  LED led_4 (.in(undriven_3));
  LED led_5 (.in(undriven));
  LED led_6 (.in(undriven));
  LED led_7 (.in(undriven_3));
  LED led_8 (.in(undriven_3));
  LED led_9 (.in(undriven_2));
  LED led_10 (.in(undriven_2));
  LED led_11 (.in(in_1));
  LED led_12 (.in(in_1));
  LED led_13 (.in(undriven_2));
  LED led_14 (.in(undriven_2));
  LED led_15 (.in(in_1));
  LED led_16 (.in(in_1));
  DotMatrix #(.dotshape("circle"), .matrixcols(7), .matrixrows(4)) dotmatrix_1 (
    .col2(in_2), .col3(in_3));  // open: col0, col1, col4, col5, col6
  LED led_17 (.in(undriven_4));
  LED led_18 (.in(undriven_4));
  LED led_19 (.in(undriven_5));
  LED led_20 (.in(undriven_5));
  LED led_21 (.in(undriven_4));
  LED led_22 (.in(undriven_4));
  LED led_23 (.in(undriven_5));
  LED led_24 (.in(undriven_5));
  LED led_25 (.in(undriven_7));
  LED led_26 (.in(undriven_7));
  LED led_27 (.in(in_1));
  LED led_28 (.in(in_1));
  LED led_29 (.in(undriven_7));
  LED led_30 (.in(undriven_7));
  LED led_31 (.in(in_1));
  LED led_32 (.in(in_1));
  assign out_28 = {{3{in_19}}, in_19};  // Bit_Extender bit_extender_1
  LED led_33 (.in(undriven_6));
  LED led_34 (.in(undriven_6));
  LED led_35 (.in(undriven_8));
  LED led_36 (.in(undriven_8));
  LED led_37 (.in(undriven_6));
  LED led_38 (.in(undriven_6));
  LED led_39 (.in(undriven_8));
  LED led_40 (.in(undriven_8));
  LED led_41 (.in(undriven_7));
  LED led_42 (.in(undriven_7));
  LED led_43 (.in(undriven_9));
  LED led_44 (.in(undriven_9));
  LED led_45 (.in(undriven_7));
  LED led_46 (.in(undriven_7));
  LED led_47 (.in(undriven_9));
  LED led_48 (.in(undriven_9));
  LED led_49 (.in(undriven_10));
  LED led_50 (.in(undriven_10));
  LED led_51 (.in(undriven_10));
  LED led_52 (.in(undriven_10));
  LED led_53 (.in(undriven_11));
  LED led_54 (.in(undriven_11));
  LED led_55 (.in(undriven_11));
  LED led_56 (.in(undriven_11));
  LED led_57 (.in(in_11[0]));
  LED led_58 (.in(in_11[0]));
  LED led_59 (.in(in_12[0]));
  LED led_60 (.in(in_12[0]));
  LED led_61 (.in(in_11[0]));
  LED led_62 (.in(in_11[0]));
  LED led_63 (.in(in_12[0]));
  LED led_64 (.in(in_12[0]));
  LED led_65 (.in(in_11[1]));
  LED led_66 (.in(in_11[1]));
  LED led_67 (.in(in_12[1]));
  LED led_68 (.in(in_12[1]));
  LED led_69 (.in(in_11[1]));
  LED led_70 (.in(in_11[1]));
  LED led_71 (.in(in_12[1]));
  LED led_72 (.in(in_12[1]));
  LED led_73 (.in(in_11[2]));
  LED led_74 (.in(in_11[2]));
  LED led_75 (.in(in_12[2]));
  LED led_76 (.in(in_12[2]));
  LED led_77 (.in(in_11[2]));
  LED led_78 (.in(in_11[2]));
  LED led_79 (.in(in_12[2]));
  LED led_80 (.in(in_12[2]));
  LED led_81 (.in(in_11[3]));
  LED led_82 (.in(in_11[3]));
  LED led_83 (.in(in_12[3]));
  LED led_84 (.in(in_12[3]));
  LED led_85 (.in(in_11[3]));
  LED led_86 (.in(in_11[3]));
  LED led_87 (.in(in_12[3]));
  LED led_88 (.in(in_12[3]));
  LED led_89 (.in(in_13[0]));
  LED led_90 (.in(in_13[0]));
  LED led_91 (.in(in_14[0]));
  LED led_92 (.in(in_14[0]));
  LED led_93 (.in(in_13[0]));
  LED led_94 (.in(in_13[0]));
  LED led_95 (.in(in_14[0]));
  LED led_96 (.in(in_14[0]));
  LED led_97 (.in(in_13[1]));
  LED led_98 (.in(in_13[1]));
  LED led_99 (.in(in_14[1]));
  LED led_100 (.in(in_14[1]));
  LED led_101 (.in(in_13[1]));
  LED led_102 (.in(in_13[1]));
  LED led_103 (.in(in_14[1]));
  LED led_104 (.in(in_14[1]));
  LED led_105 (.in(in_13[2]));
  LED led_106 (.in(in_13[2]));
  LED led_107 (.in(in_14[2]));
  LED led_108 (.in(in_14[2]));
  LED led_109 (.in(in_13[2]));
  LED led_110 (.in(in_13[2]));
  LED led_111 (.in(in_14[2]));
  LED led_112 (.in(in_14[2]));
  LED led_113 (.in(in_13[3]));
  LED led_114 (.in(in_13[3]));
  LED led_115 (.in(in_14[3]));
  LED led_116 (.in(in_14[3]));
  LED led_117 (.in(in_13[3]));
  LED led_118 (.in(in_13[3]));
  LED led_119 (.in(in_14[3]));
  LED led_120 (.in(in_14[3]));
  LED led_121 (.in(in_16[0]));
  LED led_122 (.in(in_16[0]));
  LED led_123 (.in(in_15[0]));
  LED led_124 (.in(in_15[0]));
  LED led_125 (.in(in_16[0]));
  LED led_126 (.in(in_16[0]));
  LED led_127 (.in(in_15[0]));
  LED led_128 (.in(in_15[0]));
  LED led_129 (.in(in_16[1]));
  LED led_130 (.in(in_16[1]));
  LED led_131 (.in(in_15[1]));
  LED led_132 (.in(in_15[1]));
  LED led_133 (.in(in_16[1]));
  LED led_134 (.in(in_16[1]));
  LED led_135 (.in(in_15[1]));
  LED led_136 (.in(in_15[1]));
  LED led_137 (.in(in_16[2]));
  LED led_138 (.in(in_16[2]));
  LED led_139 (.in(in_15[2]));
  LED led_140 (.in(in_15[2]));
  LED led_141 (.in(in_16[2]));
  LED led_142 (.in(in_16[2]));
  LED led_143 (.in(in_15[2]));
  LED led_144 (.in(in_15[2]));
  LED led_145 (.in(in_16[3]));
  LED led_146 (.in(in_16[3]));
  LED led_147 (.in(in_15[3]));
  LED led_148 (.in(in_15[3]));
  LED led_149 (.in(in_16[3]));
  LED led_150 (.in(in_16[3]));
  LED led_151 (.in(in_15[3]));
  LED led_152 (.in(in_15[3]));
  LED led_153 (.in(undriven_15));
  LED led_154 (.in(undriven_15));
  LED led_155 (.in(undriven_12));
  LED led_156 (.in(undriven_12));
  LED led_157 (.in(undriven_15));
  LED led_158 (.in(undriven_15));
  LED led_159 (.in(undriven_12));
  LED led_160 (.in(undriven_12));
  LED led_161 (.in(undriven_16));
  LED led_162 (.in(undriven_16));
  LED led_163 (.in(undriven_13));
  LED led_164 (.in(undriven_13));
  LED led_165 (.in(undriven_16));
  LED led_166 (.in(undriven_16));
  LED led_167 (.in(undriven_13));
  LED led_168 (.in(undriven_13));
  LED led_169 (.in(undriven_17));
  LED led_170 (.in(undriven_17));
  LED led_171 (.in(undriven_14));
  LED led_172 (.in(undriven_14));
  LED led_173 (.in(undriven_17));
  LED led_174 (.in(undriven_17));
  LED led_175 (.in(undriven_14));
  LED led_176 (.in(undriven_14));
  LED led_177 (.in(in_21[3]));
  LED led_178 (.in(in_21[3]));
  LED led_179 (.in(in_20[3]));
  LED led_180 (.in(in_20[3]));
  LED led_181 (.in(in_21[3]));
  LED led_182 (.in(in_21[3]));
  LED led_183 (.in(in_20[3]));
  LED led_184 (.in(in_20[3]));
  LED led_185 (.in(in_17[0]));
  LED led_186 (.in(in_17[0]));
  LED led_187 (.in(in_17[0]));
  LED led_188 (.in(in_17[0]));
  LED led_189 (.in(in_17[1]));
  LED led_190 (.in(in_17[1]));
  LED led_191 (.in(in_17[1]));
  LED led_192 (.in(in_17[1]));
  LED led_193 (.in(in_17[2]));
  LED led_194 (.in(in_17[2]));
  LED led_195 (.in(in_17[2]));
  LED led_196 (.in(in_17[2]));
  LED led_197 (.in(in_17[3]));
  LED led_198 (.in(in_17[3]));
  LED led_199 (.in(in_17[3]));
  LED led_200 (.in(in_17[3]));
  LED led_201 (.in(undriven_18));
  LED led_202 (.in(undriven_18));
  LED led_203 (.in(undriven_21));
  LED led_204 (.in(undriven_21));
  LED led_205 (.in(undriven_18));
  LED led_206 (.in(undriven_18));
  LED led_207 (.in(undriven_21));
  LED led_208 (.in(undriven_21));
  LED led_209 (.in(undriven_19));
  LED led_210 (.in(undriven_19));
  LED led_211 (.in(undriven_22));
  LED led_212 (.in(undriven_22));
  LED led_213 (.in(undriven_19));
  LED led_214 (.in(undriven_19));
  LED led_215 (.in(undriven_22));
  LED led_216 (.in(undriven_22));
  LED led_217 (.in(undriven_20));
  LED led_218 (.in(undriven_20));
  LED led_219 (.in(undriven_23));
  LED led_220 (.in(undriven_23));
  LED led_221 (.in(undriven_20));
  LED led_222 (.in(undriven_20));
  LED led_223 (.in(undriven_23));
  LED led_224 (.in(undriven_23));
  LED led_225 (.in(in_22[3]));
  LED led_226 (.in(in_22[3]));
  LED led_227 (.in(in_23[3]));
  LED led_228 (.in(in_23[3]));
  LED led_229 (.in(in_22[3]));
  LED led_230 (.in(in_22[3]));
  LED led_231 (.in(in_23[3]));
  LED led_232 (.in(in_23[3]));
  LED led_233 (.in(in_4[3]));
  LED led_234 (.in(in_4[3]));
  LED led_235 (.in(in_4[3]));
  LED led_236 (.in(in_4[3]));
  LED led_237 (.in(in_4[2]));
  LED led_238 (.in(in_4[2]));
  LED led_239 (.in(in_4[2]));
  LED led_240 (.in(in_4[2]));
  LED led_241 (.in(in_4[1]));
  LED led_242 (.in(in_4[1]));
  LED led_243 (.in(in_4[1]));
  LED led_244 (.in(in_4[1]));
  LED led_245 (.in(in_4[0]));
  LED led_246 (.in(in_4[0]));
  LED led_247 (.in(in_4[0]));
  LED led_248 (.in(in_4[0]));
  LED led_249 (.in(undriven_24));
  LED led_250 (.in(undriven_24));
  LED led_251 (.in(undriven_27));
  LED led_252 (.in(undriven_27));
  LED led_253 (.in(undriven_24));
  LED led_254 (.in(undriven_24));
  LED led_255 (.in(undriven_27));
  LED led_256 (.in(undriven_27));
  LED led_257 (.in(undriven_25));
  LED led_258 (.in(undriven_25));
  LED led_259 (.in(undriven_28));
  LED led_260 (.in(undriven_28));
  LED led_261 (.in(undriven_25));
  LED led_262 (.in(undriven_25));
  LED led_263 (.in(undriven_28));
  LED led_264 (.in(undriven_28));
  LED led_265 (.in(undriven_26));
  LED led_266 (.in(undriven_26));
  LED led_267 (.in(undriven_29));
  LED led_268 (.in(undriven_29));
  LED led_269 (.in(undriven_26));
  LED led_270 (.in(undriven_26));
  LED led_271 (.in(undriven_29));
  LED led_272 (.in(undriven_29));
  LED led_273 (.in(in_24[3]));
  LED led_274 (.in(in_24[3]));
  LED led_275 (.in(in_25[3]));
  LED led_276 (.in(in_25[3]));
  LED led_277 (.in(in_24[3]));
  LED led_278 (.in(in_24[3]));
  LED led_279 (.in(in_25[3]));
  LED led_280 (.in(in_25[3]));
  LED led_281 (.in(in_5[3]));
  LED led_282 (.in(in_5[3]));
  LED led_283 (.in(in_6[3]));
  LED led_284 (.in(in_6[3]));
  LED led_285 (.in(in_5[3]));
  LED led_286 (.in(in_5[3]));
  LED led_287 (.in(in_6[3]));
  LED led_288 (.in(in_6[3]));
  LED led_289 (.in(in_5[2]));
  LED led_290 (.in(in_5[2]));
  LED led_291 (.in(in_6[2]));
  LED led_292 (.in(in_6[2]));
  LED led_293 (.in(in_5[2]));
  LED led_294 (.in(in_5[2]));
  LED led_295 (.in(in_6[2]));
  LED led_296 (.in(in_6[2]));
  LED led_297 (.in(in_5[1]));
  LED led_298 (.in(in_5[1]));
  LED led_299 (.in(in_6[1]));
  LED led_300 (.in(in_6[1]));
  LED led_301 (.in(in_5[1]));
  LED led_302 (.in(in_5[1]));
  LED led_303 (.in(in_6[1]));
  LED led_304 (.in(in_6[1]));
  LED led_305 (.in(in_5[0]));
  LED led_306 (.in(in_5[0]));
  LED led_307 (.in(in_6[0]));
  LED led_308 (.in(in_6[0]));
  LED led_309 (.in(in_5[0]));
  LED led_310 (.in(in_5[0]));
  LED led_311 (.in(in_6[0]));
  LED led_312 (.in(in_6[0]));
  LED led_313 (.in(undriven_30));
  LED led_314 (.in(undriven_30));
  LED led_315 (.in(undriven_30));
  LED led_316 (.in(undriven_30));
  LED led_317 (.in(undriven_31));
  LED led_318 (.in(undriven_31));
  LED led_319 (.in(undriven_31));
  LED led_320 (.in(undriven_31));
  LED led_321 (.in(undriven_32));
  LED led_322 (.in(undriven_32));
  LED led_323 (.in(undriven_32));
  LED led_324 (.in(undriven_32));
  LED led_325 (.in(in_26[3]));
  LED led_326 (.in(in_26[3]));
  LED led_327 (.in(in_26[3]));
  LED led_328 (.in(in_26[3]));
  LED led_329 (.in(in_7[3]));
  LED led_330 (.in(in_7[3]));
  LED led_331 (.in(in_8[3]));
  LED led_332 (.in(in_8[3]));
  LED led_333 (.in(in_7[3]));
  LED led_334 (.in(in_7[3]));
  LED led_335 (.in(in_8[3]));
  LED led_336 (.in(in_8[3]));
  LED led_337 (.in(in_7[2]));
  LED led_338 (.in(in_7[2]));
  LED led_339 (.in(in_8[2]));
  LED led_340 (.in(in_8[2]));
  LED led_341 (.in(in_7[2]));
  LED led_342 (.in(in_7[2]));
  LED led_343 (.in(in_8[2]));
  LED led_344 (.in(in_8[2]));
  LED led_345 (.in(in_7[1]));
  LED led_346 (.in(in_7[1]));
  LED led_347 (.in(in_8[1]));
  LED led_348 (.in(in_8[1]));
  LED led_349 (.in(in_7[1]));
  LED led_350 (.in(in_7[1]));
  LED led_351 (.in(in_8[1]));
  LED led_352 (.in(in_8[1]));
  LED led_353 (.in(in_7[0]));
  LED led_354 (.in(in_7[0]));
  LED led_355 (.in(in_8[0]));
  LED led_356 (.in(in_8[0]));
  LED led_357 (.in(in_7[0]));
  LED led_358 (.in(in_7[0]));
  LED led_359 (.in(in_8[0]));
  LED led_360 (.in(in_8[0]));
  LED led_361 (.in(in_9[3]));
  LED led_362 (.in(in_9[3]));
  LED led_363 (.in(in_10[3]));
  LED led_364 (.in(in_10[3]));
  LED led_365 (.in(in_9[3]));
  LED led_366 (.in(in_9[3]));
  LED led_367 (.in(in_10[3]));
  LED led_368 (.in(in_10[3]));
  LED led_369 (.in(in_9[2]));
  LED led_370 (.in(in_9[2]));
  LED led_371 (.in(in_10[2]));
  LED led_372 (.in(in_10[2]));
  LED led_373 (.in(in_9[2]));
  LED led_374 (.in(in_9[2]));
  LED led_375 (.in(in_10[2]));
  LED led_376 (.in(in_10[2]));
  LED led_377 (.in(in_9[1]));
  LED led_378 (.in(in_9[1]));
  LED led_379 (.in(in_10[1]));
  LED led_380 (.in(in_10[1]));
  LED led_381 (.in(in_9[1]));
  LED led_382 (.in(in_9[1]));
  LED led_383 (.in(in_10[1]));
  LED led_384 (.in(in_10[1]));
  LED led_385 (.in(in_9[0]));
  LED led_386 (.in(in_9[0]));
  LED led_387 (.in(in_10[0]));
  LED led_388 (.in(in_10[0]));
  LED led_389 (.in(in_9[0]));
  LED led_390 (.in(in_9[0]));
  LED led_391 (.in(in_10[0]));
  LED led_392 (.in(in_10[0]));

  assign out_27 = {4{in_18}};
endmodule
