// Logisim project sum.circ as structural Verilog
module semi (
  input  in_1,
  input  in_2,
  output s,
  output Cout
);

  wire and_2_out, and_3_out;

  and and_1 (Cout, in_2, in_1);
  and and_2 (and_2_out, ~in_2, in_1);  // AND_Gate
  and and_3 (and_3_out, in_2, ~in_1);  // AND_Gate
  or or_1 (s, and_3_out, and_2_out);

  // Notes on the sheet:
  //   Semisumador de 1 bit
endmodule

module sum_1bit (
  input  Cin,
  input  in_2,
  input  in_3,
  output s,
  output Cout
);

  wire semi_1_cout, semi_1_s, semi_2_cout;

  semi semi_1 (.in_1(in_3), .in_2(in_2), .s(semi_1_s), .Cout(semi_1_cout));
  semi semi_2 (.in_1(Cin), .in_2(semi_1_s), .s(s), .Cout(semi_2_cout));
  or or_1 (Cout, semi_2_cout, semi_1_cout);

  // Notes on the sheet:
  //   Sumador completo de 1 bit
endmodule

module sum_2bit (
  input  Cin,
  input  [1:0] in_2,
  input  [1:0] in_3,
  output [1:0] s,
  output Cout
);

  wire sum_1bit_1_cout;

  sum_1bit sum_1bit_1 (.Cin(Cin), .in_2(in_3[0]), .in_3(in_2[0]), .s(s[0]), .Cout(sum_1bit_1_cout));
  sum_1bit sum_1bit_2 (.Cin(sum_1bit_1_cout), .in_2(in_3[1]), .in_3(in_2[1]), .s(s[1]), .Cout(Cout));

  // Notes on the sheet:
  //   Sumador completo de 2 bits
endmodule

module sum_4bit (
  input  Cin,
  input  [3:0] in_2,
  input  [3:0] in_3,
  output [3:0] s,
  output Cout
);

  wire sum_2bit_1_cout;

  sum_2bit sum_2bit_1 (.Cin(Cin), .in_2(in_3[1:0]), .in_3(in_2[1:0]), .s(s[1:0]), .Cout(sum_2bit_1_cout));
  sum_2bit sum_2bit_2 (.Cin(sum_2bit_1_cout), .in_2(in_3[3:2]), .in_3(in_2[3:2]), .s(s[3:2]), .Cout(Cout));

  // Notes on the sheet:
  //   Sumador completo de 4 bits
endmodule

module sum_8bit (
  input  Cin,
  input  [7:0] in_2,
  input  [7:0] in_3,
  output [7:0] s,
  output Cout
);

  wire sum_4bit_1_cout;

  sum_4bit sum_4bit_1 (.Cin(Cin), .in_2(in_3[3:0]), .in_3(in_2[3:0]), .s(s[3:0]), .Cout(sum_4bit_1_cout));
  sum_4bit sum_4bit_2 (.Cin(sum_4bit_1_cout), .in_2(in_3[7:4]), .in_3(in_2[7:4]), .s(s[7:4]), .Cout(Cout));

  // Notes on the sheet:
  //   Sumador completo de 8 bits
endmodule

module pruebas (
  input  in_1,
  input  [7:0] in_2,
  input  [7:0] in_3,
  output [8:0] out_4
);

  sum_8bit sum_8bit_1 (.Cin(in_1), .in_2(in_3), .in_3(in_2), .s(out_4[7:0]), .Cout(out_4[8]));

  // Notes on the sheet:
  //   Representación de leds con 8 bits
endmodule

module sum_4c1 (
  input  Cin,
  input  [3:0] in_2,
  input  [3:0] in_3,
  output [3:0] s,
  output Cout
);

  wire sum_1bit_1_cout, sum_1bit_2_cout, sum_1bit_3_cout;

  sum_1bit sum_1bit_1 (.Cin(Cin), .in_2(in_3[0]), .in_3(in_2[0]), .s(s[0]), .Cout(sum_1bit_1_cout));
  sum_1bit sum_1bit_2 (.Cin(sum_1bit_1_cout), .in_2(in_3[1]), .in_3(in_2[1]), .s(s[1]), .Cout(sum_1bit_2_cout));
  sum_1bit sum_1bit_3 (.Cin(sum_1bit_2_cout), .in_2(in_3[2]), .in_3(in_2[2]), .s(s[2]), .Cout(sum_1bit_3_cout));
  sum_1bit sum_1bit_4 (.Cin(sum_1bit_3_cout), .in_2(in_3[3]), .in_3(in_2[3]), .s(s[3]), .Cout(Cout));

  // Notes on the sheet:
  //   Sumador completo de 4 bits usando sumadores completos de 1 bit
endmodule

module sum_2 (
  input  [1:0] b,
  input  [1:0] a,
  output [1:0] s,
  output Cout
);

  wire and_1_out, and_2_out, and_3_out, and_4_out, and_5_out, and_6_out, and_7_out, and_8_out, and_9_out,
       and_10_out, and_11_out;

  and and_1 (and_1_out, ~a[0], b[0]);  // AND_Gate
  or or_1 (s[0], and_1_out, and_2_out);
  and and_2 (and_2_out, a[0], ~b[0]);  // AND_Gate
  and and_3 (and_3_out, a[1], ~b[0], ~b[1]);  // AND_Gate
  and and_4 (and_4_out, ~a[0], ~a[1], b[1]);  // AND_Gate
  and and_5 (and_5_out, ~a[0], a[1], ~b[1]);  // AND_Gate
  and and_6 (and_6_out, a[0], a[1], b[0], b[1]);
  and and_7 (and_7_out, a[0], ~a[1], ~b[0], b[1]);  // AND_Gate
  and and_8 (and_8_out, a[0], ~a[1], b[0], ~b[1]);  // AND_Gate
  and and_9 (and_9_out, a[1], b[1]);
  and and_10 (and_10_out, a[0], a[1], b[0]);
  or or_2 (Cout, and_9_out, and_10_out, and_11_out);
  and and_11 (and_11_out, a[0], b[0], b[1]);
  or or_3 (s[1], and_3_out, and_4_out, and_5_out, and_6_out, and_7_out, and_8_out);

  // Notes on the sheet:
  //   Sumador de 2 bits con Karnaugh
endmodule

module sum_4bit_2 (
  input  Cin,
  input  [3:0] in_2,
  input  [3:0] in_3,
  output [3:0] s,
  output Cout
);

  wire sum_2bit_1_cout;

  sum_2bit sum_2bit_1 (.Cin(Cin), .in_2(in_2[1:0]), .in_3(in_3[1:0]), .s(s[1:0]), .Cout(sum_2bit_1_cout));
  sum_2bit sum_2bit_2 (.Cin(sum_2bit_1_cout), .in_2(in_2[3:2]), .in_3(in_3[3:2]), .s(s[3:2]), .Cout(Cout));
endmodule
