// Logisim project sum_classic.circ as structural Verilog
module HA_1bit (
  input  a,
  input  b,
  output s,
  output Cout
);

  wire and_1_out, and_2_out;

  and and_1 (and_1_out, ~a, b);  // AND_Gate
  or or_1 (s, and_1_out, and_2_out);
  and and_2 (and_2_out, a, ~b);  // AND_Gate
  and and_3 (Cout, a, b);

  // Notes on the sheet:
  //   Semisumador de 1 bit
endmodule

module FA_1bit (
  input  Cin,
  input  a,
  input  b,
  output s,
  output Cout
);

  wire HA_1_cout, HA_1_s, HA_2_cout;

  HA_1bit HA_1 (.a(a), .b(b), .s(HA_1_s), .Cout(HA_1_cout));
  HA_1bit HA_2 (.a(Cin), .b(HA_1_s), .s(s), .Cout(HA_2_cout));
  or or_1 (Cout, HA_2_cout, HA_1_cout);

  // Notes on the sheet:
  //   Sumador completo de 1 bit
endmodule

module FA_2bit (
  input  Cin,
  input  [1:0] a,
  input  [1:0] b,
  output [1:0] s,
  output Cout
);

  wire FA_1bit_1_cout;

  FA_1bit FA_1bit_1 (.Cin(Cin), .a(a[0]), .b(b[0]), .s(s[0]), .Cout(FA_1bit_1_cout));
  FA_1bit FA_1bit_2 (.Cin(FA_1bit_1_cout), .a(a[1]), .b(b[1]), .s(s[1]), .Cout(Cout));

  // Notes on the sheet:
  //   Sumador completo de 2 bits
endmodule

module FA_4bit (
  input  Cin,
  input  [3:0] a,
  input  [3:0] b,
  output [3:0] s,
  output Cout
);

  wire FA_2bit_1_cout;

  FA_2bit FA_2bit_1 (.Cin(Cin), .a(a[1:0]), .b(b[1:0]), .s(s[1:0]), .Cout(FA_2bit_1_cout));
  FA_2bit FA_2bit_2 (.Cin(FA_2bit_1_cout), .a(a[3:2]), .b(b[3:2]), .s(s[3:2]), .Cout(Cout));

  // Notes on the sheet:
  //   Sumador completo de 4 bits
endmodule

module FA_8bit (
  input  Cin,
  input  [7:0] a,
  input  [7:0] b,
  output [7:0] s,
  output Cout
);

  wire FA_4bit_1_cout;

  FA_4bit FA_4bit_1 (.Cin(Cin), .a(a[3:0]), .b(b[3:0]), .s(s[3:0]), .Cout(FA_4bit_1_cout));
  FA_4bit FA_4bit_2 (.Cin(FA_4bit_1_cout), .a(a[7:4]), .b(b[7:4]), .s(s[7:4]), .Cout(Cout));

  // Notes on the sheet:
  //   Sumador completo de 8 bits
endmodule

module pruebas (
  input  Cin,
  input  [7:0] a,
  input  [7:0] b,
  output [8:0] s
);

  FA_8bit fa_8bit_1 (.Cin(Cin), .a(a), .b(b), .s(s[7:0]));  // open: Cout

  // Notes on the sheet:
  //   Representación de leds con 8 bits
endmodule

module sum_4c1 (
  input  Cin,
  input  [3:0] a,
  input  [3:0] b,
  output [3:0] s,
  output Cout
);

  wire fa_1bit_1_cout, fa_1bit_2_cout, FA_cout;

  FA_1bit FA (.Cin(Cin), .a(a[0]), .b(b[0]), .s(s[0]), .Cout(FA_cout));
  FA_1bit fa_1bit_1 (.Cin(FA_cout), .a(a[1]), .b(b[1]), .s(s[1]), .Cout(fa_1bit_1_cout));
  FA_1bit fa_1bit_2 (.Cin(fa_1bit_1_cout), .a(a[2]), .b(b[2]), .s(s[2]), .Cout(fa_1bit_2_cout));
  FA_1bit fa_1bit_3 (.Cin(fa_1bit_2_cout), .a(a[3]), .b(b[3]), .s(s[3]), .Cout(Cout));

  // Notes on the sheet:
  //   Sumador completo de 4 bits usando sumadores completos de 1 bit
endmodule

module sum_2 (
  input  [1:0] a,
  input  [1:0] b,
  output [1:0] s,
  output Cout
);

  wire and_1_out, and_2_out, and_3_out, and_4_out, and_5_out, and_6_out, and_7_out, and_8_out, and_9_out,
       and_10_out, and_11_out;

  and and_1 (and_1_out, ~b[0], a[0]);  // AND_Gate
  or or_1 (s[0], and_1_out, and_2_out);
  and and_2 (and_2_out, b[0], ~a[0]);  // AND_Gate
  and and_3 (and_3_out, b[1], ~a[0], ~a[1]);  // AND_Gate
  and and_4 (and_4_out, ~b[0], ~b[1], a[1]);  // AND_Gate
  and and_5 (and_5_out, ~b[0], b[1], ~a[1]);  // AND_Gate
  and and_6 (and_6_out, b[0], b[1], a[0], a[1]);
  and and_7 (and_7_out, b[0], ~b[1], ~a[0], a[1]);  // AND_Gate
  and and_8 (and_8_out, b[0], ~b[1], a[0], ~a[1]);  // AND_Gate
  and and_9 (and_9_out, b[1], a[1]);
  and and_10 (and_10_out, b[0], b[1], a[0]);
  or or_2 (Cout, and_9_out, and_10_out, and_11_out);
  and and_11 (and_11_out, b[0], a[0], a[1]);
  or or_3 (s[1], and_3_out, and_4_out, and_5_out, and_6_out, and_7_out, and_8_out);

  // Notes on the sheet:
  //   Sumador de 2 bits con Karnaugh
endmodule

module resta (
  input  [1:0] minuendo,
  input  [1:0] sustraendo,
  output out_3
);

  FA_2bit fa_2bit_1 (.Cin(1'b1), .a(sustraendo), .b(2'b11), .Cout(out_3));  // open: s
endmodule

module predictor (
  input  Cin,
  input  [7:0] a,
  input  [7:0] b
);
endmodule
