// Logisim project suma.circ as structural Verilog: 1 circuit, main circuit main
module main (
  input  a,
  input  b,
  input  x3,
  input  x2,
  input  x1,
  input  x0,
  input  in_7,
  input  in_8,
  input  in_9,
  input  in_10,
  output out_11,
  output out_12,
  output a_b,
  output out_14,
  output out_15,
  output a_b_2,
  output out_17,
  output out_18
);

  wire and_1_out, and_2_out, and_3_out, and_4_out, and_5_out, and_6_out, and_7_out, and_9_out, and_10_out,
       and_11_out, and_12_out, and_13_out, and_14_out, and_15_out, and_16_out, and_17_out, and_18_out,
       and_19_out, or_1_out, or_2_out, or_3_out, or_4_out, or_5_out, or_6_out;

  and and_1 (and_1_out, ~b, a);  // AND_Gate
  and and_2 (and_2_out, b, ~a);  // AND_Gate
  and dig1 (out_11, b, a);
  or dig0 (out_12, and_1_out, and_2_out);
  and and_3 (and_3_out, ~x0, x2);  // AND_Gate
  and and_4 (and_4_out, x0, ~x2);  // AND_Gate
  or or_1 (or_1_out, x0, x1, x3);
  or or_2 (or_2_out, x1, x2, x3);
  or or_3 (or_3_out, x0, ~x1, ~x3);  // OR_Gate
  or or_4 (or_4_out, ~x1, x2, ~x3);  // OR_Gate
  or or_5 (or_5_out, ~x0, ~x1, ~x2, x3);  // OR_Gate
  or or_6 (or_6_out, x0, x1, ~x2, ~x3);  // OR_Gate
  and and_5 (and_5_out, x1, x3);
  and and_6 (and_6_out, x0, x2, x3);
  and and_7 (and_7_out, x0, x1, x2);
  or or_7 (out_15, and_3_out, and_4_out);
  and and_8 (out_14, or_1_out, or_2_out, or_3_out, or_4_out, or_5_out, or_6_out);
  or or_8 (a_b, and_5_out, and_6_out, and_7_out);
  and and_9 (and_9_out, ~in_10, in_8);  // AND_Gate
  and and_10 (and_10_out, in_10, ~in_8);  // AND_Gate
  and and_11 (and_11_out, in_9, ~in_8, ~in_7);  // AND_Gate
  and and_12 (and_12_out, ~in_10, ~in_9, in_7);  // AND_Gate
  and and_13 (and_13_out, in_10, ~in_9, ~in_8, in_7);  // AND_Gate
  and and_14 (and_14_out, ~in_10, in_9, ~in_7);  // AND_Gate
  and and_15 (and_15_out, in_10, in_9, in_8, in_7);
  and and_16 (and_16_out, in_10, ~in_9, in_8, ~in_7);  // AND_Gate
  and and_17 (and_17_out, in_9, in_7);
  and and_18 (and_18_out, in_10, in_8, in_7);
  and and_19 (and_19_out, in_10, in_9, in_8);
  or or_9 (out_18, and_9_out, and_10_out);
  or or_10 (out_17, and_11_out, and_12_out, and_13_out, and_14_out, and_15_out, and_16_out);
  or or_11 (a_b_2, and_17_out, and_18_out, and_19_out);

  // Notes on the sheet:
  //   Somma di due numeri: a + b
  //   Somma di due numeri con due digiti: a + b
  //   a
  //   OR:
  //   b
  //   TUTTO AND:
  //   a
  //   b
endmodule
